// Logisim project cpu24 - 副本.circ as structural Verilog: 26 circuits, main circuit ◇单周期MIPS
module \单周期MIPS  (
  input  IR1,
  input  IR2,
  input  IR3,
  output RegWrite,
  output MemWrite,
  output [31:0] PC,
  output [31:0] IR,
  output [31:0] RDin,
  output [31:0] MDin,
  output [31:0] LedData
);

  wire AluScrB, and_1_out, and_2_out, and_4_out, Beq, Bne, CLK, clock_2_out, comparator_1_eq,
       comparator_1_lt, comparator_2_eq, controlled_buffer_1_out, d_ff_1_q, Go, halt, IR1_t, IR2_t, IR3_t,
       IRA, IRB, IRC, JAL, JMP, JR, ledin, MemToReg, mips_alu_1_equal, nand_1_out, not_1_out, not_2_out,
       or_4_out, RegDst, SignedExt, Syscall, W1, W2, W3;
  wire [3:0] AluOP;
  wire [4:0] multiplexer_4_out, multiplexer_5_out, multiplexer_6_out, multiplexer_7_out;
  wire [12:0] CNT_num;
  wire [15:0] \总周期数 ;
  wire [31:0] adder_1_out, adder_2_out, bit_extender_1_out, bit_extender_2_out, mips_alu_1_result,
       mips_regifile_1_r1, multiplexer_1_out, multiplexer_2_out, multiplexer_3_out, multiplexer_8_out,
       multiplexer_9_out, multiplexer_10_out, ram_1_data, shifter_1_out;

  Clock #(.highDuration(1), .lowDuration(1)) clock_1 (.out(CLK));
  Button _1 (.out(IRA));
  Button _2 (.out(IRB));
  Button _3 (.out(IRC));
  Button \u_继续运行  (.out(Go));
  LED #(.active("true")) led_1 (.in(W1));
  LED #(.active("true")) led_2 (.in(W2));
  LED #(.active("true")) led_3 (.in(W3));
  D_Flip_Flop #(.trigger("high"), .Pre_Clr_Positions("LEGACY"), .NegatePresetClear("false"), .enable("true"), .NewFFLayout("false")) d_ff_1 (.Q(d_ff_1_q));  // open: clk, D, Qn, preset, en, reset
  // Probe on 13'h607
  Hex_Digit_Display hex_digit_display_1 (.value(LedData[31:28]));  // open: dp
  Clock #(.highDuration(1), .lowDuration(1)) clock_2 (.out(clock_2_out));
  Hex_Digit_Display hex_digit_display_2 (.value(LedData[23:20]));  // open: dp
  Hex_Digit_Display hex_digit_display_3 (.value(LedData[27:24]));  // open: dp
  Comparator #(.width(13), .mode("twosComplement")) comparator_1 (
    .a(CNT_num), .b(13'h607), .eq(comparator_1_eq), .lt(comparator_1_lt));  // open: gt
  Hex_Digit_Display hex_digit_display_4 (.value(LedData[15:12]));  // open: dp
  Hex_Digit_Display hex_digit_display_5 (.value(LedData[19:16]));  // open: dp
  Multiplexer #(.select(1), .width(32), .disabled("Z"), .enable("false")) multiplexer_1 (
    .in0(adder_1_out), .in1(adder_2_out), .out(multiplexer_1_out), .sel(or_4_out));
  Multiplexer #(.select(1), .width(32), .disabled("Z"), .enable("false")) multiplexer_2 (
    .in0(multiplexer_1_out), .in1({4'b0000, IR[25:0], 2'b00}), .out(multiplexer_2_out), .sel(JMP));
  nand nand_1 (nand_1_out, d_ff_1_q, comparator_1_eq);
  Counter #(.width(13), .max('h1fff), .ongoal("stay"), .trigger("rising"), .behavior("old")) counter_1 (
    .count(comparator_1_lt), .Q(CNT_num), .clk(clock_2_out));  // open: load, D, carry, clr, preset
  Hex_Digit_Display hex_digit_display_6 (.value(LedData[11:8]));  // open: dp
  Hex_Digit_Display hex_digit_display_7 (.value(LedData[7:4]));  // open: dp
  // Probe on \总周期数 
  Multiplexer #(.select(1), .width(32), .disabled("Z"), .enable("false")) multiplexer_3 (
    .in0(multiplexer_2_out), .in1(mips_regifile_1_r1), .out(multiplexer_3_out), .sel(JR));
  not not_1 (not_1_out, halt);
  assign controlled_buffer_1_out = nand_1_out ? clock_2_out : 1'bz;  // Controlled_Buffer controlled_buffer_1
  Pull_Resistor #(.pull(1)) pull_resistor_1 (.node(controlled_buffer_1_out));
  Hex_Digit_Display hex_digit_display_8 (.value(LedData[3:0]));  // open: dp
  Register #(.width(32), .trigger("rising"), .Select("low")) u_PC (
    .D(multiplexer_3_out), .en(not_1_out), .Q(PC), .clk(CLK));  // open: clr
  Adder #(.width(32)) adder_1 (.a(PC), .b(32'h4), .out(adder_1_out));  // open: cin, cout
  or or_1 (IR1_t, IR1, IRA);
  ROM #(.addrWidth(10), .dataWidth(32), .Select("high")) rom_1 (.addr(PC[11:2]), .data(IR));
  or or_2 (IR2_t, IR2, IRB);
  // Mips_Probe mips_probe_1: pin names not known; wires that end beside it: IR
  or or_3 (IR3_t, IR3, IRC);
  Multiplexer #(.select(1), .width(5), .disabled("Z"), .enable("false")) multiplexer_4 (
    .in0(IR[20:16]), .in1(IR[15:11]), .out(multiplexer_4_out), .sel(RegDst));
  assign bit_extender_1_out = {{16{1'b0}}, IR[15:0]};  // Bit_Extender bit_extender_1
  assign bit_extender_2_out = {{16{IR[15]}}, IR[15:0]};  // Bit_Extender bit_extender_2
  Multiplexer #(.select(1), .width(5), .disabled("Z"), .enable("false")) multiplexer_5 (
    .in0(IR[25:21]), .in1(5'b00010), .out(multiplexer_5_out), .sel(Syscall));
  Multiplexer #(.select(1), .width(5), .disabled("Z"), .enable("false")) multiplexer_6 (
    .in0(IR[20:16]), .in1(5'b00100), .out(multiplexer_6_out), .sel(Syscall));
  Multiplexer #(.select(1), .width(5), .disabled("Z"), .enable("false")) multiplexer_7 (
    .in0(multiplexer_4_out), .in1({5{1'b1}}), .out(multiplexer_7_out), .sel(JAL));
  Multiplexer #(.select(1), .width(32), .disabled("Z"), .enable("false")) multiplexer_8 (
    .in0(bit_extender_1_out), .in1(bit_extender_2_out), .out(multiplexer_8_out), .sel(SignedExt));
  or or_4 (or_4_out, and_1_out, and_2_out);
  MIPS_Regifile mips_regifile_1 (
    .Din(RDin), .Clk(CLK), .R1(mips_regifile_1_r1), .R2(MDin), .WE(RegWrite), .W_num(multiplexer_7_out),
    .R1_num(multiplexer_5_out), .R2_num(multiplexer_6_out));
  and and_1 (and_1_out, Beq, mips_alu_1_equal);
  and and_2 (and_2_out, Bne, ~mips_alu_1_equal);  // AND_Gate
  Multiplexer #(.select(1), .width(32), .disabled("Z"), .enable("false")) multiplexer_9 (
    .in0(MDin), .in1(multiplexer_8_out), .out(multiplexer_9_out), .sel(AluScrB));
  MIPS_ALU mips_alu_1 (
    .X(mips_regifile_1_r1), .Y(multiplexer_9_out), .AluOP(AluOP), .Equal(mips_alu_1_equal),
    .Result(mips_alu_1_result), .shamt(IR[10:6]));  // open: Result_2
  Shifter #(.width(32), .shift("ll")) shifter_1 (.in(bit_extender_2_out), .\dist (5'b00010), .out(shifter_1_out));
  Adder #(.width(32)) adder_2 (.a(shifter_1_out), .b(adder_1_out), .out(adder_2_out));  // open: cin, cout
  Comparator #(.width(32), .mode("twosComplement")) comparator_2 (
    .a(32'h22), .b(mips_regifile_1_r1), .eq(comparator_2_eq));  // open: gt, lt
  Counter #(.width(16), .max('hffff), .ongoal("stay"), .trigger("rising"), .behavior("old")) counter_2 (
    .count(not_2_out), .Q(\总周期数 ), .clk(CLK));  // open: load, D, carry, clr, preset
  not not_2 (not_2_out, halt);
  Register #(.width(32), .trigger("rising"), .Select("low")) register_1 (
    .D(MDin), .en(ledin), .Q(LedData), .clk(CLK));  // open: clr
  and and_3 (ledin, Syscall, comparator_2_eq);
  and and_4 (and_4_out, Syscall, ~comparator_2_eq);  // AND_Gate
  RAM #(.addrWidth(10), .dataWidth(32), .bus("separate"), .Select("high")) ram_1 (
    .addr(mips_alu_1_result[11:2]), .din(MDin), .data(ram_1_data), .str(MemWrite), .clk(CLK), .ld(1'b1));  // open: sel, clr
  Register #(.width(1), .trigger("rising"), .Select("low")) register_2 (
    .D(Syscall), .en(and_4_out), .Q(halt), .clk(CLK), .clr(Go));
  Multiplexer #(.select(1), .width(32), .disabled("Z"), .enable("false")) multiplexer_10 (
    .in0(mips_alu_1_result), .in1(ram_1_data), .out(multiplexer_10_out), .sel(MemToReg));
  Multiplexer #(.select(1), .width(32), .disabled("Z"), .enable("false")) multiplexer_11 (
    .in0(multiplexer_10_out), .in1(adder_1_out), .out(RDin), .sel(JAL));
  \单周期硬布线控制器  \u_单周期硬布线控制器_1  (
    .Func(IR[5:0]), .OP(IR[31:26]), .ALU_OP(AluOP), .MemToReg(MemToReg), .MemWrite(MemWrite),
    .ALU_SRC(AluScrB), .RegWrite(RegWrite), .SysCALL(Syscall), .SignedExt(SignedExt), .RegDst(RegDst),
    .JR(JR), .JMP(JMP), .Beq(Beq), .JAL(JAL), .Bne(Bne));  // open: SLLV, XOR, SH, BLTZ

  // Other names for the same wires on the sheet: Func[5:0] = IR[5:0]; OP[5:0] = IR[31:26]

  // Notes on the sheet:
  //   中断源
  //   中断等待指示
  //   总复位信号应将除ROM以外所有存储组件全部清零
  //   控制位
  //   暂停节拍，不能为0
  //   戳工具置1进入计数暂停模式，ctrl+k时钟自动运行到对应节拍暂停
  //   ctrl+k关闭时钟连续运行，将控制位置零，进入单步调试模式调试
  //   用这个时钟源需要去掉电路中的其他时钟源
  //   数码管输出
  //   数码管输出应该用寄存器锁存，否则显示数据只能一闪而过
  //   可计数暂停的时钟源
  //   指令存储器
  //   contents of rom_1 (hex, n*v repeats v):
  //   20110001 8000c05 20110001 20120002 20130003 8000c09 20110001 20120002 20130003 8000c0d 20110001
  //   20120002 20130003 8000c11 20110001 20120002 20130003 c000cb8 20100001 20110001 118fc0 112020
  //   20020022 c 118882 12200001 8000c15 112020 20020022 c 20110001 118880 112020 20020022 c 12200001
  //   8000c1f 20110001 118fc0 112020 20020022 c 1188c3 112020 20020022 c 118903 112020 20020022 c 118903
  //   112020 20020022 c 118903 112020 20020022 c 118903 112020 20020022 c 118903 112020 20020022 c 118903
  //   112020 20020022 c 118903 112020 20020022 c 20100001 109fc0 139fc3 8021 2012000c 24160003 26100001
  //   3210000f 20080008 20090001 139900 2709825 132020 20020022 c 1094022 1500fff9 22100001 2018000f
  //   2188024 108700 20080008 20090001 139902 2709825 132021 20020022 c 1094022 1500fff9 108702 2c9b022
  //   12c00001 8000c50 4020 1084027 84400 3508ffff 82021 20020022 c 2010ffff 20110000 ae300000 22100001
  //   22310004 ae300000 22100001 22310004 ae300000 22100001 22310004 ae300000 22100001 22310004 ae300000
  //   22100001 22310004 ae300000 22100001 22310004 ae300000 22100001 22310004 ae300000 22100001 22310004
  //   ae300000 22100001 22310004 ae300000 22100001 22310004 ae300000 22100001 22310004 ae300000 22100001
  //   22310004 ae300000 22100001 22310004 ae300000 22100001 22310004 ae300000 22100001 22310004 ae300000
  //   22100001 22310004 22100001 8020 2011003c 8e130000 8e340000 274402a 11000002 ae330000 ae140000
  //   2231fffc 1611fff8 102020 20020022 c 22100004 2011003c 1611fff2 20020032 c 20100000 22100001 102020
  //   20020022 c 22100002 102020 20020022 c 22100003 102020 20020022 c 22100004 102020 20020022 c 22100005
  //   102020 20020022 c 22100006 102020 20020022 c 22100007 102020 20020022 c 22100008 102020 20020022
  //   20020022 c 3e00008
  //   指令字
  //   OP
  //   Func
  //   rs
  //   rt
  //   rd
  //   为方便自动评测，需要输出PC，IR，寄存器堆写如数据RDin
  //   RAM写使能MemWrite、RAM写入数据MDin等信号
  //   JMP
  //   JR
  //   OP
  //   Func
  //   Beq
  //   Bne
  //   MemToReg
  //   MemWrite
  //   AluOP
  //   AluSrcB
  //   RegWrite
  //   JAL
  //   RegDst
  //   Syscall
endmodule

// 单周期硬布线控制器
module \单周期硬布线控制器  (
  input  [5:0] OP,
  input  [5:0] Func,
  output [3:0] ALU_OP,
  output ALU_SRC,
  output RegDst,
  output RegWrite,
  output SignedExt,
  output MemWrite,
  output MemToReg,
  output SysCALL,
  output Beq,
  output Bne,
  output JR,
  output JMP,
  output JAL,
  output SLLV,
  output XOR,
  output SH,
  output BLTZ
);

  wire comparator_1_eq, comparator_2_eq, comparator_3_eq, \控制信号自动生成_1_alu_src , \控制信号自动生成_1_memwrite ,
       \控制信号自动生成_1_regdst , \控制信号自动生成_1_regwrite , \控制信号自动生成_1_signedext ;

  Comparator #(.width(6), .mode("twosComplement")) comparator_1 (
    .a(OP), .b({6{1'b0}}), .eq(comparator_1_eq));  // open: gt, lt
  Comparator #(.width(6), .mode("twosComplement")) comparator_2 (
    .a(Func), .b(6'b000100), .eq(comparator_2_eq));  // open: gt, lt
  Comparator #(.width(6), .mode("twosComplement")) comparator_3 (
    .a(Func), .b(6'b100110), .eq(comparator_3_eq));  // open: gt, lt
  Comparator #(.width(6), .mode("twosComplement")) comparator_4 (.a(OP), .b(6'b101001), .eq(SH));  // open: gt, lt
  Comparator #(.width(6), .mode("twosComplement")) comparator_5 (.a(OP), .b(6'b000001), .eq(BLTZ));  // open: gt, lt
  \运算控制器自动生成  \u_运算控制器自动生成_1  (
    .OP0(OP[0]), .OP1(OP[1]), .OP2(OP[2]), .OP3(OP[3]), .OP4(OP[4]), .OP5(OP[5]), .F0(Func[0]), .F1(Func[1]),
    .F2(Func[2]), .F3(Func[3]), .F4(Func[4]), .F5(Func[5]), .S0(ALU_OP[0]), .S1(ALU_OP[1]), .S2(ALU_OP[2]),
    .S3(ALU_OP[3]));
  \控制信号自动生成  \u_控制信号自动生成_1  (
    .OP0(OP[0]), .OP1(OP[1]), .OP2(OP[2]), .OP3(OP[3]), .OP4(OP[4]), .OP5(OP[5]), .F0(Func[0]), .F1(Func[1]),
    .F2(Func[2]), .F3(Func[3]), .F4(Func[4]), .F5(Func[5]), .MemToReg(MemToReg),
    .MemWrite(\控制信号自动生成_1_memwrite ), .ALU_SRC(\控制信号自动生成_1_alu_src ), .RegWrite(\控制信号自动生成_1_regwrite ),
    .SysCALL(SysCALL), .SignedExt(\控制信号自动生成_1_signedext ), .RegDst(\控制信号自动生成_1_regdst ), .BEQ(Beq),
    .BNE(Bne), .JR(JR), .JUMP(JMP), .JAL(JAL));
  and and_1 (SLLV, comparator_1_eq, comparator_2_eq);
  and and_2 (XOR, comparator_1_eq, comparator_3_eq);
  or or_1 (ALU_SRC, \控制信号自动生成_1_alu_src , SH);
  or or_2 (MemWrite, \控制信号自动生成_1_memwrite , SH);
  or or_3 (RegWrite, \控制信号自动生成_1_regwrite , SLLV, XOR);
  or or_4 (SignedExt, \控制信号自动生成_1_signedext , SH);
  or or_5 (RegDst, \控制信号自动生成_1_regdst , SLLV);

  // Other names for the same wires on the sheet: OP_CODE[5:0] = OP

  // Notes on the sheet:
  //   运算器控制器，根据指令生成运算器功能选择信号
  //   控制信号生成，产生数据通路需要的其他控制信号
endmodule

// 运算器控制器
module \运算控制器自动生成  (
  input  OP0,
  input  OP1,
  input  OP2,
  input  OP3,
  input  OP4,
  input  OP5,
  input  F0,
  input  F1,
  input  F2,
  input  F3,
  input  F4,
  input  F5,
  output S0,
  output S1,
  output S2,
  output S3
);

  wire and_1_out, and_2_out, and_3_out, and_4_out, and_5_out, and_6_out, and_7_out, and_8_out, and_9_out,
       and_10_out, and_11_out, and_12_out, and_13_out, and_14_out, and_15_out, and_16_out, and_17_out,
       and_18_out, and_19_out, and_20_out, and_21_out, and_22_out, and_23_out, and_24_out, and_25_out,
       and_26_out, not_1_out, not_2_out, not_3_out, not_4_out, not_5_out, not_6_out, not_7_out, not_8_out,
       not_9_out, not_10_out, not_11_out, not_12_out, not_13_out, not_14_out, not_15_out, not_16_out,
       not_17_out, not_18_out, not_19_out, not_20_out, not_21_out, not_22_out, not_23_out, not_24_out,
       not_25_out, not_26_out, not_27_out, not_28_out, not_29_out, not_30_out, not_31_out, not_32_out,
       not_33_out, not_34_out, not_35_out, not_36_out, not_37_out, not_38_out, not_39_out, not_40_out,
       not_41_out, not_42_out, not_43_out, not_44_out, not_45_out, not_46_out, not_47_out, not_48_out,
       not_49_out, not_50_out, not_51_out, not_52_out, not_53_out, not_54_out, not_55_out, not_56_out,
       not_57_out, not_58_out, not_59_out, not_60_out, not_61_out, not_62_out, not_63_out, not_64_out,
       not_65_out, not_66_out, not_67_out, not_68_out, not_69_out, not_70_out, not_71_out, not_72_out,
       not_73_out, not_74_out, not_75_out, not_76_out, not_77_out, not_78_out, not_79_out, not_80_out,
       not_81_out, not_82_out, not_83_out, not_84_out, not_85_out, not_86_out, not_87_out, not_88_out,
       not_89_out, not_90_out, not_91_out, not_92_out, not_93_out, not_94_out, not_95_out, not_96_out,
       not_97_out, not_98_out, not_99_out, not_100_out, not_101_out, not_102_out, not_103_out, not_104_out,
       not_105_out, not_106_out, not_107_out, not_108_out, not_109_out, not_110_out, not_111_out,
       not_112_out, not_113_out, not_114_out, not_115_out, not_116_out, not_117_out, not_118_out,
       not_119_out, not_120_out, not_121_out, not_122_out, not_123_out, not_124_out, not_125_out,
       not_126_out, not_127_out, not_128_out, not_129_out, not_130_out, not_131_out, not_132_out,
       not_133_out, not_134_out, not_135_out, not_136_out, not_137_out, not_138_out, not_139_out,
       not_140_out, not_141_out, not_142_out, not_143_out, not_144_out, not_145_out, not_146_out,
       not_147_out, not_148_out, not_149_out, not_150_out, not_151_out, not_152_out, not_153_out,
       not_154_out, not_155_out, not_156_out, not_157_out, not_158_out, not_159_out, not_160_out,
       not_161_out, not_162_out, not_163_out, not_164_out, not_165_out, not_166_out;

  not not_1 (not_1_out, OP0);
  not not_2 (not_2_out, OP1);
  not not_3 (not_3_out, OP2);
  not not_4 (not_4_out, OP4);
  not not_5 (not_5_out, OP5);
  not not_6 (not_6_out, F1);
  not not_7 (not_7_out, F2);
  not not_8 (not_8_out, F3);
  not not_9 (not_9_out, F4);
  not not_10 (not_10_out, OP0);
  not not_11 (not_11_out, OP1);
  not not_12 (not_12_out, OP2);
  not not_13 (not_13_out, OP4);
  not not_14 (not_14_out, OP5);
  not not_15 (not_15_out, F0);
  not not_16 (not_16_out, F3);
  not not_17 (not_17_out, F4);
  not not_18 (not_18_out, OP0);
  not not_19 (not_19_out, OP1);
  not not_20 (not_20_out, OP2);
  not not_21 (not_21_out, OP4);
  not not_22 (not_22_out, OP5);
  not not_23 (not_23_out, F0);
  not not_24 (not_24_out, F2);
  not not_25 (not_25_out, F4);
  not not_26 (not_26_out, OP0);
  not not_27 (not_27_out, OP1);
  not not_28 (not_28_out, OP2);
  not not_29 (not_29_out, OP4);
  not not_30 (not_30_out, OP5);
  not not_31 (not_31_out, F2);
  not not_32 (not_32_out, F3);
  not not_33 (not_33_out, F4);
  not not_34 (not_34_out, F5);
  not not_35 (not_35_out, OP0);
  not not_36 (not_36_out, OP1);
  not not_37 (not_37_out, OP4);
  not not_38 (not_38_out, OP5);
  not not_39 (not_39_out, OP0);
  not not_40 (not_40_out, OP2);
  not not_41 (not_41_out, OP4);
  not not_42 (not_42_out, OP5);
  not not_43 (not_43_out, OP1);
  not not_44 (not_44_out, OP2);
  not not_45 (not_45_out, OP4);
  not not_46 (not_46_out, OP2);
  not not_47 (not_47_out, OP4);
  not not_48 (not_48_out, OP0);
  not not_49 (not_49_out, OP1);
  not not_50 (not_50_out, OP2);
  not not_51 (not_51_out, OP3);
  not not_52 (not_52_out, OP4);
  not not_53 (not_53_out, OP5);
  not not_54 (not_54_out, F0);
  not not_55 (not_55_out, F1);
  not not_56 (not_56_out, F3);
  not not_57 (not_57_out, F4);
  not not_58 (not_58_out, OP0);
  not not_59 (not_59_out, OP1);
  not not_60 (not_60_out, OP2);
  not not_61 (not_61_out, OP3);
  not not_62 (not_62_out, OP4);
  not not_63 (not_63_out, OP5);
  not not_64 (not_64_out, F0);
  not not_65 (not_65_out, F2);
  not not_66 (not_66_out, F3);
  not not_67 (not_67_out, F4);
  not not_68 (not_68_out, OP0);
  not not_69 (not_69_out, OP1);
  not not_70 (not_70_out, OP2);
  not not_71 (not_71_out, OP3);
  not not_72 (not_72_out, OP4);
  not not_73 (not_73_out, OP5);
  not not_74 (not_74_out, F0);
  not not_75 (not_75_out, F2);
  not not_76 (not_76_out, F4);
  not not_77 (not_77_out, OP0);
  not not_78 (not_78_out, OP1);
  not not_79 (not_79_out, OP2);
  not not_80 (not_80_out, OP3);
  not not_81 (not_81_out, OP4);
  not not_82 (not_82_out, OP5);
  not not_83 (not_83_out, F3);
  not not_84 (not_84_out, F4);
  not not_85 (not_85_out, OP0);
  not not_86 (not_86_out, OP1);
  not not_87 (not_87_out, OP4);
  not not_88 (not_88_out, OP5);
  not not_89 (not_89_out, OP0);
  not not_90 (not_90_out, OP2);
  not not_91 (not_91_out, OP4);
  not not_92 (not_92_out, OP5);
  not not_93 (not_93_out, OP0);
  not not_94 (not_94_out, OP1);
  not not_95 (not_95_out, OP2);
  not not_96 (not_96_out, OP4);
  not not_97 (not_97_out, OP5);
  not not_98 (not_98_out, F0);
  not not_99 (not_99_out, F1);
  not not_100 (not_100_out, F3);
  not not_101 (not_101_out, F4);
  not not_102 (not_102_out, OP0);
  not not_103 (not_103_out, OP1);
  not not_104 (not_104_out, OP2);
  not not_105 (not_105_out, OP4);
  not not_106 (not_106_out, OP5);
  not not_107 (not_107_out, F0);
  not not_108 (not_108_out, F2);
  not not_109 (not_109_out, F3);
  not not_110 (not_110_out, F4);
  not not_111 (not_111_out, OP0);
  not not_112 (not_112_out, OP1);
  not not_113 (not_113_out, OP2);
  not not_114 (not_114_out, OP4);
  not not_115 (not_115_out, OP5);
  not not_116 (not_116_out, F1);
  not not_117 (not_117_out, F2);
  not not_118 (not_118_out, F3);
  not not_119 (not_119_out, F4);
  not not_120 (not_120_out, OP0);
  not not_121 (not_121_out, OP1);
  not not_122 (not_122_out, OP2);
  not not_123 (not_123_out, OP4);
  not not_124 (not_124_out, OP5);
  not not_125 (not_125_out, F2);
  not not_126 (not_126_out, F4);
  not not_127 (not_127_out, OP0);
  not not_128 (not_128_out, OP1);
  not not_129 (not_129_out, OP4);
  not not_130 (not_130_out, OP5);
  not not_131 (not_131_out, OP1);
  not not_132 (not_132_out, OP2);
  not not_133 (not_133_out, OP4);
  not not_134 (not_134_out, OP2);
  not not_135 (not_135_out, OP4);
  not not_136 (not_136_out, OP0);
  not not_137 (not_137_out, OP1);
  not not_138 (not_138_out, OP2);
  not not_139 (not_139_out, OP3);
  not not_140 (not_140_out, OP4);
  not not_141 (not_141_out, OP5);
  not not_142 (not_142_out, F2);
  not not_143 (not_143_out, F4);
  not not_144 (not_144_out, OP0);
  not not_145 (not_145_out, OP1);
  not not_146 (not_146_out, OP2);
  not not_147 (not_147_out, OP3);
  not not_148 (not_148_out, OP4);
  not not_149 (not_149_out, OP5);
  not not_150 (not_150_out, F3);
  not not_151 (not_151_out, F4);
  not not_152 (not_152_out, OP0);
  not not_153 (not_153_out, OP1);
  not not_154 (not_154_out, OP2);
  not not_155 (not_155_out, OP3);
  not not_156 (not_156_out, OP4);
  not not_157 (not_157_out, OP5);
  not not_158 (not_158_out, F3);
  not not_159 (not_159_out, F4);
  not not_160 (not_160_out, OP0);
  not not_161 (not_161_out, OP2);
  not not_162 (not_162_out, OP4);
  not not_163 (not_163_out, OP5);
  not not_164 (not_164_out, OP1);
  not not_165 (not_165_out, OP4);
  not not_166 (not_166_out, OP5);
  and and_1 (and_1_out, not_1_out, not_2_out, not_3_out, not_4_out, not_5_out, not_6_out, not_7_out, not_8_out, not_9_out, F5);
  and and_2 (and_2_out, not_10_out, not_11_out, not_12_out, not_13_out, not_14_out, not_15_out, F2, not_16_out, not_17_out, F5);
  and and_3 (and_3_out, not_18_out, not_19_out, not_20_out, not_21_out, not_22_out, not_23_out, F1, not_24_out, F3, not_25_out, F5);
  and and_4 (and_4_out, not_26_out, not_27_out, not_28_out, not_29_out, not_30_out, F0, F1, not_31_out, not_32_out, not_33_out, not_34_out);
  and and_5 (and_5_out, not_35_out, not_36_out, OP3, not_37_out, not_38_out);
  and and_6 (and_6_out, not_39_out, not_40_out, OP3, not_41_out, not_42_out);
  and and_7 (and_7_out, OP0, not_43_out, not_44_out, OP3, not_45_out);
  and and_8 (and_8_out, OP0, OP1, not_46_out, not_47_out, OP5);
  and and_9 (and_9_out, not_48_out, not_49_out, not_50_out, not_51_out, not_52_out, not_53_out, not_54_out, not_55_out, F2, not_56_out, not_57_out, F5);
  and and_10 (and_10_out, not_58_out, not_59_out, not_60_out, not_61_out, not_62_out, not_63_out, not_64_out, F1, not_65_out, not_66_out, not_67_out);
  and and_11 (and_11_out, not_68_out, not_69_out, not_70_out, not_71_out, not_72_out, not_73_out, not_74_out, F1, not_75_out, not_76_out, F5);
  and and_12 (and_12_out, not_77_out, not_78_out, not_79_out, not_80_out, not_81_out, not_82_out, F0, F1, F2, not_83_out, not_84_out, F5);
  and and_13 (and_13_out, not_85_out, not_86_out, OP2, OP3, not_87_out, not_88_out);
  and and_14 (and_14_out, not_89_out, OP1, not_90_out, OP3, not_91_out, not_92_out);
  and and_15 (and_15_out, not_93_out, not_94_out, not_95_out, not_96_out, not_97_out, not_98_out, not_99_out, not_100_out, not_101_out, F5);
  and and_16 (and_16_out, not_102_out, not_103_out, not_104_out, not_105_out, not_106_out, not_107_out, not_108_out, not_109_out, not_110_out, F5);
  and and_17 (and_17_out, not_111_out, not_112_out, not_113_out, not_114_out, not_115_out, not_116_out, not_117_out, not_118_out, not_119_out, F5);
  and and_18 (and_18_out, not_120_out, not_121_out, not_122_out, not_123_out, not_124_out, F0, F1, not_125_out, F3, not_126_out, F5);
  and and_19 (and_19_out, not_127_out, not_128_out, OP3, not_129_out, not_130_out);
  and and_20 (and_20_out, OP0, not_131_out, not_132_out, OP3, not_133_out);
  and and_21 (and_21_out, OP0, OP1, not_134_out, not_135_out, OP5);
  and and_22 (and_22_out, not_136_out, not_137_out, not_138_out, not_139_out, not_140_out, not_141_out, F1, not_142_out, F3, not_143_out, F5);
  and and_23 (and_23_out, not_144_out, not_145_out, not_146_out, not_147_out, not_148_out, not_149_out, F1, F2, not_150_out, not_151_out, F5);
  and and_24 (and_24_out, not_152_out, not_153_out, not_154_out, not_155_out, not_156_out, not_157_out, F0, F2, not_158_out, not_159_out, F5);
  and and_25 (and_25_out, not_160_out, OP1, not_161_out, OP3, not_162_out, not_163_out);
  and and_26 (and_26_out, OP0, not_164_out, OP2, OP3, not_165_out, not_166_out);
  or or_1 (S0, and_1_out, and_2_out, and_3_out, and_4_out, and_5_out, and_6_out, and_7_out, and_8_out);
  or or_2 (S1, and_9_out, and_10_out, and_11_out, and_12_out, and_13_out, and_14_out);
  or or_3 (S2, and_15_out, and_16_out, and_17_out, and_18_out, and_19_out, and_20_out, and_21_out);
  or or_4 (S3, and_22_out, and_23_out, and_24_out, and_25_out, and_26_out);
endmodule

// 控制信号生成
module \控制信号自动生成  (
  input  OP0,
  input  OP1,
  input  OP2,
  input  OP3,
  input  OP4,
  input  OP5,
  input  F0,
  input  F1,
  input  F2,
  input  F3,
  input  F4,
  input  F5,
  output MemToReg,
  output MemWrite,
  output ALU_SRC,
  output RegWrite,
  output SysCALL,
  output SignedExt,
  output RegDst,
  output BEQ,
  output BNE,
  output JR,
  output JUMP,
  output JAL
);

  wire and_3_out, and_4_out, and_5_out, and_6_out, and_7_out, and_8_out, and_9_out, and_10_out, and_11_out,
       and_12_out, and_13_out, and_15_out, and_16_out, and_17_out, and_18_out, and_19_out, and_20_out,
       and_21_out, and_22_out, and_23_out, and_27_out, and_28_out, not_1_out, not_2_out, not_3_out,
       not_4_out, not_5_out, not_6_out, not_7_out, not_8_out, not_9_out, not_10_out, not_11_out, not_12_out,
       not_13_out, not_14_out, not_15_out, not_16_out, not_17_out, not_18_out, not_19_out, not_20_out,
       not_21_out, not_22_out, not_23_out, not_24_out, not_25_out, not_26_out, not_27_out, not_28_out,
       not_29_out, not_30_out, not_31_out, not_32_out, not_33_out, not_34_out, not_35_out, not_36_out,
       not_37_out, not_38_out, not_39_out, not_40_out, not_41_out, not_42_out, not_43_out, not_44_out,
       not_45_out, not_46_out, not_47_out, not_48_out, not_49_out, not_50_out, not_51_out, not_52_out,
       not_53_out, not_54_out, not_55_out, not_56_out, not_57_out, not_58_out, not_59_out, not_60_out,
       not_61_out, not_62_out, not_63_out, not_64_out, not_65_out, not_66_out, not_67_out, not_68_out,
       not_69_out, not_70_out, not_71_out, not_72_out, not_73_out, not_74_out, not_75_out, not_76_out,
       not_77_out, not_78_out, not_79_out, not_80_out, not_81_out, not_82_out, not_83_out, not_84_out,
       not_85_out, not_86_out, not_87_out, not_88_out, not_89_out, not_90_out, not_91_out, not_92_out,
       not_93_out, not_94_out, not_95_out, not_96_out, not_97_out, not_98_out, not_99_out, not_100_out,
       not_101_out, not_102_out, not_103_out, not_104_out, not_105_out, not_106_out, not_107_out,
       not_108_out, not_109_out, not_110_out, not_111_out, not_112_out, not_113_out, not_114_out,
       not_115_out, not_116_out, not_117_out, not_118_out, not_119_out, not_120_out, not_121_out,
       not_122_out, not_123_out, not_124_out, not_125_out, not_126_out, not_127_out, not_128_out,
       not_129_out, not_130_out, not_131_out, not_132_out, not_133_out, not_134_out, not_135_out,
       not_136_out, not_137_out, not_138_out, not_139_out, not_140_out, not_141_out, not_142_out,
       not_143_out, not_144_out, not_145_out, not_146_out, not_147_out, not_148_out, not_149_out,
       not_150_out, not_151_out, not_152_out, not_153_out, not_154_out, not_155_out, not_156_out,
       not_157_out, not_158_out, not_159_out, not_160_out, not_161_out, not_162_out, not_163_out,
       not_164_out, not_165_out, not_166_out, not_167_out, not_168_out, not_169_out, not_170_out,
       not_171_out, not_172_out, not_173_out, not_174_out, not_175_out, not_176_out, not_177_out;

  not not_1 (not_1_out, OP2);
  not not_2 (not_2_out, OP3);
  not not_3 (not_3_out, OP4);
  not not_4 (not_4_out, OP2);
  not not_5 (not_5_out, OP4);
  not not_6 (not_6_out, OP0);
  not not_7 (not_7_out, OP2);
  not not_8 (not_8_out, OP4);
  not not_9 (not_9_out, OP5);
  not not_10 (not_10_out, OP1);
  not not_11 (not_11_out, OP4);
  not not_12 (not_12_out, OP5);
  not not_13 (not_13_out, OP2);
  not not_14 (not_14_out, OP4);
  not not_15 (not_15_out, OP0);
  not not_16 (not_16_out, OP1);
  not not_17 (not_17_out, OP2);
  not not_18 (not_18_out, OP4);
  not not_19 (not_19_out, OP5);
  not not_20 (not_20_out, F0);
  not not_21 (not_21_out, F2);
  not not_22 (not_22_out, F3);
  not not_23 (not_23_out, F4);
  not not_24 (not_24_out, OP0);
  not not_25 (not_25_out, OP1);
  not not_26 (not_26_out, OP2);
  not not_27 (not_27_out, OP4);
  not not_28 (not_28_out, OP5);
  not not_29 (not_29_out, F1);
  not not_30 (not_30_out, F3);
  not not_31 (not_31_out, F4);
  not not_32 (not_32_out, OP0);
  not not_33 (not_33_out, OP1);
  not not_34 (not_34_out, OP2);
  not not_35 (not_35_out, OP4);
  not not_36 (not_36_out, OP5);
  not not_37 (not_37_out, F2);
  not not_38 (not_38_out, F3);
  not not_39 (not_39_out, F4);
  not not_40 (not_40_out, F5);
  not not_41 (not_41_out, OP0);
  not not_42 (not_42_out, OP1);
  not not_43 (not_43_out, OP2);
  not not_44 (not_44_out, OP4);
  not not_45 (not_45_out, OP5);
  not not_46 (not_46_out, F2);
  not not_47 (not_47_out, F4);
  not not_48 (not_48_out, OP0);
  not not_49 (not_49_out, OP1);
  not not_50 (not_50_out, OP2);
  not not_51 (not_51_out, OP4);
  not not_52 (not_52_out, OP5);
  not not_53 (not_53_out, F3);
  not not_54 (not_54_out, F4);
  not not_55 (not_55_out, OP0);
  not not_56 (not_56_out, OP2);
  not not_57 (not_57_out, OP4);
  not not_58 (not_58_out, OP5);
  not not_59 (not_59_out, OP1);
  not not_60 (not_60_out, OP4);
  not not_61 (not_61_out, OP5);
  not not_62 (not_62_out, OP2);
  not not_63 (not_63_out, OP3);
  not not_64 (not_64_out, OP4);
  not not_65 (not_65_out, OP0);
  not not_66 (not_66_out, OP1);
  not not_67 (not_67_out, OP2);
  not not_68 (not_68_out, OP3);
  not not_69 (not_69_out, OP4);
  not not_70 (not_70_out, OP5);
  not not_71 (not_71_out, F0);
  not not_72 (not_72_out, F1);
  not not_73 (not_73_out, F4);
  not not_74 (not_74_out, F5);
  not not_75 (not_75_out, OP0);
  not not_76 (not_76_out, OP2);
  not not_77 (not_77_out, OP4);
  not not_78 (not_78_out, OP5);
  not not_79 (not_79_out, OP1);
  not not_80 (not_80_out, OP2);
  not not_81 (not_81_out, OP4);
  not not_82 (not_82_out, OP5);
  not not_83 (not_83_out, OP2);
  not not_84 (not_84_out, OP4);
  not not_85 (not_85_out, OP0);
  not not_86 (not_86_out, OP1);
  not not_87 (not_87_out, OP2);
  not not_88 (not_88_out, OP3);
  not not_89 (not_89_out, OP4);
  not not_90 (not_90_out, OP5);
  not not_91 (not_91_out, F0);
  not not_92 (not_92_out, F1);
  not not_93 (not_93_out, F3);
  not not_94 (not_94_out, F4);
  not not_95 (not_95_out, OP0);
  not not_96 (not_96_out, OP1);
  not not_97 (not_97_out, OP2);
  not not_98 (not_98_out, OP3);
  not not_99 (not_99_out, OP4);
  not not_100 (not_100_out, OP5);
  not not_101 (not_101_out, F0);
  not not_102 (not_102_out, F2);
  not not_103 (not_103_out, F3);
  not not_104 (not_104_out, F4);
  not not_105 (not_105_out, OP0);
  not not_106 (not_106_out, OP1);
  not not_107 (not_107_out, OP2);
  not not_108 (not_108_out, OP3);
  not not_109 (not_109_out, OP4);
  not not_110 (not_110_out, OP5);
  not not_111 (not_111_out, F1);
  not not_112 (not_112_out, F3);
  not not_113 (not_113_out, F4);
  not not_114 (not_114_out, OP0);
  not not_115 (not_115_out, OP1);
  not not_116 (not_116_out, OP2);
  not not_117 (not_117_out, OP3);
  not not_118 (not_118_out, OP4);
  not not_119 (not_119_out, OP5);
  not not_120 (not_120_out, F3);
  not not_121 (not_121_out, F4);
  not not_122 (not_122_out, OP0);
  not not_123 (not_123_out, OP1);
  not not_124 (not_124_out, OP2);
  not not_125 (not_125_out, OP3);
  not not_126 (not_126_out, OP4);
  not not_127 (not_127_out, OP5);
  not not_128 (not_128_out, F2);
  not not_129 (not_129_out, F3);
  not not_130 (not_130_out, F4);
  not not_131 (not_131_out, F5);
  not not_132 (not_132_out, OP0);
  not not_133 (not_133_out, OP1);
  not not_134 (not_134_out, OP2);
  not not_135 (not_135_out, OP3);
  not not_136 (not_136_out, OP4);
  not not_137 (not_137_out, OP5);
  not not_138 (not_138_out, F2);
  not not_139 (not_139_out, F4);
  not not_140 (not_140_out, OP0);
  not not_141 (not_141_out, OP1);
  not not_142 (not_142_out, OP3);
  not not_143 (not_143_out, OP4);
  not not_144 (not_144_out, OP5);
  not not_145 (not_145_out, OP1);
  not not_146 (not_146_out, OP3);
  not not_147 (not_147_out, OP4);
  not not_148 (not_148_out, OP5);
  not not_149 (not_149_out, OP0);
  not not_150 (not_150_out, OP1);
  not not_151 (not_151_out, OP2);
  not not_152 (not_152_out, OP3);
  not not_153 (not_153_out, OP4);
  not not_154 (not_154_out, OP5);
  not not_155 (not_155_out, F0);
  not not_156 (not_156_out, F1);
  not not_157 (not_157_out, F2);
  not not_158 (not_158_out, F4);
  not not_159 (not_159_out, F5);
  not not_160 (not_160_out, OP0);
  not not_161 (not_161_out, OP2);
  not not_162 (not_162_out, OP3);
  not not_163 (not_163_out, OP4);
  not not_164 (not_164_out, OP5);
  not not_165 (not_165_out, F0);
  not not_166 (not_166_out, F1);
  not not_167 (not_167_out, F2);
  not not_168 (not_168_out, F4);
  not not_169 (not_169_out, F5);
  not not_170 (not_170_out, OP2);
  not not_171 (not_171_out, OP3);
  not not_172 (not_172_out, OP4);
  not not_173 (not_173_out, OP5);
  not not_174 (not_174_out, OP2);
  not not_175 (not_175_out, OP3);
  not not_176 (not_176_out, OP4);
  not not_177 (not_177_out, OP5);
  and and_1 (MemToReg, OP0, OP1, not_1_out, not_2_out, not_3_out, OP5);
  and and_2 (MemWrite, OP0, OP1, not_4_out, OP3, not_5_out, OP5);
  and and_3 (and_3_out, not_6_out, not_7_out, OP3, not_8_out, not_9_out);
  or or_1 (ALU_SRC, and_3_out, and_4_out, and_5_out);
  and and_4 (and_4_out, not_10_out, OP3, not_11_out, not_12_out);
  and and_5 (and_5_out, OP0, OP1, not_13_out, not_14_out, OP5);
  and and_6 (and_6_out, not_15_out, not_16_out, not_17_out, not_18_out, not_19_out, not_20_out, not_21_out, not_22_out, not_23_out);
  and and_7 (and_7_out, not_24_out, not_25_out, not_26_out, not_27_out, not_28_out, not_29_out, not_30_out, not_31_out, F5);
  and and_8 (and_8_out, not_32_out, not_33_out, not_34_out, not_35_out, not_36_out, F1, not_37_out, not_38_out, not_39_out, not_40_out);
  and and_9 (and_9_out, not_41_out, not_42_out, not_43_out, not_44_out, not_45_out, F1, not_46_out, F3, not_47_out, F5);
  and and_10 (and_10_out, not_48_out, not_49_out, not_50_out, not_51_out, not_52_out, F0, F2, not_53_out, not_54_out, F5);
  and and_11 (and_11_out, not_55_out, not_56_out, OP3, not_57_out, not_58_out);
  and and_12 (and_12_out, not_59_out, OP3, not_60_out, not_61_out);
  and and_13 (and_13_out, OP0, OP1, not_62_out, not_63_out, not_64_out);
  and and_14 (SysCALL, not_65_out, not_66_out, not_67_out, not_68_out, not_69_out, not_70_out, not_71_out, not_72_out, F2, F3, not_73_out, not_74_out);
  and and_15 (and_15_out, not_75_out, not_76_out, OP3, not_77_out, not_78_out);
  and and_16 (and_16_out, not_79_out, not_80_out, OP3, not_81_out, not_82_out);
  or or_2 (SignedExt, and_15_out, and_16_out, and_17_out);
  and and_17 (and_17_out, OP0, OP1, not_83_out, not_84_out, OP5);
  and and_18 (and_18_out, not_85_out, not_86_out, not_87_out, not_88_out, not_89_out, not_90_out, not_91_out, not_92_out, not_93_out, not_94_out);
  and and_19 (and_19_out, not_95_out, not_96_out, not_97_out, not_98_out, not_99_out, not_100_out, not_101_out, not_102_out, not_103_out, not_104_out);
  and and_20 (and_20_out, not_105_out, not_106_out, not_107_out, not_108_out, not_109_out, not_110_out, not_111_out, not_112_out, not_113_out, F5);
  and and_21 (and_21_out, not_114_out, not_115_out, not_116_out, not_117_out, not_118_out, not_119_out, F2, not_120_out, not_121_out, F5);
  and and_22 (and_22_out, not_122_out, not_123_out, not_124_out, not_125_out, not_126_out, not_127_out, F1, not_128_out, not_129_out, not_130_out, not_131_out);
  and and_23 (and_23_out, not_132_out, not_133_out, not_134_out, not_135_out, not_136_out, not_137_out, F1, not_138_out, F3, not_139_out, F5);
  and and_24 (BEQ, not_140_out, not_141_out, OP2, not_142_out, not_143_out, not_144_out);
  and and_25 (BNE, OP0, not_145_out, OP2, not_146_out, not_147_out, not_148_out);
  and and_26 (JR, not_149_out, not_150_out, not_151_out, not_152_out, not_153_out, not_154_out, not_155_out, not_156_out, not_157_out, F3, not_158_out, not_159_out);
  and and_27 (and_27_out, not_160_out, not_161_out, not_162_out, not_163_out, not_164_out, not_165_out, not_166_out, not_167_out, F3, not_168_out, not_169_out);
  and and_28 (and_28_out, OP1, not_170_out, not_171_out, not_172_out, not_173_out);
  and and_29 (JAL, OP0, OP1, not_174_out, not_175_out, not_176_out, not_177_out);
  or or_3 (RegWrite, and_6_out, and_7_out, and_8_out, and_9_out, and_10_out, and_11_out, and_12_out, and_13_out);
  or or_4 (RegDst, and_18_out, and_19_out, and_20_out, and_21_out, and_22_out, and_23_out);
  or or_5 (JUMP, and_27_out, and_28_out);
endmodule

// ALU
module MIPS_ALU (
  input  [4:0] shamt,
  input  [31:0] X,
  input  [31:0] Y,
  input  [3:0] AluOP,
  output Equal,
  output [31:0] Result,
  output [31:0] Result_2
);

  wire [0:0] comparator_1_lt, comparator_2_lt;
  wire [31:0] adder_1_out, AND_out, divider_1_out, divider_1_rem, multiplier_1_cout, multiplier_1_out,
       NOR_out, OR_out, shifter_1_out, shifter_2_out, shifter_3_out, subtractor_1_out, XOR_out;

  assign AND_out = X & Y;  // AND_Gate AND, 32 bits wide
  assign OR_out = X | Y;  // OR_Gate OR, 32 bits wide
  Shifter #(.width(32), .shift("ll")) shifter_1 (.in(Y), .\dist (shamt), .out(shifter_1_out));
  Shifter #(.width(32), .shift("ar")) shifter_2 (.in(Y), .\dist (shamt), .out(shifter_2_out));
  Shifter #(.width(32), .shift("lr")) shifter_3 (.in(Y), .\dist (shamt), .out(shifter_3_out));
  Multiplier #(.width(32)) multiplier_1 (.a(X), .b(Y), .out(multiplier_1_out), .cout(multiplier_1_cout));  // open: cin
  Divider #(.width(32)) divider_1 (.a(X), .b(Y), .out(divider_1_out), .rem(divider_1_rem));  // open: upper
  Adder #(.width(32)) adder_1 (.a(X), .b(Y), .out(adder_1_out));  // open: cin, cout
  Subtractor #(.width(32)) subtractor_1 (.a(X), .b(Y), .out(subtractor_1_out));  // open: bin, bout
  assign XOR_out = X ^ Y;  // XOR_Gate XOR, 32 bits wide
  assign NOR_out = ~(X | Y);  // NOR_Gate NOR, 32 bits wide
  Comparator #(.width(32), .mode("twosComplement")) comparator_1 (
    .a(X), .b(Y), .eq(Equal), .lt(comparator_1_lt[0]));  // open: gt
  Comparator #(.width(32), .mode("unsigned")) comparator_2 (.a(X), .b(Y), .lt(comparator_2_lt[0]));  // open: gt, eq
  Multiplexer #(.select(4), .width(32), .disabled("Z"), .enable("false")) multiplexer_1 (
    .in0(shifter_1_out), .in1(shifter_2_out), .in2(shifter_3_out), .in3(multiplier_1_out),
    .in4(divider_1_out), .in5(adder_1_out), .in6(subtractor_1_out), .in7(AND_out), .in8(OR_out),
    .in9(XOR_out), .in10(NOR_out), .in11({{31{1'b0}}, comparator_1_lt[0]}),
    .in12({{31{1'b0}}, comparator_2_lt[0]}), .in13({32{1'b0}}), .in14({32{1'b0}}), .in15({32{1'b0}}),
    .out(Result), .sel(AluOP));
  Multiplexer #(.select(4), .width(32), .disabled("Z"), .enable("false")) multiplexer_2 (
    .in0({32{1'b0}}), .in1({32{1'b0}}), .in2({32{1'b0}}), .in3(multiplier_1_cout), .in4(divider_1_rem),
    .in5({32{1'b0}}), .in6({32{1'b0}}), .in7({32{1'b0}}), .in8({32{1'b0}}), .in9({32{1'b0}}),
    .in10({32{1'b0}}), .in11({32{1'b0}}), .in12({32{1'b0}}), .in13({32{1'b0}}), .in14({32{1'b0}}),
    .in15({32{1'b0}}), .out(Result_2), .sel(AluOP));

  // Other names for the same wires on the sheet: Result2[31:0] = Result_2; S[3:0] = AluOP

  // Notes on the sheet:
  //   不要改变此引脚区域内容，也不要改变ALU封装形式
  //   输入引脚
  //   输出引脚
endmodule

module MIPS_Regifile (
  input  [31:0] Din,
  input  Clk,
  input  WE,
  input  [4:0] R1_num,
  input  [4:0] W_num,
  input  [4:0] R2_num,
  output [31:0] R1,
  output [31:0] R2
);

  // RegisterFile registerfile_1: pin names not known; wires that end beside it: Din, Clk, WE, W_num, R1_num, R2_num, R1, R2
endmodule

module MIPS_REGIFILR (
  input  [31:0] Din,
  input  Clk,
  input  WE,
  input  [4:0] R1_num,
  input  [4:0] W_num,
  input  [4:0] R2_num,
  output [31:0] R1,
  output [31:0] R2
);

  // RegisterFile registerfile_1: pin names not known; wires that end beside it: Din, Clk, WE, W_num, R1_num, R2_num, R1, R2
endmodule

module \理想流水线  (
  output RegWrite,
  output MemWrite,
  output [31:0] IF_PC,
  output [31:0] ID_PC,
  output [31:0] EX_PC,
  output [31:0] M_PC,
  output [31:0] WB_PC,
  output [31:0] RDin,
  output [31:0] MDin,
  output [31:0] LedData
);

  wire AluScrB, AluScrB2, and_1_out, and_2_out, and_3_out, and_4_out, and_5_out, and_7_out, and_8_out, Beq,
       Beq2, Bne, Bne2, CLK, clock_2_out, comparator_1_eq, comparator_1_lt, comparator_2_eq,
       controlled_buffer_1_out, d_ff_1_q, Go, halt, IR1, IR2, IR3, JAL, JAL2, JAL3, JAL4, JMP, JMP2, JR, JR2,
       JR3, ledin, MemToReg, MemToReg2, MemToReg3, MemToReg4, MemWrite2, MemWrite_t, mips_alu_1_equal,
       nand_1_out, not_1_out, not_2_out, or_1_out, RegDst, RegDst2, RegDst3, RegWrite2, RegWrite3,
       RegWrite_t, RST, SignedExt, Syscall, Syscall2, Syscall3, W1, W2, W3;
  wire [3:0] AluOP, AluOP2;
  wire [4:0] ID_EX_imm_out, multiplexer_4_out, multiplexer_5_out, multiplexer_6_out, WriteReg, WriteReg2,
       WriteReg3, WriteReg4;
  wire [5:0] Func;
  wire [12:0] CNT_num;
  wire [15:0] \LoadUse次数 , \总周期数 , \插入气泡数 , \无条件分支数 , \条件分支成功数 ;
  wire [31:0] adder_1_out, adder_2_out, adder_3_out, adder_4_out, bit_extender_1_out, bit_extender_2_out,
       EX_IR, ex_mem_ideal_1_a, ex_mem_ideal_1_alu_out, ID_EX_a, ID_EX_b, ID_EX_mux_out, \ID_EX_有符号扩展_out ,
       IF_IR, MEM_IR, MEM_WB_alu_out, MEM_WB_rd_out, mips_alu_1_result, mips_regifile_1_r1,
       mips_regifile_1_r2, multiplexer_1_out, multiplexer_2_out, multiplexer_3_out, multiplexer_8_out,
       multiplexer_9_out, multiplexer_10_out, ram_1_data, shifter_1_out, WB_IR;
  wire [31:6] ID_IR;

  Button \u_总复位  (.out(RST));
  Button _1 (.out(IR1));
  Button _2 (.out(IR2));
  Button _3 (.out(IR3));
  // Probe on \总周期数 
  // Probe on \总周期数 
  Button \u_继续运行  (.out(Go));
  LED #(.active("true")) led_1 (.in(W1));
  LED #(.active("true")) led_2 (.in(W2));
  LED #(.active("true")) led_3 (.in(W3));
  Multiplexer #(.select(1), .width(32), .disabled("Z"), .enable("false")) multiplexer_1 (
    .in0(adder_1_out), .in1(adder_3_out), .out(multiplexer_1_out), .sel(or_1_out));
  Hex_Digit_Display hex_digit_display_1 (.value(LedData[31:28]));  // open: dp
  // Probe on IF_PC[19:0]
  // Mips_Probe mips_probe_1: pin names not known; wires that end beside it: IF_IR
  Multiplexer #(.select(1), .width(32), .disabled("Z"), .enable("false")) multiplexer_2 (
    .in0(multiplexer_1_out), .in1({4'b0000, ID_IR[25:6], Func, 2'b00}), .out(multiplexer_2_out), .sel(JMP));
  Multiplexer #(.select(1), .width(32), .disabled("Z"), .enable("false")) multiplexer_3 (
    .in0(multiplexer_2_out), .in1(ex_mem_ideal_1_a), .out(multiplexer_3_out), .sel(JR3));
  not not_1 (not_1_out, halt);
  Hex_Digit_Display hex_digit_display_2 (.value(LedData[23:20]));  // open: dp
  Hex_Digit_Display hex_digit_display_3 (.value(LedData[27:24]));  // open: dp
  // Probe on ID_PC[19:0]
  // Mips_Probe mips_probe_2: pin names not known; wires that end beside it: {ID_IR, Func}
  Register #(.width(32), .trigger("rising"), .Select("low")) PC (
    .D(multiplexer_3_out), .en(not_1_out), .Q(IF_PC), .clk(CLK), .clr(RST));
  Hex_Digit_Display hex_digit_display_4 (.value(LedData[15:12]));  // open: dp
  Hex_Digit_Display hex_digit_display_5 (.value(LedData[19:16]));  // open: dp
  Adder #(.width(32)) adder_1 (.a(IF_PC), .b(32'h4), .out(adder_1_out));  // open: cin, cout
  Hex_Digit_Display hex_digit_display_6 (.value(LedData[11:8]));  // open: dp
  Hex_Digit_Display hex_digit_display_7 (.value(LedData[7:4]));  // open: dp
  Clock #(.highDuration(1), .lowDuration(1)) clock_1 (.out(CLK));
  // Probe on EX_PC[19:0]
  // Mips_Probe mips_probe_3: pin names not known; wires that end beside it: EX_IR
  and and_1 (and_1_out, CLK, ~halt);  // AND_Gate
  Hex_Digit_Display hex_digit_display_8 (.value(LedData[3:0]));  // open: dp
  // Mips_Probe mips_probe_4: pin names not known; wires that end beside it: IF_IR
  ROM #(.addrWidth(10), .dataWidth(32), .Select("high")) rom_1 (.addr(IF_PC[11:2]), .data(IF_IR));
  IF_ID IF_ID (
    .PC_in(IF_PC), .IR_in(IF_IR), .clk(and_1_out), .\同步清零 (RST), .PC_out(ID_PC), .IR_out({ID_IR, Func}));  // open: 使能
  // Probe on \总周期数 
  // Probe on M_PC[19:0]
  // Mips_Probe mips_probe_5: pin names not known; wires that end beside it: MEM_IR
  // Probe on \总周期数 
  // Probe on \无条件分支数 
  // Probe on \条件分支成功数 
  // Probe on \插入气泡数 
  // Probe on \LoadUse次数 
  Multiplexer #(.select(1), .width(5), .disabled("Z"), .enable("false")) multiplexer_4 (
    .in0(ID_IR[20:16]), .in1(ID_IR[15:11]), .out(multiplexer_4_out), .sel(RegDst));
  // Probe on IF_PC[11:0]
  // Probe on WB_PC[19:0]
  // Mips_Probe mips_probe_6: pin names not known; wires that end beside it: WB_IR
  Multiplexer #(.select(1), .width(5), .disabled("Z"), .enable("false")) multiplexer_5 (
    .in0(ID_IR[25:21]), .in1(5'b00010), .out(multiplexer_5_out), .sel(Syscall));
  Multiplexer #(.select(1), .width(5), .disabled("Z"), .enable("false")) multiplexer_6 (
    .in0(ID_IR[20:16]), .in1(5'b00100), .out(multiplexer_6_out), .sel(Syscall));
  Multiplexer #(.select(1), .width(5), .disabled("Z"), .enable("false")) multiplexer_7 (
    .in0(multiplexer_4_out), .in1({5{1'b1}}), .out(WriteReg), .sel(JAL));
  assign bit_extender_1_out = {{16{1'b0}}, {ID_IR[15:6], Func}};  // Bit_Extender bit_extender_1
  assign bit_extender_2_out = {{16{ID_IR[15]}}, {ID_IR[15:6], Func}};  // Bit_Extender bit_extender_2
  // Probe on ID_PC[11:0]
  // Probe on EX_PC[11:0]
  Multiplexer #(.select(1), .width(32), .disabled("Z"), .enable("false")) multiplexer_8 (
    .in0(bit_extender_1_out), .in1(bit_extender_2_out), .out(multiplexer_8_out), .sel(SignedExt));
  // Probe on M_PC[11:0]
  D_Flip_Flop #(.trigger("high"), .Pre_Clr_Positions("LEGACY"), .NegatePresetClear("false"), .enable("true"), .NewFFLayout("false")) d_ff_1 (.Q(d_ff_1_q));  // open: clk, D, Qn, preset, en, reset
  // Probe on 13'hc
  MIPS_Regifile mips_regifile_1 (
    .Din(RDin), .Clk(CLK), .R1(mips_regifile_1_r1), .R2(mips_regifile_1_r2), .WE(RegWrite),
    .W_num(WriteReg4), .R1_num(multiplexer_5_out), .R2_num(multiplexer_6_out));
  // Probe on WB_PC[11:0]
  Comparator #(.width(13), .mode("twosComplement")) comparator_1 (
    .a(CNT_num), .b(13'hc), .eq(comparator_1_eq), .lt(comparator_1_lt));  // open: gt
  Clock #(.highDuration(1), .lowDuration(1)) clock_2 (.out(clock_2_out));
  or or_1 (or_1_out, and_3_out, and_4_out);
  ID_EX ID_EX (
    .IR_in({ID_IR, Func}), .ALUOP_in(AluOP), .PC_in(ID_PC), .MemToReg_in(MemToReg), .MemWrite_in(MemWrite_t),
    .R1(mips_regifile_1_r1), .ALU_SRC_in(AluScrB), .RegWrite_in(RegWrite_t), .R2(mips_regifile_1_r2),
    .Syscall_in(Syscall), .RegDst_in(RegDst), .IMM(ID_IR[10:6]), .Beq_in(Beq), .Bne_in(Bne),
    .MUX_in(multiplexer_8_out), .JR_in(JR), .JMP_in(JMP), .JAL_in(JAL), .\有符号扩展 (bit_extender_2_out),
    .clk(and_2_out), .\同步清零 (RST), .IR_out(EX_IR), .ALUOP(AluOP2), .PC_out(EX_PC), .MemToReg(MemToReg2),
    .MemWrite(MemWrite2), .A(ID_EX_a), .ALU_SRC(AluScrB2), .RegWrite(RegWrite2), .B(ID_EX_b),
    .SysCALL(Syscall2), .RegDst(RegDst2), .imm_out(ID_EX_imm_out), .Beq(Beq2), .Bne(Bne2),
    .MUX_out(ID_EX_mux_out), .JR(JR2), .JMP(JMP2), .JAL(JAL2), .\有符号扩展_out (\ID_EX_有符号扩展_out ),
    .WriteReg(WriteReg), .WriteReg_out(WriteReg2));  // open: 使能, SLLV, XOR, SH, BLTZ, BLTZ_in, SH_in, XOR_in, SLLV_in, JMPaddr, JMPaddr_out, forward2, forward2_out, forward1, forward1_out
  and and_2 (and_2_out, CLK, ~halt);  // AND_Gate
  nand nand_1 (nand_1_out, d_ff_1_q, comparator_1_eq);
  Counter #(.width(13), .max('h1fff), .ongoal("stay"), .trigger("rising"), .behavior("old")) counter_1 (
    .count(comparator_1_lt), .Q(CNT_num), .clk(clock_2_out));  // open: load, D, carry, clr, preset
  and and_3 (and_3_out, Beq2, mips_alu_1_equal);
  and and_4 (and_4_out, Bne2, ~mips_alu_1_equal);  // AND_Gate
  assign controlled_buffer_1_out = nand_1_out ? clock_2_out : 1'bz;  // Controlled_Buffer controlled_buffer_1
  Multiplexer #(.select(1), .width(32), .disabled("Z"), .enable("false")) multiplexer_9 (
    .in0(ID_EX_b), .in1(ID_EX_mux_out), .out(multiplexer_9_out), .sel(AluScrB2));
  Shifter #(.width(32), .shift("ll")) shifter_1 (.in(\ID_EX_有符号扩展_out ), .\dist (5'b00010), .out(shifter_1_out));
  Adder #(.width(32)) adder_2 (.a(EX_PC), .b(32'h4), .out(adder_2_out));  // open: cin, cout
  Pull_Resistor #(.pull(1)) pull_resistor_1 (.node(controlled_buffer_1_out));
  MIPS_ALU mips_alu_1 (
    .X(ID_EX_a), .Y(multiplexer_9_out), .AluOP(AluOP2), .Equal(mips_alu_1_equal), .Result(mips_alu_1_result),
    .shamt(ID_EX_imm_out));  // open: Result_2
  Adder #(.width(32)) adder_3 (.a(shifter_1_out), .b(adder_2_out), .out(adder_3_out));  // open: cin, cout
  and and_5 (and_5_out, CLK, ~halt);  // AND_Gate
  EX_MEM_ideal ex_mem_ideal_1 (
    .MemToReg_in(MemToReg2), .IR_in(EX_IR), .MemWrite_in(MemWrite2), .PC_in(EX_PC), .RegWrite_in(RegWrite2),
    .Syscall_in(Syscall2), .A_in(ID_EX_a), .RegDst_in(RegDst2), .B(ID_EX_b), .ALU_in(mips_alu_1_result),
    .JR_in(JR2), .WriteReg(WriteReg2), .JAL_in(JAL2), .clk(and_5_out), .\同步清零 (RST), .MemToReg(MemToReg3),
    .IR_out(MEM_IR), .MemWrite(MemWrite), .PC_out(M_PC), .RegWrite(RegWrite3), .A(ex_mem_ideal_1_a),
    .SysCALL(Syscall3), .RegDst(RegDst3), .B_2(MDin), .Bne(JR3), .ALU_out(ex_mem_ideal_1_alu_out), .JR(JR3),
    .WriteReg_out(WriteReg3), .JAL(JAL3));  // open: SLLV_in, XOR_in, SH_in, BLTZ_in, ALUOP_in, ALU_SRC_in, LEDIN_IN, Beq_in, Bne_in, JMP_in, 使能, SLLV, XOR, SH, BLTZ, ALUOP, ALU_SRC, ledin, Beq, JMP
  Comparator #(.width(32), .mode("twosComplement")) comparator_2 (
    .a(32'h22), .b(ex_mem_ideal_1_a), .eq(comparator_2_eq));  // open: gt, lt
  Register #(.width(32), .trigger("rising"), .Select("low")) register_1 (
    .D(MDin), .en(ledin), .Q(LedData), .clk(CLK));  // open: clr
  \单周期硬布线控制器  \u_单周期硬布线控制器_1  (
    .Func(Func), .OP(ID_IR[31:26]), .ALU_OP(AluOP), .MemToReg(MemToReg), .MemWrite(MemWrite_t),
    .ALU_SRC(AluScrB), .RegWrite(RegWrite_t), .SysCALL(Syscall), .SignedExt(SignedExt), .RegDst(RegDst),
    .JR(JR), .JMP(JMP), .Beq(Beq), .JAL(JAL), .Bne(Bne));  // open: SLLV, XOR, SH, BLTZ
  and and_6 (ledin, Syscall3, comparator_2_eq);
  and and_7 (and_7_out, Syscall3, ~comparator_2_eq);  // AND_Gate
  RAM #(.addrWidth(10), .dataWidth(32), .bus("separate"), .Select("high")) ram_1 (
    .addr(ex_mem_ideal_1_alu_out[11:2]), .din(MDin), .data(ram_1_data), .str(MemWrite), .clk(CLK), .ld(1'b1));  // open: sel, clr
  Register #(.width(1), .trigger("rising"), .Select("low")) register_2 (
    .D(Syscall3), .en(and_7_out), .Q(halt), .clk(CLK), .clr(Go));
  not not_2 (not_2_out, halt);
  MEM_WB MEM_WB (
    .MemToReg_in(MemToReg3), .IR_in(MEM_IR), .PC_in(M_PC), .RegWrite_in(RegWrite3), .RD(ram_1_data),
    .ALU_in(ex_mem_ideal_1_alu_out), .WriteReg(WriteReg3), .JAL_in(JAL3), .clk(and_8_out), .\同步清零 (RST),
    .MemToReg(MemToReg4), .IR_out(WB_IR), .PC_out(WB_PC), .RegWrite(RegWrite), .RD_out(MEM_WB_rd_out),
    .ALU_out(MEM_WB_alu_out), .WriteReg_out(WriteReg4), .JAL(JAL4));  // open: ALUOP_in, MemWrite_in, ALU_SRC_in, Syscall_in, RegDst_in, Beq_in, Bne_in, JR_in, JMP_in, 使能, ALUOP, MemWrite, ALU_SRC, SysCALL, RegDst, Beq, Bne, JR, JMP, SLLV_in, SLLV, XOR_in, XOR, SH_in, SH, BLTZ_in, BLTZ, leddata, leddata_out, HALT_in, halt
  and and_8 (and_8_out, CLK, ~halt);  // AND_Gate
  Counter #(.width(16), .max('hffff), .ongoal("stay"), .trigger("rising"), .behavior("old")) counter_2 (
    .count(not_2_out), .Q(\总周期数 ), .clk(CLK));  // open: load, D, carry, clr, preset
  Multiplexer #(.select(1), .width(32), .disabled("Z"), .enable("false")) multiplexer_10 (
    .in0(MEM_WB_alu_out), .in1(MEM_WB_rd_out), .out(multiplexer_10_out), .sel(MemToReg4));
  Adder #(.width(32)) adder_4 (.a(WB_PC), .b(32'h4), .out(adder_4_out));  // open: cin, cout
  Multiplexer #(.select(1), .width(32), .disabled("Z"), .enable("false")) multiplexer_11 (
    .in0(multiplexer_10_out), .in1(adder_4_out), .out(RDin), .sel(JAL4));

  // Other names for the same wires on the sheet: ID_IR[5:0] = Func; OP[5:0] = ID_IR[31:26]; MEM_PC[31:0] = M_PC;
  //   MemWrite3 = MemWrite; RegWrite4 = RegWrite

  // Notes on the sheet:
  //   中断源
  //   时空图监测，可删除
  //   中断等待指示
  //   数码管输出
  //   指令存储器
  //   contents of rom_1 (hex, n*v repeats v):
  //   20100000 20110000 20120000 20130000 36100000 36310001 36520002 36730003 ae100000 ae110004 ae120008
  //   ae13000c 2002000a 20110000 20120000 20130000 c
  //   OP
  //   Func
  //   rs
  //   rt
  //   指令字
  //   rd
  //   控制位
  //   流水调试日志用
  //   暂停节拍，不能为0
  //   戳工具置1进入计数暂停模式，ctrl+k时钟自动运行到对应节拍暂停
  //   ctrl+k关闭时钟连续运行，将控制位置零，进入单步调试模式调试
  //   用这个时钟源需要去掉电路中的其他时钟源
  //   可计数暂停的时钟源
  //   为方便自动评测，需要输出流水线各段保存的PC值，注意是PC不是PC+4，另外ID段寄存器写入信息，Mem段内存写入信息也要输出
  //   JMP
  //   JR
  //   OP
  //   Func
  //   Beq
  //   Bne
  //   MemToReg
  //   MemWrite
  //   AluOP
  //   AluSrcB
  //   RegWrite
  //   JAL
  //   RegDst
  //   Syscall
endmodule

module \气泡流水线  (
  output RegWrite,
  output MemWrite,
  output [31:0] IF_PC,
  output [31:0] ID_PC,
  output [31:0] EX_PC,
  output [31:0] M_PC,
  output [31:0] WB_PC,
  output [31:0] RDin,
  output [31:0] MDin,
  output [31:0] LedData
);

  wire AluScrB, AluScrB2, and_1_out, and_2_out, and_3_out, and_4_out, and_6_out, and_7_out, and_8_out, Beq,
       Beq2, BLTZ, BLTZ2, Bne, Bne2, branch, CLK, clock_1_out, clock_2_out, comparator_1_eq, comparator_1_lt,
       comparator_2_eq, comparator_3_lt, d_ff_1_q, EX_halt, EX_ledin, Go, halt, \ID_EX_冲突 , \ID_EX气泡 ,
       \ID_MEM_冲突 , \IF_ID气泡 , IR1, IR2, IR3, JAL, JAL2, JAL3, JAL4, JMP, JMP2, JR, JR2, ledin, MemToReg,
       MemToReg2, MemToReg3, MemToReg4, MemWrite2, MemWrite_t, mips_alu_1_equal, multiplexer_9_out,
       nand_1_out, nor_1_out, nor_2_out, not_1_out, or_1_out, or_7_out, or_8_out, RegDst, RegDst2, RegDst3,
       RegWrite2, RegWrite3, RegWrite_t, RST, SH, SH2, SH3, SignedExt, SLLV, SLLV2, Syscall, Syscall2,
       Syscall3, W1, W2, W3, XOR, \数据相关检测_1_ex冲突1 , \数据相关检测_1_ex冲突2 , \数据相关检测_1_mem冲突1 , \数据相关检测_1_mem冲突2 ;
  wire [3:0] AluOP, AluOP2;
  wire [4:0] ID_EX_imm_out, ID_R1, ID_R2, multiplexer_4_out, multiplexer_11_out, WriteReg, WriteReg2,
       WriteReg3, WriteReg4;
  wire [5:0] Func;
  wire [12:0] CNT_num;
  wire [15:0] counter_5_q, counter_6_q, \LoadUse次数 , ram_1_data, ram_1_data_2, \总周期数 , \插入气泡数 , \无条件分支数 ,
       \条件分支成功数 ;
  wire [31:0] adder_2_out, adder_5_out, bit_extender_1_out, bit_extender_2_out, EX_IR, EX_MEM_alu_out,
       EX_MEM_b_2, GPR_rs, ID_EX_b, ID_EX_mux_out, \ID_EX_有符号扩展_out , IF_IR, JMPaddr2, leddata_t, MEM_IR,
       MEM_WB_alu_out, MEM_WB_rd_out, mips_alu_1_result, mips_regifilr_1_r1, mips_regifilr_1_r2,
       multiplexer_1_out, multiplexer_2_out, multiplexer_3_out, multiplexer_8_out, multiplexer_10_out,
       multiplexer_13_out, multiplexer_14_out, pc_4, PC_4_BranchAddr, shifter_1_out, WB_IR;
  wire [31:6] ID_IR;

  Button \u_总复位  (.out(RST));
  Button _1 (.out(IR1));
  Button _2 (.out(IR2));
  Button _3 (.out(IR3));
  // Probe on \总周期数 
  // Probe on \总周期数 
  Button \u_继续运行  (.out(Go));
  LED #(.active("true")) led_1 (.in(W1));
  LED #(.active("true")) led_2 (.in(W2));
  LED #(.active("true")) led_3 (.in(W3));
  Hex_Digit_Display hex_digit_display_1 (.value(LedData[31:28]));  // open: dp
  // Probe on IF_PC[19:0]
  // Mips_Probe mips_probe_1: pin names not known; wires that end beside it: IF_IR
  Hex_Digit_Display hex_digit_display_2 (.value(LedData[27:24]));  // open: dp
  Hex_Digit_Display hex_digit_display_3 (.value(LedData[23:20]));  // open: dp
  // Probe on ID_PC[19:0]
  // Mips_Probe mips_probe_2: pin names not known; wires that end beside it: {ID_IR, Func}
  Hex_Digit_Display hex_digit_display_4 (.value(LedData[15:12]));  // open: dp
  Hex_Digit_Display hex_digit_display_5 (.value(LedData[19:16]));  // open: dp
  Hex_Digit_Display hex_digit_display_6 (.value(LedData[11:8]));  // open: dp
  Hex_Digit_Display hex_digit_display_7 (.value(LedData[7:4]));  // open: dp
  Clock #(.highDuration(1), .lowDuration(1)) clock_1 (.out(clock_1_out));
  // Probe on EX_PC[19:0]
  // Mips_Probe mips_probe_3: pin names not known; wires that end beside it: clock_1_out, EX_IR, CLK
  Multiplexer #(.select(1), .width(32), .disabled("Z"), .enable("false")) multiplexer_1 (
    .in0(pc_4), .in1(PC_4_BranchAddr), .out(multiplexer_1_out), .sel(branch));
  Hex_Digit_Display hex_digit_display_8 (.value(LedData[3:0]));  // open: dp
  Multiplexer #(.select(1), .width(32), .disabled("Z"), .enable("false")) multiplexer_2 (
    .in0(multiplexer_1_out), .in1(JMPaddr2), .out(multiplexer_2_out), .sel(JMP2));
  Multiplexer #(.select(1), .width(32), .disabled("Z"), .enable("false")) multiplexer_3 (
    .in0(multiplexer_2_out), .in1(GPR_rs), .out(multiplexer_3_out), .sel(JR2));
  nor nor_1 (nor_1_out, \ID_MEM_冲突 , \ID_EX_冲突 , halt);
  // Probe on \总周期数 
  // Probe on M_PC[19:0]
  // Mips_Probe mips_probe_4: pin names not known; wires that end beside it: MEM_IR
  Register #(.width(32), .trigger("rising"), .Select("low")) PC (
    .D(multiplexer_3_out), .en(nor_1_out), .Q(IF_PC), .clk(CLK), .clr(RST));
  // Probe on \总周期数 
  // Probe on \无条件分支数 
  // Probe on \条件分支成功数 
  // Probe on \插入气泡数 
  // Probe on \LoadUse次数 
  Adder #(.width(32)) adder_1 (.a(IF_PC), .b(32'h4), .out(pc_4));  // open: cin, cout
  nor nor_2 (nor_2_out, \ID_MEM_冲突 , \ID_EX_冲突 );
  // Probe on IF_PC[11:0]
  // Probe on WB_PC[19:0]
  // Mips_Probe mips_probe_5: pin names not known; wires that end beside it: WB_IR
  and and_1 (and_1_out, CLK, ~halt);  // AND_Gate
  // Probe on ID_PC[11:0]
  // Probe on EX_PC[11:0]
  // Mips_Probe mips_probe_6: pin names not known; wires that end beside it: IF_IR
  ROM #(.addrWidth(10), .dataWidth(32), .Select("high")) rom_1 (.addr(IF_PC[11:2]), .data(IF_IR));
  IF_ID IF_ID (
    .PC_in(IF_PC), .IR_in(IF_IR), .clk(and_1_out), .\使能 (nor_2_out), .\同步清零 (or_1_out), .PC_out(ID_PC),
    .IR_out({ID_IR, Func}));
  or or_1 (or_1_out, \IF_ID气泡 , RST);
  or or_2 (\IF_ID气泡 , JMP2, branch);
  // Probe on M_PC[11:0]
  D_Flip_Flop #(.trigger("high"), .Pre_Clr_Positions("LEGACY"), .NegatePresetClear("false"), .enable("true"), .NewFFLayout("false")) d_ff_1 (.Q(d_ff_1_q));  // open: clk, D, Qn, preset, en, reset
  // Probe on 13'h1c2
  // Probe on WB_PC[11:0]
  Comparator #(.width(13), .mode("twosComplement")) comparator_1 (
    .a(CNT_num), .b(13'h1c2), .eq(comparator_1_eq), .lt(comparator_1_lt));  // open: gt
  Clock #(.highDuration(1), .lowDuration(1)) clock_2 (.out(clock_2_out));
  \数据相关检测  \u_数据相关检测_1  (
    .OP(ID_IR[31:26]), .FUNC(Func), .ID_ReadReg1(ID_R1), .EX_RegWrite(RegWrite2), .EX_WriteReg(WriteReg2),
    .MEM_WriteReg(WriteReg3), .ID_ReadReg2(ID_R2), .\EX冲突1 (\数据相关检测_1_ex冲突1 ), .\MEM冲突1 (\数据相关检测_1_mem冲突1 ),
    .\EX冲突2 (\数据相关检测_1_ex冲突2 ), .\MEM冲突2 (\数据相关检测_1_mem冲突2 ), .MEM_RegWrite(RegWrite3));
  Multiplexer #(.select(1), .width(5), .disabled("Z"), .enable("false")) multiplexer_4 (
    .in0(ID_IR[20:16]), .in1(ID_IR[15:11]), .out(multiplexer_4_out), .sel(RegDst));
  nand nand_1 (nand_1_out, d_ff_1_q, comparator_1_eq);
  Counter #(.width(13), .max('h1fff), .ongoal("stay"), .trigger("rising"), .behavior("old")) counter_1 (
    .count(comparator_1_lt), .Q(CNT_num), .clk(clock_2_out));  // open: load, D, carry, clr, preset
  Multiplexer #(.select(1), .width(5), .disabled("Z"), .enable("false")) multiplexer_5 (
    .in0(ID_IR[25:21]), .in1(5'b00010), .out(ID_R1), .sel(Syscall));
  Multiplexer #(.select(1), .width(5), .disabled("Z"), .enable("false")) multiplexer_6 (
    .in0(ID_IR[20:16]), .in1(5'b00100), .out(ID_R2), .sel(Syscall));
  Multiplexer #(.select(1), .width(5), .disabled("Z"), .enable("false")) multiplexer_7 (
    .in0(multiplexer_4_out), .in1({5{1'b1}}), .out(WriteReg), .sel(JAL));
  assign bit_extender_1_out = {{16{1'b0}}, {ID_IR[15:6], Func}};  // Bit_Extender bit_extender_1
  assign bit_extender_2_out = {{16{ID_IR[15]}}, {ID_IR[15:6], Func}};  // Bit_Extender bit_extender_2
  assign CLK = nand_1_out ? clock_2_out : 1'bz;  // Controlled_Buffer controlled_buffer_1
  or or_3 (\ID_EX_冲突 , \数据相关检测_1_ex冲突1 , \数据相关检测_1_ex冲突2 );
  or or_4 (\ID_MEM_冲突 , \数据相关检测_1_mem冲突1 , \数据相关检测_1_mem冲突2 );
  Multiplexer #(.select(1), .width(32), .disabled("Z"), .enable("false")) multiplexer_8 (
    .in0(bit_extender_1_out), .in1(bit_extender_2_out), .out(multiplexer_8_out), .sel(SignedExt));
  Pull_Resistor #(.pull(1)) pull_resistor_1 (.node(CLK));
  MIPS_REGIFILR mips_regifilr_1 (
    .Din(RDin), .Clk(CLK), .R1(mips_regifilr_1_r1), .R2(mips_regifilr_1_r2), .WE(RegWrite),
    .W_num(WriteReg4), .R1_num(ID_R1), .R2_num(ID_R2));
  and and_2 (and_2_out, CLK, ~halt);  // AND_Gate
  or or_5 (branch, and_3_out, and_4_out, multiplexer_9_out);
  or or_6 (\ID_EX气泡 , JMP2, \ID_MEM_冲突 , \ID_EX_冲突 , branch);
  and and_3 (and_3_out, Beq2, mips_alu_1_equal);
  and and_4 (and_4_out, Bne2, ~mips_alu_1_equal);  // AND_Gate
  ID_EX ID_EX (
    .IR_in({ID_IR, Func}), .ALUOP_in(AluOP), .PC_in(ID_PC), .MemToReg_in(MemToReg), .MemWrite_in(MemWrite_t),
    .R1(mips_regifilr_1_r1), .ALU_SRC_in(AluScrB), .RegWrite_in(RegWrite_t), .R2(mips_regifilr_1_r2),
    .Syscall_in(Syscall), .RegDst_in(RegDst), .IMM(ID_IR[10:6]), .Beq_in(Beq), .Bne_in(Bne),
    .MUX_in(multiplexer_8_out), .JR_in(JR), .JMP_in(JMP), .JAL_in(JAL), .\有符号扩展 (bit_extender_2_out),
    .clk(and_2_out), .\同步清零 (or_7_out), .IR_out(EX_IR), .ALUOP(AluOP2), .PC_out(EX_PC), .MemToReg(MemToReg2),
    .MemWrite(MemWrite2), .A(GPR_rs), .ALU_SRC(AluScrB2), .RegWrite(RegWrite2), .B(ID_EX_b),
    .SysCALL(Syscall2), .RegDst(RegDst2), .imm_out(ID_EX_imm_out), .Beq(Beq2), .Bne(Bne2),
    .MUX_out(ID_EX_mux_out), .JR(JR2), .JMP(JMP2), .JAL(JAL2), .\有符号扩展_out (\ID_EX_有符号扩展_out ),
    .WriteReg(WriteReg), .WriteReg_out(WriteReg2), .SLLV(SLLV2), .SH(SH2), .BLTZ(BLTZ2), .BLTZ_in(BLTZ),
    .SH_in(SH), .SLLV_in(SLLV), .JMPaddr({4'b0000, ID_IR[25:6], Func, 2'b00}), .JMPaddr_out(JMPaddr2));  // open: 使能, XOR, XOR_in, forward2, forward2_out, forward1, forward1_out
  or or_7 (or_7_out, \ID_EX气泡 , RST);
  Multiplexer #(.select(1), .width(1), .disabled("Z"), .enable("false")) multiplexer_9 (
    .in0(1'b0), .in1(comparator_3_lt), .out(multiplexer_9_out), .sel(BLTZ2));
  Multiplexer #(.select(1), .width(32), .disabled("Z"), .enable("false")) multiplexer_10 (
    .in0(ID_EX_b), .in1(ID_EX_mux_out), .out(multiplexer_10_out), .sel(AluScrB2));
  Shifter #(.width(32), .shift("ll")) shifter_1 (.in(\ID_EX_有符号扩展_out ), .\dist (5'b00010), .out(shifter_1_out));
  Adder #(.width(32)) adder_2 (.a(EX_PC), .b(32'h4), .out(adder_2_out));  // open: cin, cout
  Multiplexer #(.select(1), .width(5), .disabled("Z"), .enable("false")) multiplexer_11 (
    .in0(ID_EX_imm_out), .in1(GPR_rs[4:0]), .out(multiplexer_11_out), .sel(SLLV2));
  Adder #(.width(32)) adder_3 (.a(shifter_1_out), .b(adder_2_out), .out(PC_4_BranchAddr));  // open: cin, cout
  \单周期硬布线控制器  \u_单周期硬布线控制器_1  (
    .Func(Func), .OP(ID_IR[31:26]), .ALU_OP(AluOP), .MemToReg(MemToReg), .MemWrite(MemWrite_t),
    .ALU_SRC(AluScrB), .RegWrite(RegWrite_t), .SysCALL(Syscall), .SignedExt(SignedExt), .RegDst(RegDst),
    .JR(JR), .JMP(JMP), .Beq(Beq), .JAL(JAL), .Bne(Bne), .SLLV(SLLV), .XOR(XOR), .SH(SH), .BLTZ(BLTZ));
  Comparator #(.width(32), .mode("twosComplement")) comparator_2 (
    .a(32'h22), .b(GPR_rs), .eq(comparator_2_eq));  // open: gt, lt
  Comparator #(.width(32), .mode("twosComplement")) comparator_3 (
    .a(GPR_rs), .b({32{1'b0}}), .lt(comparator_3_lt));  // open: gt, eq
  MIPS_ALU mips_alu_1 (
    .X(GPR_rs), .Y(multiplexer_10_out), .AluOP(AluOP2), .Equal(mips_alu_1_equal), .Result(mips_alu_1_result),
    .shamt(multiplexer_11_out));  // open: Result_2
  and and_5 (EX_ledin, Syscall2, comparator_2_eq);
  and and_6 (and_6_out, Syscall2, ~comparator_2_eq);  // AND_Gate
  and and_7 (and_7_out, CLK, ~halt);  // AND_Gate
  Register #(.width(1), .trigger("rising"), .Select("low")) register_1 (
    .D(Syscall2), .en(and_6_out), .Q(EX_halt), .clk(CLK), .clr(Go));
  not not_1 (not_1_out, halt);
  or or_8 (or_8_out, JMP2, JR2);
  EX_MEM EX_MEM (
    .MemToReg_in(MemToReg2), .IR_in(EX_IR), .MemWrite_in(MemWrite2), .PC_in(EX_PC), .RegWrite_in(RegWrite2),
    .Syscall_in(Syscall2), .halt(EX_halt), .RegDst_in(RegDst2), .B(ID_EX_b), .ALU_in(mips_alu_1_result),
    .JAL_in(JAL2), .clk(and_7_out), .\同步清零 (RST), .MemToReg(MemToReg3), .IR_out(MEM_IR), .MemWrite(MemWrite),
    .PC_out(M_PC), .RegWrite(RegWrite3), .SysCALL(Syscall3), .halt_2(halt), .RegDst(RegDst3),
    .B_2(EX_MEM_b_2), .ALU_out(EX_MEM_alu_out), .JAL(JAL3), .WriteReg(WriteReg2), .WriteReg_out(WriteReg3),
    .SH_in(SH2), .SH(SH3), .LEDIN_IN(EX_ledin), .ledin(ledin));  // open: ALUOP_in, ALU_SRC_in, Beq_in, Bne_in, JR_in, JMP_in, 使能, ALUOP, ALU_SRC, Beq, Bne, JR, JMP, SLLV_in, SLLV, XOR_in, XOR, BLTZ_in, BLTZ
  Counter #(.width(16), .max('hffff), .ongoal("stay"), .trigger("rising"), .behavior("old")) counter_2 (
    .count(not_1_out), .Q(\总周期数 ), .clk(CLK), .clr(RST));  // open: load, D, carry, preset
  Counter #(.width(16), .max('hffff), .ongoal("stay"), .trigger("rising"), .behavior("old")) counter_3 (
    .count(or_8_out), .Q(\无条件分支数 ), .clk(CLK), .clr(RST));  // open: load, D, carry, preset
  Counter #(.width(16), .max('hffff), .ongoal("stay"), .trigger("rising"), .behavior("old")) counter_4 (
    .count(branch), .Q(\条件分支成功数 ), .clk(CLK), .clr(RST));  // open: load, D, carry, preset
  Multiplexer #(.select(1), .width(32), .disabled("Z"), .enable("false")) multiplexer_12 (
    .in0(EX_MEM_b_2), .in1(multiplexer_13_out), .out(MDin), .sel(SH3));
  Multiplexer #(.select(1), .width(32), .disabled("Z"), .enable("false")) multiplexer_13 (
    .in0({ram_1_data_2, EX_MEM_b_2[15:0]}), .in1({EX_MEM_b_2[15:0], ram_1_data}), .out(multiplexer_13_out),
    .sel(EX_MEM_alu_out[1]));
  Register #(.width(32), .trigger("rising"), .Select("low")) register_2 (
    .D(MDin), .en(ledin), .Q(leddata_t), .clk(CLK));  // open: clr
  RAM #(.addrWidth(10), .dataWidth(32), .bus("separate"), .Select("high")) ram_1 (
    .addr(EX_MEM_alu_out[11:2]), .din(MDin), .data({ram_1_data_2, ram_1_data}), .str(MemWrite), .clk(CLK),
    .ld(1'b1));  // open: sel, clr
  and and_8 (and_8_out, CLK, ~halt);  // AND_Gate
  Counter #(.width(16), .max('hffff), .ongoal("stay"), .trigger("rising"), .behavior("old")) counter_5 (
    .count(\IF_ID气泡 ), .Q(counter_5_q), .clk(CLK), .clr(RST));  // open: load, D, carry, preset
  Counter #(.width(16), .max('hffff), .ongoal("stay"), .trigger("rising"), .behavior("old")) counter_6 (
    .count(\ID_EX气泡 ), .Q(counter_6_q), .clk(CLK), .clr(RST));  // open: load, D, carry, preset
  MEM_WB MEM_WB (
    .MemToReg_in(MemToReg3), .IR_in(MEM_IR), .PC_in(M_PC), .RegWrite_in(RegWrite3),
    .RD({ram_1_data_2, ram_1_data}), .ALU_in(EX_MEM_alu_out), .WriteReg(WriteReg3), .JAL_in(JAL3),
    .clk(and_8_out), .\同步清零 (RST), .MemToReg(MemToReg4), .IR_out(WB_IR), .PC_out(WB_PC), .RegWrite(RegWrite),
    .RD_out(MEM_WB_rd_out), .ALU_out(MEM_WB_alu_out), .WriteReg_out(WriteReg4), .JAL(JAL4),
    .leddata(leddata_t), .leddata_out(LedData));  // open: ALUOP_in, MemWrite_in, ALU_SRC_in, Syscall_in, RegDst_in, Beq_in, Bne_in, JR_in, JMP_in, 使能, ALUOP, MemWrite, ALU_SRC, SysCALL, RegDst, Beq, Bne, JR, JMP, SLLV_in, SLLV, XOR_in, XOR, SH_in, SH, BLTZ_in, BLTZ, HALT_in, halt
  Adder #(.width(16)) adder_4 (.a(counter_5_q), .b(counter_6_q), .out(\插入气泡数 ));  // open: cin, cout
  Multiplexer #(.select(1), .width(32), .disabled("Z"), .enable("false")) multiplexer_14 (
    .in0(MEM_WB_alu_out), .in1(MEM_WB_rd_out), .out(multiplexer_14_out), .sel(MemToReg4));
  Adder #(.width(32)) adder_5 (.a(WB_PC), .b(32'h4), .out(adder_5_out));  // open: cin, cout
  Multiplexer #(.select(1), .width(32), .disabled("Z"), .enable("false")) multiplexer_15 (
    .in0(multiplexer_14_out), .in1(adder_5_out), .out(RDin), .sel(JAL4));

  // Other names for the same wires on the sheet: OP[5:0] = ID_IR[31:26]; ID_IR[5:0] = Func;
  //   JMPaddr[27:2] = {ID_IR[25:6], Func}; MEM_PC[31:0] = M_PC; MemWrite3 = MemWrite; RegWrite4 = RegWrite

  // Notes on the sheet:
  //   中断源
  //   时空图监测，可删除
  //   中断等待指示
  //   数码管输出
  //   指令存储器
  //   控制位
  //   contents of rom_1 (hex, n*v repeats v):
  //   20110001 8000c05 20110001 20120002 20130003 8000c09 20110001 20120002 20130003 8000c0d 20110001
  //   20120002 20130003 8000c11 20110001 20120002 20130003 c000cb8 20100001 20110001 118fc0 112020
  //   20020022 c 118882 12200001 8000c15 112020 20020022 c 20110001 118880 112020 20020022 c 12200001
  //   8000c1f 20110001 118fc0 112020 20020022 c 1188c3 112020 20020022 c 118903 112020 20020022 c 118903
  //   112020 20020022 c 118903 112020 20020022 c 118903 112020 20020022 c 118903 112020 20020022 c 118903
  //   112020 20020022 c 118903 112020 20020022 c 20100001 109fc0 139fc3 8021 2012000c 24160003 26100001
  //   3210000f 20080008 20090001 139900 2709825 132020 20020022 c 1094022 1500fff9 22100001 2018000f
  //   2188024 108700 20080008 20090001 139902 2709825 132021 20020022 c 1094022 1500fff9 108702 2c9b022
  //   12c00001 8000c50 4020 1084027 84400 3508ffff 82021 20020022 c 2010ffff 20110000 ae300000 22100001
  //   22310004 ae300000 22100001 22310004 ae300000 22100001 22310004 ae300000 22100001 22310004 ae300000
  //   22100001 22310004 ae300000 22100001 22310004 ae300000 22100001 22310004 ae300000 22100001 22310004
  //   ae300000 22100001 22310004 ae300000 22100001 22310004 ae300000 22100001 22310004 ae300000 22100001
  //   22310004 ae300000 22100001 22310004 ae300000 22100001 22310004 ae300000 22100001 22310004 ae300000
  //   22100001 22310004 22100001 8020 2011003c 8e130000 8e340000 274402a 11000002 ae330000 ae140000
  //   2231fffc 1611fff8 102020 20020022 c 22100004 2011003c 1611fff2 20020032 c 20100000 22100001 102020
  //   20020022 c 22100002 102020 20020022 c 22100003 102020 20020022 c 22100004 102020 20020022 c 22100005
  //   102020 20020022 c 22100006 102020 20020022 c 22100007 102020 20020022 c 22100008 102020 20020022
  //   20020022 c 3e00008
  //   流水调试日志用
  //   暂停节拍，不能为0
  //   OP
  //   Func
  //   rs
  //   rt
  //   指令字
  //   rd
  //   戳工具置1进入计数暂停模式，ctrl+k时钟自动运行到对应节拍暂停
  //   ctrl+k关闭时钟连续运行，将控制位置零，进入单步调试模式调试
  //   可计数暂停的时钟源
  //   为方便自动评测，需要输出流水线各段保存的PC值，注意是PC不是PC+4，另外ID段寄存器写入信息，Mem段内存写入信息也要输出
  //   JMP
  //   JR
  //   OP
  //   Func
  //   Beq
  //   Bne
  //   MemToReg
  //   MemWrite
  //   AluOP
  //   AluSrcB
  //   RegWrite
  //   JAL
  //   RegDst
  //   Syscall
endmodule

module \重定向流水线  (
  output RegWrite,
  output MemWrite,
  output [31:0] IF_PC,
  output [31:0] ID_PC,
  output [31:0] EX_PC,
  output [31:0] M_PC,
  output [31:0] WB_PC,
  output [31:0] RDin,
  output [31:0] MDin,
  output [31:0] LedData
);

  wire AluScrB, AluScrB2, and_1_out, and_2_out, and_3_out, and_4_out, and_6_out, and_7_out, and_8_out, Beq,
       Beq2, BLTZ, BLTZ2, Bne, Bne2, branch, CLK, clock_1_out, clock_2_out, comparator_1_eq, comparator_1_lt,
       comparator_3_lt, d_ff_1_q, EX_halt, EX_ledin, Go, halt, \ID_EX气泡 , \IF_ID气泡 , IR1, IR2, IR3, JAL,
       JAL2, JAL3, JAL4, JMP, JMP2, JR, JR2, ledin, load_use, MEM_halt, MEM_WB_halt, MemToReg, MemToReg2,
       MemToReg3, MemToReg4, MemWrite2, MemWrite_t, mips_alu_1_equal, multiplexer_9_out, nand_1_out,
       nor_1_out, not_1_out, not_2_out, or_1_out, or_4_out, or_6_out, RegDst, RegDst2, RegDst3, RegWrite2,
       RegWrite3, RegWrite_t, RST, SH, SH2, SH3, SignedExt, SLLV, SLLV2, Syscall, Syscall2, Syscall3,
       Syscall4, W1, W2, W3, XOR, \冲突 ;
  wire [1:0] EX_Forward1, EX_Forward2, Forward1, Forward2;
  wire [3:0] AluOP, AluOP2;
  wire [4:0] ID_EX_imm_out, ID_R1, ID_R2, multiplexer_4_out, multiplexer_11_out, WriteReg, WriteReg2,
       WriteReg3, WriteReg4;
  wire [5:0] Func;
  wire [12:0] CNT_num;
  wire [15:0] counter_5_q, counter_6_q, EX_MEM_b_2_2, \LoadUse次数 , ram_1_data, ram_1_data_2, \总周期数 , \插入气泡数 ,
       \无条件分支数 , \条件分支成功数 ;
  wire [31:0] adder_2_out, adder_5_out, ALU_in, ALU_out, bit_extender_1_out, bit_extender_2_out, EX_IR,
       EX_R1, EX_R2, GPR_rs, ID_EX_mux_out, \ID_EX_有符号扩展_out , IF_IR, JMPaddr2, leddata_t, MEM_IR,
       MEM_readData, mips_alu_1_result, mips_regifilr_1_r1, mips_regifilr_1_r2, multiplexer_1_out,
       multiplexer_2_out, multiplexer_3_out, multiplexer_8_out, multiplexer_10_out, multiplexer_14_out,
       multiplexer_16_out, pc_4, PC_4_BranchAddr, R2, shifter_1_out, WB_IR;
  wire [31:6] ID_IR;
  wire [31:16] EX_MEM_b_2;

  Button \u_总复位  (.out(RST));
  Button _1 (.out(IR1));
  Button _2 (.out(IR2));
  Button _3 (.out(IR3));
  // Probe on \总周期数 
  // Probe on \总周期数 
  Button \u_继续运行  (.out(Go));
  LED #(.active("true")) led_1 (.in(W1));
  LED #(.active("true")) led_2 (.in(W2));
  LED #(.active("true")) led_3 (.in(W3));
  Hex_Digit_Display hex_digit_display_1 (.value(LedData[31:28]));  // open: dp
  // Probe on IF_PC[19:0]
  // Mips_Probe mips_probe_1: pin names not known; wires that end beside it: IF_IR
  Hex_Digit_Display hex_digit_display_2 (.value(LedData[23:20]));  // open: dp
  Hex_Digit_Display hex_digit_display_3 (.value(LedData[27:24]));  // open: dp
  // Probe on ID_PC[19:0]
  // Mips_Probe mips_probe_2: pin names not known; wires that end beside it: {ID_IR, Func}
  Hex_Digit_Display hex_digit_display_4 (.value(LedData[15:12]));  // open: dp
  Hex_Digit_Display hex_digit_display_5 (.value(LedData[19:16]));  // open: dp
  Hex_Digit_Display hex_digit_display_6 (.value(LedData[7:4]));  // open: dp
  Hex_Digit_Display hex_digit_display_7 (.value(LedData[11:8]));  // open: dp
  Clock #(.highDuration(1), .lowDuration(1)) clock_1 (.out(clock_1_out));
  // Probe on EX_PC[19:0]
  // Mips_Probe mips_probe_3: pin names not known; wires that end beside it: clock_1_out, EX_IR, CLK
  Multiplexer #(.select(1), .width(32), .disabled("Z"), .enable("false")) multiplexer_1 (
    .in0(pc_4), .in1(PC_4_BranchAddr), .out(multiplexer_1_out), .sel(branch));
  Hex_Digit_Display hex_digit_display_8 (.value(LedData[3:0]));  // open: dp
  Multiplexer #(.select(1), .width(32), .disabled("Z"), .enable("false")) multiplexer_2 (
    .in0(multiplexer_1_out), .in1(JMPaddr2), .out(multiplexer_2_out), .sel(JMP2));
  Multiplexer #(.select(1), .width(32), .disabled("Z"), .enable("false")) multiplexer_3 (
    .in0(multiplexer_2_out), .in1(GPR_rs), .out(multiplexer_3_out), .sel(JR2));
  nor nor_1 (nor_1_out, load_use, halt);
  // Probe on \总周期数 
  // Probe on M_PC[19:0]
  // Mips_Probe mips_probe_4: pin names not known; wires that end beside it: MEM_IR
  \重定向检测  \u_重定向检测_1  (
    .MEM_MemToReg(MemToReg3), .OP(ID_IR[31:26]), .ID_ReadReg1(ID_R1), .FUNC(Func), .EX_WriteReg(WriteReg2),
    .EX_RegWrite(RegWrite2), .MEM_WriteReg(WriteReg3), .ID_ReadReg2(ID_R2), .FORWARD1(Forward1),
    .FORWARD2(Forward2), .MEM_RegWrite(RegWrite3), .EX_MemToReg(MemToReg2), .Load_Use(load_use), .\冲突 (\冲突 ));
  Register #(.width(32), .trigger("rising"), .Select("low")) PC (
    .D(multiplexer_3_out), .en(nor_1_out), .Q(IF_PC), .clk(CLK), .clr(RST));
  // Probe on \总周期数 
  // Probe on \无条件分支数 
  // Probe on \条件分支成功数 
  // Probe on \插入气泡数 
  // Probe on \LoadUse次数 
  Adder #(.width(32)) adder_1 (.a(IF_PC), .b(32'h4), .out(pc_4));  // open: cin, cout
  and and_1 (and_1_out, CLK, ~halt);  // AND_Gate
  // Probe on IF_PC[11:0]
  // Probe on WB_PC[19:0]
  // Mips_Probe mips_probe_5: pin names not known; wires that end beside it: WB_IR
  not not_1 (not_1_out, load_use);
  // Probe on EX_PC[11:0]
  // Probe on ID_PC[11:0]
  // Mips_Probe mips_probe_6: pin names not known; wires that end beside it: IF_IR
  ROM #(.addrWidth(10), .dataWidth(32), .Select("high")) rom_1 (.addr(IF_PC[11:2]), .data(IF_IR));
  IF_ID IF_ID (
    .PC_in(IF_PC), .IR_in(IF_IR), .clk(and_1_out), .\使能 (not_1_out), .\同步清零 (or_1_out), .PC_out(ID_PC),
    .IR_out({ID_IR, Func}));
  or or_1 (or_1_out, \IF_ID气泡 , RST);
  or or_2 (\IF_ID气泡 , JMP2, branch);
  // Probe on M_PC[11:0]
  D_Flip_Flop #(.trigger("high"), .Pre_Clr_Positions("LEGACY"), .NegatePresetClear("false"), .enable("true"), .NewFFLayout("false")) d_ff_1 (.Q(d_ff_1_q));  // open: clk, D, Qn, preset, en, reset
  // Probe on 13'h36
  // Probe on WB_PC[11:0]
  Comparator #(.width(13), .mode("twosComplement")) comparator_1 (
    .a(CNT_num), .b(13'h36), .eq(comparator_1_eq), .lt(comparator_1_lt));  // open: gt
  Clock #(.highDuration(1), .lowDuration(1)) clock_2 (.out(clock_2_out));
  Multiplexer #(.select(1), .width(5), .disabled("Z"), .enable("false")) multiplexer_4 (
    .in0(ID_IR[20:16]), .in1(ID_IR[15:11]), .out(multiplexer_4_out), .sel(RegDst));
  nand nand_1 (nand_1_out, d_ff_1_q, comparator_1_eq);
  Counter #(.width(13), .max('h1fff), .ongoal("stay"), .trigger("rising"), .behavior("old")) counter_1 (
    .count(comparator_1_lt), .Q(CNT_num), .clk(clock_2_out));  // open: load, D, carry, clr, preset
  Multiplexer #(.select(1), .width(5), .disabled("Z"), .enable("false")) multiplexer_5 (
    .in0(ID_IR[25:21]), .in1(5'b00010), .out(ID_R1), .sel(Syscall));
  Multiplexer #(.select(1), .width(5), .disabled("Z"), .enable("false")) multiplexer_6 (
    .in0(ID_IR[20:16]), .in1(5'b00100), .out(ID_R2), .sel(Syscall));
  Multiplexer #(.select(1), .width(5), .disabled("Z"), .enable("false")) multiplexer_7 (
    .in0(multiplexer_4_out), .in1({5{1'b1}}), .out(WriteReg), .sel(JAL));
  assign bit_extender_1_out = {{16{1'b0}}, {ID_IR[15:6], Func}};  // Bit_Extender bit_extender_1
  assign bit_extender_2_out = {{16{ID_IR[15]}}, {ID_IR[15:6], Func}};  // Bit_Extender bit_extender_2
  assign CLK = nand_1_out ? clock_2_out : 1'bz;  // Controlled_Buffer controlled_buffer_1
  Multiplexer #(.select(1), .width(32), .disabled("Z"), .enable("false")) multiplexer_8 (
    .in0(bit_extender_1_out), .in1(bit_extender_2_out), .out(multiplexer_8_out), .sel(SignedExt));
  Pull_Resistor #(.pull(1)) pull_resistor_1 (.node(CLK));
  MIPS_REGIFILR mips_regifilr_1 (
    .Din(RDin), .Clk(CLK), .R1(mips_regifilr_1_r1), .R2(mips_regifilr_1_r2), .WE(RegWrite),
    .W_num(WriteReg4), .R1_num(ID_R1), .R2_num(ID_R2));
  and and_2 (and_2_out, CLK, ~halt);  // AND_Gate
  or or_3 (branch, and_3_out, and_4_out, multiplexer_9_out);
  or or_4 (or_4_out, \ID_EX气泡 , RST);
  or or_5 (\ID_EX气泡 , JMP2, load_use, branch);
  and and_3 (and_3_out, Beq2, mips_alu_1_equal);
  and and_4 (and_4_out, Bne2, ~mips_alu_1_equal);  // AND_Gate
  ID_EX ID_EX (
    .IR_in({ID_IR, Func}), .ALUOP_in(AluOP), .PC_in(ID_PC), .MemToReg_in(MemToReg), .MemWrite_in(MemWrite_t),
    .R1(mips_regifilr_1_r1), .ALU_SRC_in(AluScrB), .RegWrite_in(RegWrite_t), .R2(mips_regifilr_1_r2),
    .Syscall_in(Syscall), .RegDst_in(RegDst), .IMM(ID_IR[10:6]), .Beq_in(Beq), .Bne_in(Bne),
    .MUX_in(multiplexer_8_out), .JR_in(JR), .JMP_in(JMP), .JAL_in(JAL), .\有符号扩展 (bit_extender_2_out),
    .clk(and_2_out), .\同步清零 (or_4_out), .IR_out(EX_IR), .ALUOP(AluOP2), .PC_out(EX_PC), .MemToReg(MemToReg2),
    .MemWrite(MemWrite2), .A(EX_R1), .ALU_SRC(AluScrB2), .RegWrite(RegWrite2), .B(EX_R2), .SysCALL(Syscall2),
    .RegDst(RegDst2), .imm_out(ID_EX_imm_out), .Beq(Beq2), .Bne(Bne2), .MUX_out(ID_EX_mux_out), .JR(JR2),
    .JMP(JMP2), .JAL(JAL2), .\有符号扩展_out (\ID_EX_有符号扩展_out ), .WriteReg(WriteReg), .WriteReg_out(WriteReg2),
    .SLLV(SLLV2), .SH(SH2), .BLTZ(BLTZ2), .BLTZ_in(BLTZ), .SH_in(SH), .SLLV_in(SLLV),
    .JMPaddr({4'b0000, ID_IR[25:6], Func, 2'b00}), .JMPaddr_out(JMPaddr2), .forward2(Forward2),
    .forward2_out(EX_Forward2), .forward1(Forward1), .forward1_out(EX_Forward1));  // open: 使能, XOR, XOR_in
  Multiplexer #(.select(1), .width(1), .disabled("Z"), .enable("false")) multiplexer_9 (
    .in0(1'b0), .in1(comparator_3_lt), .out(multiplexer_9_out), .sel(BLTZ2));
  Shifter #(.width(32), .shift("ll")) shifter_1 (.in(\ID_EX_有符号扩展_out ), .\dist (5'b00010), .out(shifter_1_out));
  Adder #(.width(32)) adder_2 (.a(EX_PC), .b(32'h4), .out(adder_2_out));  // open: cin, cout
  Multiplexer #(.select(1), .width(32), .disabled("Z"), .enable("false")) multiplexer_10 (
    .in0(R2), .in1(ID_EX_mux_out), .out(multiplexer_10_out), .sel(AluScrB2));
  Adder #(.width(32)) adder_3 (.a(shifter_1_out), .b(adder_2_out), .out(PC_4_BranchAddr));  // open: cin, cout
  \单周期硬布线控制器  \u_单周期硬布线控制器_1  (
    .Func(Func), .OP(ID_IR[31:26]), .ALU_OP(AluOP), .MemToReg(MemToReg), .MemWrite(MemWrite_t),
    .ALU_SRC(AluScrB), .RegWrite(RegWrite_t), .SysCALL(Syscall), .SignedExt(SignedExt), .RegDst(RegDst),
    .JR(JR), .JMP(JMP), .Beq(Beq), .JAL(JAL), .Bne(Bne), .SLLV(SLLV), .XOR(XOR), .SH(SH), .BLTZ(BLTZ));
  Comparator #(.width(32), .mode("twosComplement")) comparator_2 (
    .a(32'h22), .b(GPR_rs), .eq(EX_halt));  // open: gt, lt
  Comparator #(.width(32), .mode("twosComplement")) comparator_3 (
    .a(GPR_rs), .b({32{1'b0}}), .lt(comparator_3_lt));  // open: gt, eq
  MIPS_ALU mips_alu_1 (
    .X(GPR_rs), .Y(multiplexer_10_out), .AluOP(AluOP2), .Equal(mips_alu_1_equal), .Result(mips_alu_1_result),
    .shamt(multiplexer_11_out));  // open: Result_2
  Multiplexer #(.select(1), .width(5), .disabled("Z"), .enable("false")) multiplexer_11 (
    .in0(ID_EX_imm_out), .in1(GPR_rs[4:0]), .out(multiplexer_11_out), .sel(SLLV2));
  and and_5 (EX_ledin, Syscall2, EX_halt);
  and and_6 (and_6_out, CLK, ~halt);  // AND_Gate
  Multiplexer #(.select(2), .width(32), .disabled("Z"), .enable("false")) multiplexer_12 (
    .in0(EX_R1), .in1(ALU_out), .in2(MEM_readData), .in3(ALU_in), .out(GPR_rs), .sel(EX_Forward1));
  not not_2 (not_2_out, halt);
  or or_6 (or_6_out, JMP2, JR2);
  EX_MEM EX_MEM (
    .MemToReg_in(MemToReg2), .IR_in(EX_IR), .MemWrite_in(MemWrite2), .PC_in(EX_PC), .RegWrite_in(RegWrite2),
    .Syscall_in(Syscall2), .halt(EX_halt), .RegDst_in(RegDst2), .B(R2), .ALU_in(mips_alu_1_result),
    .JAL_in(JAL2), .clk(and_6_out), .\同步清零 (RST), .MemToReg(MemToReg3), .IR_out(MEM_IR), .MemWrite(MemWrite),
    .PC_out(M_PC), .RegWrite(RegWrite3), .SysCALL(Syscall3), .halt_2(MEM_halt), .RegDst(RegDst3),
    .B_2({EX_MEM_b_2, EX_MEM_b_2_2}), .ALU_out(ALU_in), .JAL(JAL3), .WriteReg(WriteReg2),
    .WriteReg_out(WriteReg3), .SH_in(SH2), .SH(SH3), .LEDIN_IN(EX_ledin), .ledin(ledin));  // open: ALUOP_in, ALU_SRC_in, Beq_in, Bne_in, JR_in, JMP_in, 使能, ALUOP, ALU_SRC, Beq, Bne, JR, JMP, SLLV_in, SLLV, XOR_in, XOR, BLTZ_in, BLTZ
  Counter #(.width(16), .max('hffff), .ongoal("stay"), .trigger("rising"), .behavior("old")) counter_2 (
    .count(not_2_out), .Q(\总周期数 ), .clk(CLK), .clr(RST));  // open: load, D, carry, preset
  Counter #(.width(16), .max('hffff), .ongoal("stay"), .trigger("rising"), .behavior("old")) counter_3 (
    .count(or_6_out), .Q(\无条件分支数 ), .clk(CLK), .clr(RST));  // open: load, D, carry, preset
  Counter #(.width(16), .max('hffff), .ongoal("stay"), .trigger("rising"), .behavior("old")) counter_4 (
    .count(branch), .Q(\条件分支成功数 ), .clk(CLK), .clr(RST));  // open: load, D, carry, preset
  Multiplexer #(.select(1), .width(32), .disabled("Z"), .enable("false")) multiplexer_13 (
    .in0({EX_MEM_b_2, EX_MEM_b_2_2}), .in1(multiplexer_14_out), .out(MDin), .sel(SH3));
  Multiplexer #(.select(1), .width(32), .disabled("Z"), .enable("false")) multiplexer_14 (
    .in0({ram_1_data_2, EX_MEM_b_2_2}), .in1({EX_MEM_b_2_2, ram_1_data}), .out(multiplexer_14_out),
    .sel(ALU_in[1]));
  Multiplexer #(.select(2), .width(32), .disabled("Z"), .enable("false")) multiplexer_15 (
    .in0(EX_R2), .in1(ALU_out), .in2(MEM_readData), .in3(ALU_in), .out(R2), .sel(EX_Forward2));
  Register #(.width(32), .trigger("rising"), .Select("low")) register_1 (
    .D(MDin), .en(ledin), .Q(leddata_t), .clk(CLK));  // open: clr
  RAM #(.addrWidth(10), .dataWidth(32), .bus("separate"), .Select("high")) ram_1 (
    .addr(ALU_in[11:2]), .din(MDin), .data({ram_1_data_2, ram_1_data}), .str(MemWrite), .clk(CLK), .ld(1'b1));  // open: sel, clr
  and and_7 (and_7_out, CLK, ~halt);  // AND_Gate
  Counter #(.width(16), .max('hffff), .ongoal("stay"), .trigger("rising"), .behavior("old")) counter_5 (
    .count(\IF_ID气泡 ), .Q(counter_5_q), .clk(CLK), .clr(RST));  // open: load, D, carry, preset
  Counter #(.width(16), .max('hffff), .ongoal("stay"), .trigger("rising"), .behavior("old")) counter_6 (
    .count(\ID_EX气泡 ), .Q(counter_6_q), .clk(CLK), .clr(RST));  // open: load, D, carry, preset
  Counter #(.width(16), .max('hffff), .ongoal("stay"), .trigger("rising"), .behavior("old")) counter_7 (
    .count(load_use), .Q(\LoadUse次数 ), .clk(CLK), .clr(RST));  // open: load, D, carry, preset
  MEM_WB MEM_WB (
    .MemToReg_in(MemToReg3), .IR_in(MEM_IR), .PC_in(M_PC), .RegWrite_in(RegWrite3), .Syscall_in(Syscall3),
    .RD({ram_1_data_2, ram_1_data}), .ALU_in(ALU_in), .WriteReg(WriteReg3), .JAL_in(JAL3), .clk(and_7_out),
    .\同步清零 (RST), .MemToReg(MemToReg4), .IR_out(WB_IR), .PC_out(WB_PC), .RegWrite(RegWrite),
    .SysCALL(Syscall4), .RD_out(MEM_readData), .ALU_out(ALU_out), .WriteReg_out(WriteReg4), .JAL(JAL4),
    .leddata(leddata_t), .leddata_out(LedData), .HALT_in(MEM_halt), .halt(MEM_WB_halt));  // open: ALUOP_in, MemWrite_in, ALU_SRC_in, RegDst_in, Beq_in, Bne_in, JR_in, JMP_in, 使能, ALUOP, MemWrite, ALU_SRC, RegDst, Beq, Bne, JR, JMP, SLLV_in, SLLV, XOR_in, XOR, SH_in, SH, BLTZ_in, BLTZ
  Adder #(.width(16)) adder_4 (.a(counter_5_q), .b(counter_6_q), .out(\插入气泡数 ));  // open: cin, cout
  Multiplexer #(.select(1), .width(32), .disabled("Z"), .enable("false")) multiplexer_16 (
    .in0(ALU_out), .in1(MEM_readData), .out(multiplexer_16_out), .sel(MemToReg4));
  Adder #(.width(32)) adder_5 (.a(WB_PC), .b(32'h4), .out(adder_5_out));  // open: cin, cout
  and and_8 (and_8_out, Syscall4, ~MEM_WB_halt);  // AND_Gate
  Multiplexer #(.select(1), .width(32), .disabled("Z"), .enable("false")) multiplexer_17 (
    .in0(multiplexer_16_out), .in1(adder_5_out), .out(RDin), .sel(JAL4));
  Register #(.width(1), .trigger("rising"), .Select("low")) register_2 (
    .D(Syscall4), .en(and_8_out), .Q(halt), .clk(CLK), .clr(Go));

  // Other names for the same wires on the sheet: OP[5:0] = ID_IR[31:26]; ID_IR[5:0] = Func;
  //   JMPaddr[27:2] = {ID_IR[25:6], Func}; MEM_PC[31:0] = M_PC; MemWrite3 = MemWrite; R1[31:0] = GPR_rs;
  //   RegWrite4 = RegWrite

  // Notes on the sheet:
  //   中断源
  //   时空图监测，可删除
  //   中断等待指示
  //   数码管输出
  //   指令存储器
  //   控制位
  //   contents of rom_1 (hex, n*v repeats v):
  //   20110001 8000c05 20110001 20120002 20130003 8000c09 20110001 20120002 20130003 8000c0d 20110001
  //   20120002 20130003 8000c11 20110001 20120002 20130003 c000d04 20100001 20110001 118fc0 112020
  //   20020022 c 118882 12200001 8000c15 112020 20020022 c 20110001 118880 112020 20020022 c 12200001
  //   8000c1f 20110001 118fc0 112020 20020022 c 1188c3 112020 20020022 c 118903 112020 20020022 c 118903
  //   112020 20020022 c 118903 112020 20020022 c 118903 112020 20020022 c 118903 112020 20020022 c 118903
  //   112020 20020022 c 118903 112020 20020022 c 20100001 109fc0 139fc3 8021 2012000c 24160003 26100001
  //   3210000f 20080008 20090001 139900 2709825 132020 20020022 c 1094022 1500fff9 22100001 2018000f
  //   2188024 108700 20080008 20090001 139902 2709825 132021 20020022 c 1094022 1500fff9 108702 2c9b022
  //   12c00001 8000c50 4020 1084027 84400 3508ffff 82021 20020022 c 2010ffff 20110000 ae300000 22100001
  //   22310004 ae300000 22100001 22310004 ae300000 22100001 22310004 ae300000 22100001 22310004 ae300000
  //   22100001 22310004 ae300000 22100001 22310004 ae300000 22100001 22310004 ae300000 22100001 22310004
  //   ae300000 22100001 22310004 ae300000 22100001 22310004 ae300000 22100001 22310004 ae300000 22100001
  //   22310004 ae300000 22100001 22310004 ae300000 22100001 22310004 ae300000 22100001 22310004 ae300000
  //   22100001 22310004 22100001 8020 2011003c 8e130000 8e340000 274402a 11000002 ae330000 ae140000
  //   2231fffc 1611fff8 102020 20020022 c 22100004 2011003c 1611fff2 20020032 c 0 0 0 20080001 20090003
  //   20110876 112020 20020022 c 200b0008 1118804 1318804 112020 20020022 c 216bffff 1560fff9 2002000a c 0
  //   0 0 2008ffff 20117777 112020 20020022 c 200b0010 2288826 112020 20020022 c 216bffff 1560fffa
  //   2002000a c 0 0 0 20090000 200b0020 20110001 20120001 a5310000 112020 20020022 c 2328820 21290002
  //   216bffff 1560fff8 200b0010 20090000 8d310000 112020 20020022 c 21290004 216bffff 1560fff9 2002000a c
  //   0 0 0 2011fff1 112020 20020022 c 22310001 620fffb 2002000a c 0 0 0 20100000 22100001 102020 20020022
  //   c 22100002 102020 20020022 c 22100003 102020 20020022 c 22100004 102020 20020022 c 22100005 102020
  //   20020022 c 22100006 102020 20020022 c 22100007 102020 20020022 c 22100008 102020 20020022 20020022 c
  //   3e00008
  //   流水调试日志用
  //   暂停节拍，不能为0
  //   OP
  //   Func
  //   rs
  //   rt
  //   指令字
  //   rd
  //   戳工具置1进入计数暂停模式，ctrl+k时钟自动运行到对应节拍暂停
  //   ctrl+k关闭时钟连续运行，将控制位置零，进入单步调试模式调试
  //   可计数暂停的时钟源
  //   为方便自动评测，需要输出流水线各段保存的PC值，注意是PC不是PC+4，另外ID段寄存器写入信息，Mem段内存写入信息也要输出
  //   JMP
  //   JR
  //   OP
  //   Func
  //   Beq
  //   Bne
  //   MemToReg
  //   MemWrite
  //   AluOP
  //   AluSrcB
  //   RegWrite
  //   JAL
  //   RegDst
  //   Syscall
endmodule

module \中断按键参考电路  (
  input  in_1,
  input  in_2,
  input  \同步清零信号 ,
  output \与中断屏蔽位与 ,
  output out_5
);

  wire and_1_out, d_ff_1_q, or_2_out;

  or or_1 (out_5, \与中断屏蔽位与 , d_ff_1_q);
  D_Flip_Flop #(.trigger("rising"), .Pre_Clr_Positions("LEGACY"), .NegatePresetClear("false"), .enable("true"), .NewFFLayout("false")) d_ff_1 (
    .clk(in_2), .D(1'b1), .Q(d_ff_1_q), .reset(\与中断屏蔽位与 ));  // open: Qn, preset, en
  or or_2 (or_2_out, d_ff_1_q, \与中断屏蔽位与 );
  and and_1 (and_1_out, or_2_out, ~\同步清零信号 );  // AND_Gate
  D_Flip_Flop #(.trigger("rising"), .Pre_Clr_Positions("LEGACY"), .NegatePresetClear("false"), .enable("true"), .NewFFLayout("false")) IR1 (
    .clk(in_1), .D(and_1_out), .Q(\与中断屏蔽位与 ));  // open: Qn, preset, en, reset

  // Notes on the sheet:
  //   中断信号采样参考电路
  //   Reset 
endmodule
module \单周期MIPS_单级中断  (
  input  IR1,
  input  IR2,
  input  IR3,
  output RegWrite,
  output MemWrite,
  output [31:0] PC,
  output [31:0] IR,
  output [31:0] RDin,
  output [31:0] MDin,
  output [31:0] LedData
);

  wire AluScrB, and_1_out, and_2_out, and_4_out, Beq, Bne, CLK, clock_2_out, comparator_1_eq,
       comparator_2_eq, comparator_3_eq, comparator_4_eq, comparator_5_eq, comparator_5_lt, comparator_7_eq,
       d_ff_1_q, decoder_1_out1, decoder_1_out2, decoder_1_out3, ERET, Go, halt, INT1, INT2, INT3, IR1_t,
       IR2_t, IR3_t, IRA, IRB, IRC, JAL, JMP, JR, ledin, MemToReg, mips_alu_1_equal, nand_1_out, not_1_out,
       not_2_out, not_3_out, or_1_out, or_5_out, or_6_out, priority_encoder_1_gs, RegDst, register_2_q, RST1,
       RST2, RST3, SignedExt, Syscall, W1, W2, W3, \中断 ;
  wire [1:0] INTNUM, register_4_q;
  wire [3:0] AluOP;
  wire [4:0] multiplexer_6_out, multiplexer_7_out, multiplexer_8_out, multiplexer_9_out;
  wire [12:0] CNT_num;
  wire [15:0] \总周期数 ;
  wire [31:0] adder_1_out, adder_2_out, bit_extender_1_out, bit_extender_2_out, EPC, mips_alu_1_result,
       mips_regifile_1_r1, multiplexer_1_out, multiplexer_2_out, multiplexer_4_out, multiplexer_5_out,
       multiplexer_10_out, multiplexer_12_out, multiplexer_14_out, PC_4, ram_1_data, shifter_1_out,
       \中断程序入口地址 ;

  Clock #(.highDuration(1), .lowDuration(1)) clock_1 ();  // open: out
  Button _1 ();  // open: out
  Button _2 ();  // open: out
  Button _3 ();  // open: out
  Button \u_继续运行  (.out(Go));
  LED #(.active("true")) led_1 (.in(W1));
  LED #(.active("true")) led_2 (.in(W2));
  LED #(.active("true")) led_3 (.in(W3));
  Hex_Digit_Display hex_digit_display_1 (.value(LedData[31:28]));  // open: dp
  Comparator #(.width(16), .mode("twosComplement")) comparator_1 (
    .a(16'h23b), .b(\总周期数 ), .eq(comparator_1_eq));  // open: gt, lt
  Comparator #(.width(16), .mode("twosComplement")) comparator_2 (
    .a(\总周期数 ), .b(16'h1), .eq(comparator_2_eq));  // open: gt, lt
  Comparator #(.width(16), .mode("twosComplement")) comparator_3 (
    .a(\总周期数 ), .b(16'h4), .eq(comparator_3_eq));  // open: gt, lt
  Comparator #(.width(16), .mode("twosComplement")) comparator_4 (
    .a(\总周期数 ), .b(16'h7), .eq(comparator_4_eq));  // open: gt, lt
  Multiplexer #(.select(1), .width(32), .disabled("Z"), .enable("false")) multiplexer_1 (
    .in0(adder_1_out), .in1(adder_2_out), .out(multiplexer_1_out), .sel(or_5_out));
  Multiplexer #(.select(1), .width(32), .disabled("Z"), .enable("false")) multiplexer_2 (
    .in0(multiplexer_1_out), .in1({4'b0000, IR[25:0], 2'b00}), .out(multiplexer_2_out), .sel(JMP));
  D_Flip_Flop #(.trigger("high"), .Pre_Clr_Positions("LEGACY"), .NegatePresetClear("false"), .enable("true"), .NewFFLayout("false")) d_ff_1 (.Q(d_ff_1_q));  // open: clk, D, Qn, preset, en, reset
  // Probe on 13'h2f6
  Hex_Digit_Display hex_digit_display_2 (.value(LedData[27:24]));  // open: dp
  Hex_Digit_Display hex_digit_display_3 (.value(LedData[23:20]));  // open: dp
  or or_1 (or_1_out, comparator_1_eq, comparator_2_eq);
  assign IRA = or_1_out ? ~CLK : 1'bz;  // Controlled_Inverter controlled_inverter_1
  assign IRB = comparator_3_eq ? ~CLK : 1'bz;  // Controlled_Inverter controlled_inverter_2
  assign IRC = comparator_4_eq ? ~CLK : 1'bz;  // Controlled_Inverter controlled_inverter_3
  Multiplexer #(.select(1), .width(32), .disabled("Z"), .enable("false")) multiplexer_3 (
    .in0(multiplexer_2_out), .in1(mips_regifile_1_r1), .out(PC_4), .sel(JR));
  Comparator #(.width(13), .mode("twosComplement")) comparator_5 (
    .a(CNT_num), .b(13'h2f6), .eq(comparator_5_eq), .lt(comparator_5_lt));  // open: gt
  Clock #(.highDuration(1), .lowDuration(1)) clock_2 (.out(clock_2_out));
  Hex_Digit_Display hex_digit_display_4 (.value(LedData[19:16]));  // open: dp
  Hex_Digit_Display hex_digit_display_5 (.value(LedData[15:12]));  // open: dp
  Pull_Resistor #(.pull(0)) pull_resistor_1 (.node(IRA));
  Pull_Resistor #(.pull(0)) pull_resistor_2 (.node(IRB));
  Pull_Resistor #(.pull(0)) pull_resistor_3 (.node(IRC));
  Multiplexer #(.select(1), .width(32), .disabled("Z"), .enable("false")) multiplexer_4 (
    .in0(PC_4), .in1(\中断程序入口地址 ), .out(multiplexer_4_out), .sel(\中断 ));
  Multiplexer #(.select(1), .width(32), .disabled("Z"), .enable("false")) multiplexer_5 (
    .in0(multiplexer_4_out), .in1(EPC), .out(multiplexer_5_out), .sel(ERET));
  nand nand_1 (nand_1_out, d_ff_1_q, comparator_5_eq);
  Counter #(.width(13), .max('h1fff), .ongoal("stay"), .trigger("rising"), .behavior("old")) counter_1 (
    .count(comparator_5_lt), .Q(CNT_num), .clk(clock_2_out));  // open: load, D, carry, clr, preset
  Hex_Digit_Display hex_digit_display_6 (.value(LedData[7:4]));  // open: dp
  Hex_Digit_Display hex_digit_display_7 (.value(LedData[11:8]));  // open: dp
  // Probe on \总周期数 
  // Probe on PC
  Register #(.width(32), .trigger("rising"), .Select("low")) u_PC (
    .D(multiplexer_5_out), .en(not_1_out), .Q(PC), .clk(CLK));  // open: clr
  not not_1 (not_1_out, halt);
  assign CLK = nand_1_out ? clock_2_out : 1'bz;  // Controlled_Buffer controlled_buffer_1
  Hex_Digit_Display hex_digit_display_8 (.value(LedData[3:0]));  // open: dp
  Adder #(.width(32)) adder_1 (.a(PC), .b(32'h4), .out(adder_1_out));  // open: cin, cout
  Pull_Resistor #(.pull(1)) pull_resistor_4 (.node(CLK));
  or or_2 (IR1_t, IR1, IRA);
  \中断按键参考电路  \u_中断按键参考电路_1  (.\与中断屏蔽位与 (INT1), .\同步清零信号 (RST1), .in_1(CLK), .in_2(IR1_t), .out_5(W1));
  \中断按键参考电路  \u_中断按键参考电路_2  (.\与中断屏蔽位与 (INT2), .\同步清零信号 (RST2), .in_1(CLK), .in_2(IR2_t), .out_5(W2));
  \中断按键参考电路  \u_中断按键参考电路_3  (.\与中断屏蔽位与 (INT3), .\同步清零信号 (RST3), .in_1(CLK), .in_2(IR3_t), .out_5(W3));
  // Mips_Probe mips_probe_1: pin names not known; wires that end beside it: IR
  ROM #(.addrWidth(10), .dataWidth(32), .Select("high")) rom_1 (.addr(PC[11:2]), .data(IR));
  or or_3 (IR2_t, IR2, IRB);
  Multiplexer #(.select(1), .width(5), .disabled("Z"), .enable("false")) multiplexer_6 (
    .in0(IR[25:21]), .in1(5'b00010), .out(multiplexer_6_out), .sel(Syscall));
  Multiplexer #(.select(1), .width(5), .disabled("Z"), .enable("false")) multiplexer_7 (
    .in0(IR[20:16]), .in1(5'b00100), .out(multiplexer_7_out), .sel(Syscall));
  Multiplexer #(.select(1), .width(5), .disabled("Z"), .enable("false")) multiplexer_8 (
    .in0(IR[20:16]), .in1(IR[15:11]), .out(multiplexer_8_out), .sel(RegDst));
  Multiplexer #(.select(1), .width(5), .disabled("Z"), .enable("false")) multiplexer_9 (
    .in0(multiplexer_8_out), .in1({5{1'b1}}), .out(multiplexer_9_out), .sel(JAL));
  assign bit_extender_1_out = {{16{1'b0}}, IR[15:0]};  // Bit_Extender bit_extender_1
  assign bit_extender_2_out = {{16{IR[15]}}, IR[15:0]};  // Bit_Extender bit_extender_2
  or or_4 (IR3_t, IR3, IRC);
  Multiplexer #(.select(1), .width(32), .disabled("Z"), .enable("false")) multiplexer_10 (
    .in0(bit_extender_1_out), .in1(bit_extender_2_out), .out(multiplexer_10_out), .sel(SignedExt));
  and and_1 (and_1_out, Beq, mips_alu_1_equal);
  or or_5 (or_5_out, and_1_out, and_2_out);
  and and_2 (and_2_out, Bne, ~mips_alu_1_equal);  // AND_Gate
  MIPS_Regifile mips_regifile_1 (
    .Din(RDin), .Clk(CLK), .R1(mips_regifile_1_r1), .R2(MDin), .WE(RegWrite), .W_num(multiplexer_9_out),
    .R1_num(multiplexer_6_out), .R2_num(multiplexer_7_out));
  Priority_Encoder #(.select(2), .disabled("Z")) priority_encoder_1 (
    .in0(1'b0), .in1(INT1), .in2(INT2), .in3(INT3), .out(INTNUM), .gs(priority_encoder_1_gs), .en_in(1'b1));  // open: en_out
  Multiplexer #(.select(2), .width(32), .disabled("Z"), .enable("false")) multiplexer_11 (
    .in1(32'h30ac), .in2(32'h3150), .in3(32'h31f4), .out(\中断程序入口地址 ), .sel(INTNUM));  // open: in0
  Comparator #(.width(32), .mode("twosComplement")) comparator_6 (.a(IR), .b(32'h42000018), .eq(ERET));  // open: gt, lt
  Multiplexer #(.select(1), .width(32), .disabled("Z"), .enable("false")) multiplexer_12 (
    .in0(MDin), .in1(multiplexer_10_out), .out(multiplexer_12_out), .sel(AluScrB));
  Shifter #(.width(32), .shift("ll")) shifter_1 (.in(bit_extender_2_out), .\dist (5'b00010), .out(shifter_1_out));
  MIPS_ALU mips_alu_1 (
    .X(mips_regifile_1_r1), .Y(multiplexer_12_out), .AluOP(AluOP), .Equal(mips_alu_1_equal),
    .Result(mips_alu_1_result), .shamt(IR[10:6]));  // open: Result_2
  Adder #(.width(32)) adder_2 (.a(shifter_1_out), .b(adder_1_out), .out(adder_2_out));  // open: cin, cout
  not not_2 (not_2_out, halt);
  or or_6 (or_6_out, \中断 , ERET);
  Comparator #(.width(32), .mode("twosComplement")) comparator_7 (
    .a(32'h22), .b(mips_regifile_1_r1), .eq(comparator_7_eq));  // open: gt, lt
  Counter #(.width(16), .max('hffff), .ongoal("stay"), .trigger("rising"), .behavior("old")) counter_2 (
    .count(not_2_out), .Q(\总周期数 ), .clk(CLK));  // open: load, D, carry, clr, preset
  and and_3 (ledin, Syscall, comparator_7_eq);
  and and_4 (and_4_out, Syscall, ~comparator_7_eq);  // AND_Gate
  Register #(.width(32), .trigger("rising"), .Select("low")) register_1 (
    .D(MDin), .en(ledin), .Q(LedData), .clk(CLK));  // open: clr
  Register #(.width(1), .trigger("rising"), .Select("low")) register_2 (
    .D(\中断 ), .en(or_6_out), .Q(register_2_q), .clk(CLK));  // open: clr
  not not_3 (not_3_out, register_2_q);
  Register #(.width(32), .trigger("rising"), .Select("low")) register_3 (
    .D(PC_4), .en(\中断 ), .Q(EPC), .clk(CLK));  // open: clr
  Register #(.width(2), .trigger("rising"), .Select("low")) register_4 (
    .D(INTNUM), .en(\中断 ), .Q(register_4_q), .clk(CLK));  // open: clr
  Register #(.width(1), .trigger("rising"), .Select("low")) register_5 (
    .D(Syscall), .en(and_4_out), .Q(halt), .clk(CLK), .clr(Go));
  RAM #(.addrWidth(10), .dataWidth(32), .bus("separate"), .Select("high")) ram_1 (
    .addr(mips_alu_1_result[11:2]), .din(MDin), .data(ram_1_data), .str(MemWrite), .clk(CLK), .ld(1'b1));  // open: sel, clr
  Multiplexer #(.select(1), .width(32), .disabled("Z"), .enable("false")) multiplexer_13 (
    .in0(multiplexer_14_out), .in1(adder_1_out), .out(RDin), .sel(JAL));
  and and_5 (\中断 , not_3_out, priority_encoder_1_gs);
  Decoder #(.select(2), .tristate("false"), .disabled("Z"), .enable("false")) decoder_1 (
    .out1(decoder_1_out1), .out2(decoder_1_out2), .out3(decoder_1_out3), .sel(register_4_q));  // open: out0
  Multiplexer #(.select(1), .width(32), .disabled("Z"), .enable("false")) multiplexer_14 (
    .in0(mips_alu_1_result), .in1(ram_1_data), .out(multiplexer_14_out), .sel(MemToReg));
  and and_6 (RST1, decoder_1_out1, ERET);
  and and_7 (RST2, decoder_1_out2, ERET);
  and and_8 (RST3, decoder_1_out3, ERET);
  \单周期硬布线控制器  \u_单周期硬布线控制器_1  (
    .Func(IR[5:0]), .OP(IR[31:26]), .ALU_OP(AluOP), .MemToReg(MemToReg), .MemWrite(MemWrite),
    .ALU_SRC(AluScrB), .RegWrite(RegWrite), .SysCALL(Syscall), .SignedExt(SignedExt), .RegDst(RegDst),
    .JR(JR), .JMP(JMP), .Beq(Beq), .JAL(JAL), .Bne(Bne));  // open: SLLV, XOR, SH, BLTZ

  // Other names for the same wires on the sheet: Func[5:0] = IR[5:0]; OP[5:0] = IR[31:26]

  // Notes on the sheet:
  //   中断源
  //   中断等待指示
  //   总复位信号应将除ROM以外所有存储组件全部清零
  //   控制位
  //   单级中断测试信号模拟器
  //   暂停节拍，不能为0
  //   戳工具置1进入计数暂停模式，ctrl+k时钟自动运行到对应节拍暂停
  //   ctrl+k关闭时钟连续运行，将控制位置零，进入单步调试模式调试
  //   用这个时钟源需要去掉电路中的其他时钟源
  //   数码管输出
  //   数码管输出应该用寄存器锁存，否则显示数据只能一闪而过
  //   可计数暂停的时钟源
  //   指令存储器
  //   指令字
  //   contents of rom_1 (hex, n*v repeats v):
  //   20110001 8000c05 20110001 20120002 20130003 8000c09 20110001 20120002 20130003 8000c0d 20110001
  //   20120002 20130003 8000c11 20110001 20120002 20130003 c000cb8 20100001 20110001 118fc0 112020
  //   20020022 c 118882 12200001 8000c15 112020 20020022 c 20110001 118880 112020 20020022 c 12200001
  //   8000c1f 20110001 118fc0 112020 20020022 c 1188c3 112020 20020022 c 118903 112020 20020022 c 118903
  //   112020 20020022 c 118903 112020 20020022 c 118903 112020 20020022 c 118903 112020 20020022 c 118903
  //   112020 20020022 c 118903 112020 20020022 c 20100001 109fc0 139fc3 8021 2012000c 24160003 26100001
  //   3210000f 20080008 20090001 139900 2709825 132020 20020022 c 1094022 1500fff9 22100001 2018000f
  //   2188024 108700 20080008 20090001 139902 2709825 132021 20020022 c 1094022 1500fff9 108702 2c9b022
  //   12c00001 8000c50 4020 1084027 84400 3508ffff 82021 20020022 c 2010ffff 20110000 ae300000 22100001
  //   22310004 ae300000 22100001 22310004 ae300000 22100001 22310004 ae300000 22100001 22310004 ae300000
  //   22100001 22310004 ae300000 22100001 22310004 ae300000 22100001 22310004 ae300000 22100001 22310004
  //   ae300000 22100001 22310004 ae300000 22100001 22310004 ae300000 22100001 22310004 ae300000 22100001
  //   22310004 ae300000 22100001 22310004 ae300000 22100001 22310004 ae300000 22100001 22310004 ae300000
  //   22100001 22310004 22100001 8020 2011003c 8e130000 8e340000 274402a 11000002 ae330000 ae140000
  //   2231fffc 1611fff8 102020 20020022 c 22100004 2011003c 1611fff2 20020032 c 20100000 22100001 102020
  //   20020022 c 22100002 102020 20020022 c 22100003 102020 20020022 c 22100004 102020 20020022 c 22100005
  //   102020 20020022 c 22100006 102020 20020022 c 22100007 102020 20020022 c 22100008 102020 20020022
  //   20020022 c 3e00008
  //   OP
  //   Func
  //   rs
  //   rt
  //   rd
  //   为方便自动评测，需要输出PC，IR，寄存器堆写如数据RDin
  //   RAM写使能MemWrite、RAM写入数据MDin等信号
  //   JMP
  //   JR
  //   OP
  //   Func
  //   Beq
  //   Bne
  //   MemToReg
  //   MemWrite
  //   AluOP
  //   AluSrcB
  //   RegWrite
  //   JAL
  //   RegDst
  //   Syscall
endmodule

module \单周期MIPS_多级中断  (
  input  IR1,
  input  IR2,
  input  IR3,
  output RegWrite,
  output MemWrite,
  output [31:0] PC,
  output [31:0] IR,
  output [31:0] RDin,
  output [31:0] MDin,
  output [31:0] LedData
);

  wire AluScrB, and_1_out, and_2_out, and_4_out, and_8_out, and_9_out, and_10_out, Beq, Bne, CLK,
       clock_2_out, comparator_1_eq, comparator_2_eq, comparator_3_eq, comparator_3_lt, comparator_4_eq,
       comparator_5_eq, comparator_6_eq, comparator_9_eq, comparator_11_eq, d_ff_1_q, decoder_1_out1,
       decoder_1_out2, decoder_1_out3, ERET, Go, halt, INT1, INT2, INT3, IR1_t, IR2_t, IR3_t, IRA, IRB, IRC,
       JAL, JMP, JR, ledin, MemToReg, MFC0, mips_alu_1_equal, MTC0, nand_1_out, not_1_out, not_2_out,
       not_3_out, or_1_out, or_2_out, or_6_out, or_7_out, or_8_out, or_9_out, or_10_out,
       priority_encoder_1_gs, RegDst, register_3_q, register_4_q, register_5_q, RST1, RST2, RST3, SignedExt,
       Syscall, W1, W2, W3, \中断 ;
  wire [1:0] INTNUM, multiplexer_16_out, nowNUM;
  wire [2:0] multiplexer_15_out;
  wire [3:0] AluOP;
  wire [4:0] multiplexer_6_out, multiplexer_7_out, multiplexer_8_out, multiplexer_10_out;
  wire [12:0] CNT_num;
  wire [15:0] \总周期数 ;
  wire [31:0] adder_1_out, adder_2_out, bit_extender_1_out, bit_extender_2_out, EPC, mips_alu_1_result,
       mips_regifile_1_r1, multiplexer_1_out, multiplexer_2_out, multiplexer_4_out, multiplexer_5_out,
       multiplexer_11_out, multiplexer_12_out, multiplexer_13_out, PC_4, ram_1_data, shifter_1_out,
       \中断程序入口地址 ;
  wire [31:2] \堆栈_2_pop ;

  Clock #(.highDuration(1), .lowDuration(1)) clock_1 ();  // open: out
  Button _1 ();  // open: out
  Button _2 ();  // open: out
  Button _3 ();  // open: out
  Button \u_继续运行  (.out(Go));
  LED #(.active("true")) led_1 (.in(W1));
  LED #(.active("true")) led_2 (.in(W2));
  LED #(.active("true")) led_3 (.in(W3));
  Multiplexer #(.select(1), .width(32), .disabled("Z"), .enable("false")) multiplexer_1 (
    .in0(adder_1_out), .in1(adder_2_out), .out(multiplexer_1_out), .sel(or_6_out));
  D_Flip_Flop #(.trigger("high"), .Pre_Clr_Positions("LEGACY"), .NegatePresetClear("false"), .enable("true"), .NewFFLayout("false")) d_ff_1 (.Q(d_ff_1_q));  // open: clk, D, Qn, preset, en, reset
  // Probe on 13'h230
  Hex_Digit_Display hex_digit_display_1 (.value(LedData[31:28]));  // open: dp
  Comparator #(.width(16), .mode("twosComplement")) comparator_1 (
    .a(\总周期数 ), .b(16'h7), .eq(comparator_1_eq));  // open: gt, lt
  Comparator #(.width(16), .mode("twosComplement")) comparator_2 (
    .a(\总周期数 ), .b(16'h241), .eq(comparator_2_eq));  // open: gt, lt
  Multiplexer #(.select(1), .width(32), .disabled("Z"), .enable("false")) multiplexer_2 (
    .in0(multiplexer_1_out), .in1({4'b0000, IR[25:0], 2'b00}), .out(multiplexer_2_out), .sel(JMP));
  Multiplexer #(.select(1), .width(32), .disabled("Z"), .enable("false")) multiplexer_3 (
    .in0(multiplexer_2_out), .in1(mips_regifile_1_r1), .out(PC_4), .sel(JR));
  Comparator #(.width(13), .mode("twosComplement")) comparator_3 (
    .a(CNT_num), .b(13'h230), .eq(comparator_3_eq), .lt(comparator_3_lt));  // open: gt
  Clock #(.highDuration(1), .lowDuration(1)) clock_2 (.out(clock_2_out));
  Hex_Digit_Display hex_digit_display_2 (.value(LedData[23:20]));  // open: dp
  Hex_Digit_Display hex_digit_display_3 (.value(LedData[27:24]));  // open: dp
  Comparator #(.width(16), .mode("twosComplement")) comparator_4 (
    .a(16'h258), .b(\总周期数 ), .eq(comparator_4_eq));  // open: gt, lt
  or or_1 (or_1_out, comparator_4_eq, comparator_5_eq);
  Comparator #(.width(16), .mode("twosComplement")) comparator_5 (
    .a(\总周期数 ), .b(16'h1), .eq(comparator_5_eq));  // open: gt, lt
  Comparator #(.width(16), .mode("twosComplement")) comparator_6 (
    .a(\总周期数 ), .b(16'h4), .eq(comparator_6_eq));  // open: gt, lt
  or or_2 (or_2_out, comparator_1_eq, comparator_2_eq);
  Multiplexer #(.select(1), .width(32), .disabled("Z"), .enable("false")) multiplexer_4 (
    .in0(PC_4), .in1(\中断程序入口地址 ), .out(multiplexer_4_out), .sel(\中断 ));
  Counter #(.width(13), .max('h1fff), .ongoal("stay"), .trigger("rising"), .behavior("old")) counter_1 (
    .count(comparator_3_lt), .Q(CNT_num), .clk(clock_2_out));  // open: load, D, carry, clr, preset
  Hex_Digit_Display hex_digit_display_4 (.value(LedData[15:12]));  // open: dp
  Hex_Digit_Display hex_digit_display_5 (.value(LedData[19:16]));  // open: dp
  Pull_Resistor #(.pull(0)) pull_resistor_1 (.node(IRA));
  assign IRA = or_1_out ? ~CLK : 1'bz;  // Controlled_Inverter controlled_inverter_1
  Pull_Resistor #(.pull(0)) pull_resistor_2 (.node(IRB));
  assign IRB = comparator_6_eq ? ~CLK : 1'bz;  // Controlled_Inverter controlled_inverter_2
  Pull_Resistor #(.pull(0)) pull_resistor_3 (.node(IRC));
  assign IRC = or_2_out ? ~CLK : 1'bz;  // Controlled_Inverter controlled_inverter_3
  Multiplexer #(.select(1), .width(32), .disabled("Z"), .enable("false")) multiplexer_5 (
    .in0(multiplexer_4_out), .in1(EPC), .out(multiplexer_5_out), .sel(ERET));
  Register #(.width(32), .trigger("rising"), .Select("low")) u_PC (
    .D(multiplexer_5_out), .en(not_1_out), .Q(PC), .clk(CLK));  // open: clr
  not not_1 (not_1_out, halt);
  nand nand_1 (nand_1_out, d_ff_1_q, comparator_3_eq);
  Hex_Digit_Display hex_digit_display_6 (.value(LedData[11:8]));  // open: dp
  Hex_Digit_Display hex_digit_display_7 (.value(LedData[7:4]));  // open: dp
  // Probe on \总周期数 
  // Probe on PC
  assign CLK = nand_1_out ? clock_2_out : 1'bz;  // Controlled_Buffer controlled_buffer_1
  Pull_Resistor #(.pull(1)) pull_resistor_4 (.node(CLK));
  Hex_Digit_Display hex_digit_display_8 (.value(LedData[3:0]));  // open: dp
  \中断按键参考电路  \u_中断按键参考电路_1  (.\与中断屏蔽位与 (INT1), .\同步清零信号 (RST1), .in_1(CLK), .in_2(IR1_t), .out_5(W1));
  \中断按键参考电路  \u_中断按键参考电路_2  (.\与中断屏蔽位与 (INT2), .\同步清零信号 (RST2), .in_1(CLK), .in_2(IR2_t), .out_5(W2));
  \中断按键参考电路  \u_中断按键参考电路_3  (.\与中断屏蔽位与 (INT3), .\同步清零信号 (RST3), .in_1(CLK), .in_2(IR3_t), .out_5(W3));
  Adder #(.width(32)) adder_1 (.a(PC), .b(32'h4), .out(adder_1_out));  // open: cin, cout
  // Mips_Probe mips_probe_1: pin names not known; wires that end beside it: IR
  ROM #(.addrWidth(10), .dataWidth(32), .Select("high")) rom_1 (.addr(PC[11:2]), .data(IR));
  or or_3 (IR1_t, IR1, IRA);
  or or_4 (IR2_t, IR2, IRB);
  Multiplexer #(.select(1), .width(5), .disabled("Z"), .enable("false")) multiplexer_6 (
    .in0(IR[20:16]), .in1(5'b00100), .out(multiplexer_6_out), .sel(Syscall));
  Multiplexer #(.select(1), .width(5), .disabled("Z"), .enable("false")) multiplexer_7 (
    .in0(IR[20:16]), .in1(IR[15:11]), .out(multiplexer_7_out), .sel(RegDst));
  Multiplexer #(.select(1), .width(5), .disabled("Z"), .enable("false")) multiplexer_8 (
    .in0(multiplexer_7_out), .in1({5{1'b1}}), .out(multiplexer_8_out), .sel(JAL));
  assign bit_extender_1_out = {{16{1'b0}}, IR[15:0]};  // Bit_Extender bit_extender_1
  assign bit_extender_2_out = {{16{IR[15]}}, IR[15:0]};  // Bit_Extender bit_extender_2
  Multiplexer #(.select(2), .width(32), .disabled("Z"), .enable("false")) multiplexer_9 (
    .in1(32'h30ac), .in2(32'h3158), .in3(32'h3204), .out(\中断程序入口地址 ), .sel(INTNUM));  // open: in0
  Comparator #(.width(32), .mode("twosComplement")) comparator_7 (.a(IR), .b(32'h42000018), .eq(ERET));  // open: gt, lt
  Multiplexer #(.select(1), .width(5), .disabled("Z"), .enable("false")) multiplexer_10 (
    .in0(IR[25:21]), .in1(5'b00010), .out(multiplexer_10_out), .sel(Syscall));
  Multiplexer #(.select(1), .width(32), .disabled("Z"), .enable("false")) multiplexer_11 (
    .in0(bit_extender_1_out), .in1(bit_extender_2_out), .out(multiplexer_11_out), .sel(SignedExt));
  or or_5 (IR3_t, IR3, IRC);
  or or_6 (or_6_out, and_1_out, and_2_out);
  MIPS_Regifile mips_regifile_1 (
    .Din(RDin), .Clk(CLK), .R1(mips_regifile_1_r1), .R2(MDin), .WE(RegWrite), .W_num(multiplexer_8_out),
    .R1_num(multiplexer_10_out), .R2_num(multiplexer_6_out));
  and and_1 (and_1_out, Beq, mips_alu_1_equal);
  and and_2 (and_2_out, Bne, ~mips_alu_1_equal);  // AND_Gate
  Multiplexer #(.select(1), .width(32), .disabled("Z"), .enable("false")) multiplexer_12 (
    .in0(MDin), .in1(multiplexer_11_out), .out(multiplexer_12_out), .sel(AluScrB));
  Shifter #(.width(32), .shift("ll")) shifter_1 (.in(bit_extender_2_out), .\dist (5'b00010), .out(shifter_1_out));
  Comparator #(.width(32), .mode("twosComplement")) comparator_8 (.a(IR), .b(32'h40800000), .eq(MTC0));  // open: gt, lt
  MIPS_ALU mips_alu_1 (
    .X(mips_regifile_1_r1), .Y(multiplexer_12_out), .AluOP(AluOP), .Equal(mips_alu_1_equal),
    .Result(mips_alu_1_result), .shamt(IR[10:6]));  // open: Result_2
  Adder #(.width(32)) adder_2 (.a(shifter_1_out), .b(adder_1_out), .out(adder_2_out));  // open: cin, cout
  Comparator #(.width(32), .mode("twosComplement")) comparator_9 (
    .a(32'h22), .b(mips_regifile_1_r1), .eq(comparator_9_eq));  // open: gt, lt
  Counter #(.width(16), .max('hffff), .ongoal("stay"), .trigger("rising"), .behavior("old")) counter_2 (
    .count(not_2_out), .Q(\总周期数 ), .clk(CLK));  // open: load, D, carry, clr, preset
  not not_2 (not_2_out, halt);
  \堆栈  \u_堆栈_1  (.push(PC_4), .pop(EPC), .choose(ERET), .en(or_7_out), .clk(CLK));
  or or_7 (or_7_out, ERET, \中断 );
  Register #(.width(32), .trigger("rising"), .Select("low")) register_1 (
    .D(MDin), .en(ledin), .Q(LedData), .clk(CLK));  // open: clr
  Comparator #(.width(32), .mode("twosComplement")) comparator_10 (
    .a(IR), .b(32'h40000000), .eq(MFC0));  // open: gt, lt
  and and_3 (ledin, Syscall, comparator_9_eq);
  and and_4 (and_4_out, Syscall, ~comparator_9_eq);  // AND_Gate
  RAM #(.addrWidth(10), .dataWidth(32), .bus("separate"), .Select("high")) ram_1 (
    .addr(mips_alu_1_result[11:2]), .din(MDin), .data(ram_1_data), .str(MemWrite), .clk(CLK), .ld(1'b1));  // open: sel, clr
  Register #(.width(1), .trigger("rising"), .Select("low")) register_2 (
    .D(Syscall), .en(and_4_out), .Q(halt), .clk(CLK), .clr(Go));
  Multiplexer #(.select(1), .width(32), .disabled("Z"), .enable("false")) multiplexer_13 (
    .in0(mips_alu_1_result), .in1(ram_1_data), .out(multiplexer_13_out), .sel(MemToReg));
  Multiplexer #(.select(1), .width(32), .disabled("Z"), .enable("false")) multiplexer_14 (
    .in0(multiplexer_13_out), .in1(adder_1_out), .out(RDin), .sel(JAL));
  // Probe on nowNUM
  Decoder #(.select(2), .tristate("false"), .disabled(0), .enable("true")) decoder_1 (
    .out1(decoder_1_out1), .out2(decoder_1_out2), .out3(decoder_1_out3), .sel(nowNUM), .en(ERET));  // open: out0
  \单周期硬布线控制器  \u_单周期硬布线控制器_1  (
    .Func(IR[5:0]), .OP(IR[31:26]), .ALU_OP(AluOP), .MemToReg(MemToReg), .MemWrite(MemWrite),
    .ALU_SRC(AluScrB), .RegWrite(RegWrite), .SysCALL(Syscall), .SignedExt(SignedExt), .RegDst(RegDst),
    .JR(JR), .JMP(JMP), .Beq(Beq), .JAL(JAL), .Bne(Bne));  // open: SLLV, XOR, SH, BLTZ
  and and_5 (RST1, decoder_1_out1, ERET);
  and and_6 (RST2, decoder_1_out2, ERET);
  and and_7 (RST3, decoder_1_out3, ERET);
  Multiplexer #(.select(2), .width(3), .disabled("Z"), .enable("false")) multiplexer_15 (
    .in0(3'b111), .in1(3'b111), .in2(3'b110), .in3(3'b100), .out(multiplexer_15_out), .sel(multiplexer_16_out));
  and and_8 (and_8_out, INT1, multiplexer_15_out[0]);
  and and_9 (and_9_out, INT2, multiplexer_15_out[1]);
  and and_10 (and_10_out, INT3, multiplexer_15_out[2]);
  Priority_Encoder #(.select(2), .disabled("Z")) priority_encoder_1 (
    .in0(1'b0), .in1(and_8_out), .in2(and_9_out), .in3(and_10_out), .out(INTNUM), .gs(priority_encoder_1_gs),
    .en_in(1'b1));  // open: en_out
  Multiplexer #(.select(1), .width(2), .disabled("Z"), .enable("false")) multiplexer_16 (
    .in0(2'b00), .in1(nowNUM), .out(multiplexer_16_out), .sel(priority_encoder_1_gs));
  \堆栈  \u_堆栈_2  (.push({{30{1'b0}}, INTNUM}), .pop({\堆栈_2_pop , nowNUM}), .choose(ERET), .en(or_8_out), .clk(CLK));
  or or_8 (or_8_out, ERET, \中断 );
  or or_9 (or_9_out, \中断 , MTC0);
  Register #(.width(1), .trigger("rising"), .Select("low")) register_3 (
    .D(or_9_out), .Q(register_3_q), .clk(CLK));  // open: en, clr
  or or_10 (or_10_out, ERET, MFC0);
  Register #(.width(1), .trigger("rising"), .Select("low")) register_4 (
    .D(or_10_out), .Q(register_4_q), .clk(CLK));  // open: en, clr
  Register #(.width(1), .trigger("rising"), .Select("low")) register_5 (
    .Q(register_5_q), .clk(CLK), .clr(register_4_q), .preset(register_3_q));  // open: D, en, cs
  not not_3 (not_3_out, register_5_q);
  Comparator #(.width(2), .mode("twosComplement")) comparator_11 (
    .a(nowNUM), .b(INTNUM), .eq(comparator_11_eq));  // open: gt, lt
  and and_11 (\中断 , not_3_out, priority_encoder_1_gs, ~comparator_11_eq);  // AND_Gate
  Pull_Resistor #(.pull(0)) pull_resistor_5 (.node(INTNUM));

  // Other names for the same wires on the sheet: Func[5:0] = IR[5:0]; OP[5:0] = IR[31:26]

  // Notes on the sheet:
  //   中断源
  //   中断等待指示
  //   总复位信号应将除ROM以外所有存储组件全部清零
  //   控制位
  //   暂停节拍，不能为0
  //   多级中断测试信号模拟器
  //   戳工具置1进入计数暂停模式，ctrl+k时钟自动运行到对应节拍暂停
  //   ctrl+k关闭时钟连续运行，将控制位置零，进入单步调试模式调试
  //   用这个时钟源需要去掉电路中的其他时钟源
  //   数码管输出
  //   数码管输出应该用寄存器锁存，否则显示数据只能一闪而过
  //   可计数暂停的时钟源
  //   指令存储器
  //   指令字
  //   contents of rom_1 (hex, n*v repeats v):
  //   201d07d0 20100001 109fc0 139fc3 8021 2012000c 24160008 26100001 3210000f 20080008 20090001 139900
  //   2709825 132020 20020022 c 1094022 1500fff9 22100001 2018000f 2188024 108700 20080008 20090001 139902
  //   2709825 132021 20020022 c 1094022 1500fff9 108702 2c9b022 12c00001 8000c07 4020 1084027 84400
  //   3508ffff 82021 20020022 c 8000c01 afa20000 23bd0004 afa40000 23bd0004 afb00000 23bd0004 afb30000
  //   23bd0004 afb40000 23bd0004 afb50000 23bd0004 afb60000 23bd0004 40000000 20160001 20140003 20150001
  //   168020 108100 2149825 132020 20020022 c 1600fffa 295a022 1680fff7 40800000 23bdfffc 8fb60000
  //   23bdfffc 8fb50000 23bdfffc 8fb40000 23bdfffc 8fb30000 23bdfffc 8fb00000 23bdfffc 8fa40000 23bdfffc
  //   8fa20000 42000018 afa20000 23bd0004 afa40000 23bd0004 afb00000 23bd0004 afb30000 23bd0004 afb40000
  //   23bd0004 afb50000 23bd0004 afb60000 23bd0004 40000000 20160002 20140003 20150001 168020 108100
  //   2149825 132020 20020022 c 1600fffa 295a022 1680fff7 40800000 23bdfffc 8fb60000 23bdfffc 8fb50000
  //   23bdfffc 8fb40000 23bdfffc 8fb30000 23bdfffc 8fb00000 23bdfffc 8fa40000 23bdfffc 8fa20000 42000018
  //   afa20000 23bd0004 afa40000 23bd0004 afb00000 23bd0004 afb30000 23bd0004 afb40000 23bd0004 afb50000
  //   23bd0004 afb60000 23bd0004 40000000 20160003 20140003 20150001 168020 108100 2149825 132020 20020022
  //   c 1600fffa 295a022 1680fff7 40800000 23bdfffc 8fb60000 23bdfffc 8fb50000 23bdfffc 8fb40000 23bdfffc
  //   8fb30000 23bdfffc 8fb00000 23bdfffc 8fa40000 23bdfffc 8fa20000 42000018
  //   OP
  //   Func
  //   rs
  //   rt
  //   rd
  //   为方便自动评测，需要输出PC，IR，寄存器堆写如数据RDin
  //   RAM写使能MemWrite、RAM写入数据MDin等信号
  //   JMP
  //   JR
  //   OP
  //   Func
  //   Beq
  //   Bne
  //   MemToReg
  //   MemWrite
  //   AluOP
  //   AluSrcB
  //   RegWrite
  //   JAL
  //   RegDst
  //   Syscall
endmodule

module \重定向流水线_单级中断  (
  input  IR1,
  input  IR2,
  input  IR3,
  output RegWrite,
  output MemWrite,
  output [31:0] IF_PC,
  output [31:0] ID_PC,
  output [31:0] EX_PC,
  output [31:0] M_PC,
  output [31:0] WB_PC,
  output [31:0] RDin,
  output [31:0] MDin,
  output [31:0] LedData
);

  wire _1_out, _2_out, _3_out, AluScrB, AluScrB2, and_1_out, and_2_out, and_3_out, and_4_out, and_6_out,
       and_7_out, and_8_out, Beq, Beq2, BLTZ, BLTZ2, Bne, Bne2, branch, CLK, clock_1_out, clock_2_out,
       comparator_1_eq, comparator_1_lt, comparator_3_lt, comparator_4_eq, comparator_5_eq, comparator_6_eq,
       comparator_7_eq, d_ff_1_q, decoder_1_out1, decoder_1_out2, decoder_1_out3, ERET, EX_halt, EX_ledin,
       Go, halt, \ID_EX气泡 , \IF_ID气泡 , INT1, INT2, INT3, IR1_t, IR2_t, IR3_t, IRA, IRB, IRC, JAL, JAL2, JAL3,
       JAL4, JMP, JMP2, JR, JR2, ledin, load_use, MEM_halt, MEM_WB_halt, MemToReg, MemToReg2, MemToReg3,
       MemToReg4, MemWrite2, MemWrite_t, mips_alu_1_equal, multiplexer_11_out, nand_1_out, nor_1_out,
       not_1_out, not_2_out, not_3_out, or_1_out, or_4_out, or_6_out, or_8_out, or_11_out,
       priority_encoder_1_gs, RegDst, RegDst2, RegDst3, register_3_q, RegWrite2, RegWrite3, RegWrite_t, RST,
       RST1, RST2, RST3, SH, SH2, SH3, SignedExt, SLLV, SLLV2, Syscall, Syscall2, Syscall3, Syscall4, W1, W2,
       W3, XOR, \中断 , \冲突 ;
  wire [1:0] EX_Forward1, EX_Forward2, Forward1, Forward2, INTNUM, register_5_q;
  wire [3:0] AluOP, AluOP2;
  wire [4:0] ID_EX_imm_out, ID_R1, ID_R2, multiplexer_6_out, multiplexer_13_out, WriteReg, WriteReg2,
       WriteReg3, WriteReg4;
  wire [5:0] Func;
  wire [12:0] CNT_num;
  wire [15:0] counter_5_q, counter_6_q, EX_MEM_b_2_2, \LoadUse次数 , ram_1_data, ram_1_data_2, \总周期数 , \插入气泡数 ,
       \无条件分支数 , \条件分支成功数 ;
  wire [31:0] adder_2_out, adder_5_out, ALU_in, ALU_out, bit_extender_1_out, bit_extender_2_out, EPC, EX_IR,
       EX_R1, EX_R2, GPR_rs, ID_EX_mux_out, \ID_EX_有符号扩展_out , IF_IR, JMPaddr2, leddata_t, MEM_IR,
       MEM_readData, mips_alu_1_result, mips_regifilr_1_r1, mips_regifilr_1_r2, multiplexer_1_out,
       multiplexer_2_out, multiplexer_4_out, multiplexer_5_out, multiplexer_10_out, multiplexer_12_out,
       multiplexer_16_out, multiplexer_18_out, PC_4, PC_4_BranchAddr, pc_4_t, R2, shifter_1_out, WB_IR,
       \中断程序入口地址 ;
  wire [31:6] ID_IR;
  wire [31:16] EX_MEM_b_2;

  Button \u_总复位  (.out(RST));
  Button _1 (.out(_1_out));
  Button _2 (.out(_2_out));
  Button _3 (.out(_3_out));
  // Probe on \总周期数 
  // Probe on \总周期数 
  Button \u_继续运行  (.out(Go));
  LED #(.active("true")) led_1 (.in(W1));
  LED #(.active("true")) led_2 (.in(W2));
  LED #(.active("true")) led_3 (.in(W3));
  Hex_Digit_Display hex_digit_display_1 (.value(LedData[31:28]));  // open: dp
  // Probe on IF_PC[19:0]
  // Mips_Probe mips_probe_1: pin names not known; wires that end beside it: _1_out, _2_out, _3_out, IR1_t, IR2_t, IR3_t, IF_IR
  Hex_Digit_Display hex_digit_display_2 (.value(LedData[27:24]));  // open: dp
  Hex_Digit_Display hex_digit_display_3 (.value(LedData[23:20]));  // open: dp
  // Probe on ID_PC[19:0]
  // Mips_Probe mips_probe_2: pin names not known; wires that end beside it: {ID_IR, Func}
  Hex_Digit_Display hex_digit_display_4 (.value(LedData[19:16]));  // open: dp
  Hex_Digit_Display hex_digit_display_5 (.value(LedData[15:12]));  // open: dp
  Multiplexer #(.select(1), .width(32), .disabled("Z"), .enable("false")) multiplexer_1 (
    .in0(pc_4_t), .in1(PC_4_BranchAddr), .out(multiplexer_1_out), .sel(branch));
  Multiplexer #(.select(1), .width(32), .disabled("Z"), .enable("false")) multiplexer_2 (
    .in0(multiplexer_1_out), .in1(JMPaddr2), .out(multiplexer_2_out), .sel(JMP2));
  Hex_Digit_Display hex_digit_display_6 (.value(LedData[11:8]));  // open: dp
  Hex_Digit_Display hex_digit_display_7 (.value(LedData[7:4]));  // open: dp
  Clock #(.highDuration(1), .lowDuration(1)) clock_1 (.out(clock_1_out));
  // Probe on EX_PC[19:0]
  // Mips_Probe mips_probe_3: pin names not known; wires that end beside it: clock_1_out, EX_IR, CLK
  Multiplexer #(.select(1), .width(32), .disabled("Z"), .enable("false")) multiplexer_3 (
    .in0(multiplexer_2_out), .in1(GPR_rs), .out(PC_4), .sel(JR2));
  Hex_Digit_Display hex_digit_display_8 (.value(LedData[3:0]));  // open: dp
  Multiplexer #(.select(1), .width(32), .disabled("Z"), .enable("false")) multiplexer_4 (
    .in0(PC_4), .in1(\中断程序入口地址 ), .out(multiplexer_4_out), .sel(\中断 ));
  Multiplexer #(.select(1), .width(32), .disabled("Z"), .enable("false")) multiplexer_5 (
    .in0(multiplexer_4_out), .in1(EPC), .out(multiplexer_5_out), .sel(ERET));
  nor nor_1 (nor_1_out, load_use, halt);
  // Probe on \总周期数 
  // Probe on M_PC[19:0]
  // Mips_Probe mips_probe_4: pin names not known; wires that end beside it: MEM_IR
  \重定向检测  \u_重定向检测_1  (
    .MEM_MemToReg(MemToReg3), .OP(ID_IR[31:26]), .ID_ReadReg1(ID_R1), .FUNC(Func), .EX_WriteReg(WriteReg2),
    .EX_RegWrite(RegWrite2), .MEM_WriteReg(WriteReg3), .ID_ReadReg2(ID_R2), .FORWARD1(Forward1),
    .FORWARD2(Forward2), .MEM_RegWrite(RegWrite3), .EX_MemToReg(MemToReg2), .Load_Use(load_use), .\冲突 (\冲突 ));
  Register #(.width(32), .trigger("rising"), .Select("low")) PC (
    .D(multiplexer_5_out), .en(nor_1_out), .Q(IF_PC), .clk(CLK), .clr(RST));
  // Probe on \总周期数 
  // Probe on \无条件分支数 
  // Probe on \条件分支成功数 
  // Probe on \插入气泡数 
  // Probe on \LoadUse次数 
  Adder #(.width(32)) adder_1 (.a(IF_PC), .b(32'h4), .out(pc_4_t));  // open: cin, cout
  and and_1 (and_1_out, CLK, ~halt);  // AND_Gate
  // Probe on IF_PC[11:0]
  // Probe on WB_PC[19:0]
  // Mips_Probe mips_probe_5: pin names not known; wires that end beside it: WB_IR
  not not_1 (not_1_out, load_use);
  // Probe on EX_PC[11:0]
  // Probe on ID_PC[11:0]
  // Mips_Probe mips_probe_6: pin names not known; wires that end beside it: IF_IR
  ROM #(.addrWidth(10), .dataWidth(32), .Select("high")) rom_1 (.addr(IF_PC[11:2]), .data(IF_IR));
  IF_ID IF_ID (
    .PC_in(IF_PC), .IR_in(IF_IR), .clk(and_1_out), .\使能 (not_1_out), .\同步清零 (or_1_out), .PC_out(ID_PC),
    .IR_out({ID_IR, Func}));
  or or_1 (or_1_out, \IF_ID气泡 , RST);
  or or_2 (\IF_ID气泡 , JMP2, \中断 , branch, ERET);
  // Probe on M_PC[11:0]
  D_Flip_Flop #(.trigger("high"), .Pre_Clr_Positions("LEGACY"), .NegatePresetClear("false"), .enable("true"), .NewFFLayout("false")) d_ff_1 (.Q(d_ff_1_q));  // open: clk, D, Qn, preset, en, reset
  // Probe on 13'h36
  // Probe on WB_PC[11:0]
  Comparator #(.width(13), .mode("twosComplement")) comparator_1 (
    .a(CNT_num), .b(13'h36), .eq(comparator_1_eq), .lt(comparator_1_lt));  // open: gt
  Clock #(.highDuration(1), .lowDuration(1)) clock_2 (.out(clock_2_out));
  Multiplexer #(.select(1), .width(5), .disabled("Z"), .enable("false")) multiplexer_6 (
    .in0(ID_IR[20:16]), .in1(ID_IR[15:11]), .out(multiplexer_6_out), .sel(RegDst));
  nand nand_1 (nand_1_out, d_ff_1_q, comparator_1_eq);
  Counter #(.width(13), .max('h1fff), .ongoal("stay"), .trigger("rising"), .behavior("old")) counter_1 (
    .count(comparator_1_lt), .Q(CNT_num), .clk(clock_2_out));  // open: load, D, carry, clr, preset
  Multiplexer #(.select(1), .width(5), .disabled("Z"), .enable("false")) multiplexer_7 (
    .in0(ID_IR[25:21]), .in1(5'b00010), .out(ID_R1), .sel(Syscall));
  Multiplexer #(.select(1), .width(5), .disabled("Z"), .enable("false")) multiplexer_8 (
    .in0(ID_IR[20:16]), .in1(5'b00100), .out(ID_R2), .sel(Syscall));
  Multiplexer #(.select(1), .width(5), .disabled("Z"), .enable("false")) multiplexer_9 (
    .in0(multiplexer_6_out), .in1({5{1'b1}}), .out(WriteReg), .sel(JAL));
  assign bit_extender_1_out = {{16{1'b0}}, {ID_IR[15:6], Func}};  // Bit_Extender bit_extender_1
  assign bit_extender_2_out = {{16{ID_IR[15]}}, {ID_IR[15:6], Func}};  // Bit_Extender bit_extender_2
  assign CLK = nand_1_out ? clock_2_out : 1'bz;  // Controlled_Buffer controlled_buffer_1
  Multiplexer #(.select(1), .width(32), .disabled("Z"), .enable("false")) multiplexer_10 (
    .in0(bit_extender_1_out), .in1(bit_extender_2_out), .out(multiplexer_10_out), .sel(SignedExt));
  Pull_Resistor #(.pull(1)) pull_resistor_1 (.node(CLK));
  MIPS_REGIFILR mips_regifilr_1 (
    .Din(RDin), .Clk(CLK), .R1(mips_regifilr_1_r1), .R2(mips_regifilr_1_r2), .WE(RegWrite),
    .W_num(WriteReg4), .R1_num(ID_R1), .R2_num(ID_R2));
  and and_2 (and_2_out, CLK, ~halt);  // AND_Gate
  or or_3 (branch, and_3_out, and_4_out, multiplexer_11_out);
  or or_4 (or_4_out, \ID_EX气泡 , RST);
  or or_5 (\ID_EX气泡 , \中断 , JMP2, ERET, load_use, branch);
  and and_3 (and_3_out, Beq2, mips_alu_1_equal);
  and and_4 (and_4_out, Bne2, ~mips_alu_1_equal);  // AND_Gate
  ID_EX ID_EX (
    .IR_in({ID_IR, Func}), .ALUOP_in(AluOP), .PC_in(ID_PC), .MemToReg_in(MemToReg), .MemWrite_in(MemWrite_t),
    .R1(mips_regifilr_1_r1), .ALU_SRC_in(AluScrB), .RegWrite_in(RegWrite_t), .R2(mips_regifilr_1_r2),
    .Syscall_in(Syscall), .RegDst_in(RegDst), .IMM(ID_IR[10:6]), .Beq_in(Beq), .Bne_in(Bne),
    .MUX_in(multiplexer_10_out), .JR_in(JR), .JMP_in(JMP), .JAL_in(JAL), .\有符号扩展 (bit_extender_2_out),
    .clk(and_2_out), .\同步清零 (or_4_out), .IR_out(EX_IR), .ALUOP(AluOP2), .PC_out(EX_PC), .MemToReg(MemToReg2),
    .MemWrite(MemWrite2), .A(EX_R1), .ALU_SRC(AluScrB2), .RegWrite(RegWrite2), .B(EX_R2), .SysCALL(Syscall2),
    .RegDst(RegDst2), .imm_out(ID_EX_imm_out), .Beq(Beq2), .Bne(Bne2), .MUX_out(ID_EX_mux_out), .JR(JR2),
    .JMP(JMP2), .JAL(JAL2), .\有符号扩展_out (\ID_EX_有符号扩展_out ), .WriteReg(WriteReg), .WriteReg_out(WriteReg2),
    .SLLV(SLLV2), .SH(SH2), .BLTZ(BLTZ2), .BLTZ_in(BLTZ), .SH_in(SH), .SLLV_in(SLLV),
    .JMPaddr({4'b0000, ID_IR[25:6], Func, 2'b00}), .JMPaddr_out(JMPaddr2), .forward2(Forward2),
    .forward2_out(EX_Forward2), .forward1(Forward1), .forward1_out(EX_Forward1));  // open: 使能, XOR, XOR_in
  Multiplexer #(.select(1), .width(1), .disabled("Z"), .enable("false")) multiplexer_11 (
    .in0(1'b0), .in1(comparator_3_lt), .out(multiplexer_11_out), .sel(BLTZ2));
  Shifter #(.width(32), .shift("ll")) shifter_1 (.in(\ID_EX_有符号扩展_out ), .\dist (5'b00010), .out(shifter_1_out));
  Adder #(.width(32)) adder_2 (.a(EX_PC), .b(32'h4), .out(adder_2_out));  // open: cin, cout
  Multiplexer #(.select(1), .width(32), .disabled("Z"), .enable("false")) multiplexer_12 (
    .in0(R2), .in1(ID_EX_mux_out), .out(multiplexer_12_out), .sel(AluScrB2));
  Adder #(.width(32)) adder_3 (.a(shifter_1_out), .b(adder_2_out), .out(PC_4_BranchAddr));  // open: cin, cout
  \单周期硬布线控制器  \u_单周期硬布线控制器_1  (
    .Func(Func), .OP(ID_IR[31:26]), .ALU_OP(AluOP), .MemToReg(MemToReg), .MemWrite(MemWrite_t),
    .ALU_SRC(AluScrB), .RegWrite(RegWrite_t), .SysCALL(Syscall), .SignedExt(SignedExt), .RegDst(RegDst),
    .JR(JR), .JMP(JMP), .Beq(Beq), .JAL(JAL), .Bne(Bne), .SLLV(SLLV), .XOR(XOR), .SH(SH), .BLTZ(BLTZ));
  Comparator #(.width(32), .mode("twosComplement")) comparator_2 (
    .a(32'h22), .b(GPR_rs), .eq(EX_halt));  // open: gt, lt
  Comparator #(.width(32), .mode("twosComplement")) comparator_3 (
    .a(GPR_rs), .b({32{1'b0}}), .lt(comparator_3_lt));  // open: gt, eq
  MIPS_ALU mips_alu_1 (
    .X(GPR_rs), .Y(multiplexer_12_out), .AluOP(AluOP2), .Equal(mips_alu_1_equal), .Result(mips_alu_1_result),
    .shamt(multiplexer_13_out));  // open: Result_2
  Multiplexer #(.select(1), .width(5), .disabled("Z"), .enable("false")) multiplexer_13 (
    .in0(ID_EX_imm_out), .in1(GPR_rs[4:0]), .out(multiplexer_13_out), .sel(SLLV2));
  and and_5 (EX_ledin, Syscall2, EX_halt);
  and and_6 (and_6_out, CLK, ~halt);  // AND_Gate
  Multiplexer #(.select(2), .width(32), .disabled("Z"), .enable("false")) multiplexer_14 (
    .in0(EX_R1), .in1(ALU_out), .in2(MEM_readData), .in3(ALU_in), .out(GPR_rs), .sel(EX_Forward1));
  not not_2 (not_2_out, halt);
  or or_6 (or_6_out, JMP2, JR2);
  EX_MEM EX_MEM (
    .MemToReg_in(MemToReg2), .IR_in(EX_IR), .MemWrite_in(MemWrite2), .PC_in(EX_PC), .RegWrite_in(RegWrite2),
    .Syscall_in(Syscall2), .halt(EX_halt), .RegDst_in(RegDst2), .B(R2), .ALU_in(mips_alu_1_result),
    .JAL_in(JAL2), .clk(and_6_out), .\同步清零 (RST), .MemToReg(MemToReg3), .IR_out(MEM_IR), .MemWrite(MemWrite),
    .PC_out(M_PC), .RegWrite(RegWrite3), .SysCALL(Syscall3), .halt_2(MEM_halt), .RegDst(RegDst3),
    .B_2({EX_MEM_b_2, EX_MEM_b_2_2}), .ALU_out(ALU_in), .JAL(JAL3), .WriteReg(WriteReg2),
    .WriteReg_out(WriteReg3), .SH_in(SH2), .SH(SH3), .LEDIN_IN(EX_ledin), .ledin(ledin));  // open: ALUOP_in, ALU_SRC_in, Beq_in, Bne_in, JR_in, JMP_in, 使能, ALUOP, ALU_SRC, Beq, Bne, JR, JMP, SLLV_in, SLLV, XOR_in, XOR, BLTZ_in, BLTZ
  Counter #(.width(16), .max('hffff), .ongoal("stay"), .trigger("rising"), .behavior("old")) counter_2 (
    .count(not_2_out), .Q(\总周期数 ), .clk(CLK), .clr(RST));  // open: load, D, carry, preset
  Counter #(.width(16), .max('hffff), .ongoal("stay"), .trigger("rising"), .behavior("old")) counter_3 (
    .count(or_6_out), .Q(\无条件分支数 ), .clk(CLK), .clr(RST));  // open: load, D, carry, preset
  Counter #(.width(16), .max('hffff), .ongoal("stay"), .trigger("rising"), .behavior("old")) counter_4 (
    .count(branch), .Q(\条件分支成功数 ), .clk(CLK), .clr(RST));  // open: load, D, carry, preset
  Multiplexer #(.select(1), .width(32), .disabled("Z"), .enable("false")) multiplexer_15 (
    .in0({EX_MEM_b_2, EX_MEM_b_2_2}), .in1(multiplexer_16_out), .out(MDin), .sel(SH3));
  Multiplexer #(.select(1), .width(32), .disabled("Z"), .enable("false")) multiplexer_16 (
    .in0({ram_1_data_2, EX_MEM_b_2_2}), .in1({EX_MEM_b_2_2, ram_1_data}), .out(multiplexer_16_out),
    .sel(ALU_in[1]));
  Multiplexer #(.select(2), .width(32), .disabled("Z"), .enable("false")) multiplexer_17 (
    .in0(EX_R2), .in1(ALU_out), .in2(MEM_readData), .in3(ALU_in), .out(R2), .sel(EX_Forward2));
  Register #(.width(32), .trigger("rising"), .Select("low")) register_1 (
    .D(MDin), .en(ledin), .Q(leddata_t), .clk(CLK));  // open: clr
  RAM #(.addrWidth(10), .dataWidth(32), .bus("separate"), .Select("high")) ram_1 (
    .addr(ALU_in[11:2]), .din(MDin), .data({ram_1_data_2, ram_1_data}), .str(MemWrite), .clk(CLK), .ld(1'b1));  // open: sel, clr
  and and_7 (and_7_out, CLK, ~halt);  // AND_Gate
  Counter #(.width(16), .max('hffff), .ongoal("stay"), .trigger("rising"), .behavior("old")) counter_5 (
    .count(\IF_ID气泡 ), .Q(counter_5_q), .clk(CLK), .clr(RST));  // open: load, D, carry, preset
  Counter #(.width(16), .max('hffff), .ongoal("stay"), .trigger("rising"), .behavior("old")) counter_6 (
    .count(\ID_EX气泡 ), .Q(counter_6_q), .clk(CLK), .clr(RST));  // open: load, D, carry, preset
  Counter #(.width(16), .max('hffff), .ongoal("stay"), .trigger("rising"), .behavior("old")) counter_7 (
    .count(load_use), .Q(\LoadUse次数 ), .clk(CLK), .clr(RST));  // open: load, D, carry, preset
  MEM_WB MEM_WB (
    .MemToReg_in(MemToReg3), .IR_in(MEM_IR), .PC_in(M_PC), .RegWrite_in(RegWrite3), .Syscall_in(Syscall3),
    .RD({ram_1_data_2, ram_1_data}), .ALU_in(ALU_in), .WriteReg(WriteReg3), .JAL_in(JAL3), .clk(and_7_out),
    .\同步清零 (RST), .MemToReg(MemToReg4), .IR_out(WB_IR), .PC_out(WB_PC), .RegWrite(RegWrite),
    .SysCALL(Syscall4), .RD_out(MEM_readData), .ALU_out(ALU_out), .WriteReg_out(WriteReg4), .JAL(JAL4),
    .leddata(leddata_t), .leddata_out(LedData), .HALT_in(MEM_halt), .halt(MEM_WB_halt));  // open: ALUOP_in, MemWrite_in, ALU_SRC_in, RegDst_in, Beq_in, Bne_in, JR_in, JMP_in, 使能, ALUOP, MemWrite, ALU_SRC, RegDst, Beq, Bne, JR, JMP, SLLV_in, SLLV, XOR_in, XOR, SH_in, SH, BLTZ_in, BLTZ
  Adder #(.width(16)) adder_4 (.a(counter_5_q), .b(counter_6_q), .out(\插入气泡数 ));  // open: cin, cout
  Multiplexer #(.select(1), .width(32), .disabled("Z"), .enable("false")) multiplexer_18 (
    .in0(ALU_out), .in1(MEM_readData), .out(multiplexer_18_out), .sel(MemToReg4));
  Adder #(.width(32)) adder_5 (.a(WB_PC), .b(32'h4), .out(adder_5_out));  // open: cin, cout
  and and_8 (and_8_out, Syscall4, ~MEM_WB_halt);  // AND_Gate
  Multiplexer #(.select(1), .width(32), .disabled("Z"), .enable("false")) multiplexer_19 (
    .in0(multiplexer_18_out), .in1(adder_5_out), .out(RDin), .sel(JAL4));
  Register #(.width(1), .trigger("rising"), .Select("low")) register_2 (
    .D(Syscall4), .en(and_8_out), .Q(halt), .clk(CLK), .clr(Go));
  or or_7 (IR1_t, IR1, IRA);
  Comparator #(.width(16), .mode("twosComplement")) comparator_4 (
    .a(16'h23b), .b(\总周期数 ), .eq(comparator_4_eq));  // open: gt, lt
  or or_8 (or_8_out, comparator_4_eq, comparator_5_eq);
  Comparator #(.width(16), .mode("twosComplement")) comparator_5 (
    .a(\总周期数 ), .b(16'h1), .eq(comparator_5_eq));  // open: gt, lt
  Comparator #(.width(16), .mode("twosComplement")) comparator_6 (
    .a(\总周期数 ), .b(16'h4), .eq(comparator_6_eq));  // open: gt, lt
  Comparator #(.width(16), .mode("twosComplement")) comparator_7 (
    .a(\总周期数 ), .b(16'h7), .eq(comparator_7_eq));  // open: gt, lt
  Pull_Resistor #(.pull(0)) pull_resistor_2 (.node(IRA));
  assign IRA = or_8_out ? ~CLK : 1'bz;  // Controlled_Inverter controlled_inverter_1
  Pull_Resistor #(.pull(0)) pull_resistor_3 (.node(IRB));
  assign IRB = comparator_6_eq ? ~CLK : 1'bz;  // Controlled_Inverter controlled_inverter_2
  Pull_Resistor #(.pull(0)) pull_resistor_4 (.node(IRC));
  assign IRC = comparator_7_eq ? ~CLK : 1'bz;  // Controlled_Inverter controlled_inverter_3
  or or_9 (IR2_t, IR2, IRB);
  or or_10 (IR3_t, IR3, IRC);
  \中断按键参考电路  \u_中断按键参考电路_1  (.\与中断屏蔽位与 (INT1), .\同步清零信号 (RST1), .in_1(CLK), .in_2(IR1_t), .out_5(W1));
  \中断按键参考电路  \u_中断按键参考电路_2  (.\与中断屏蔽位与 (INT2), .\同步清零信号 (RST2), .in_1(CLK), .in_2(IR2_t), .out_5(W2));
  \中断按键参考电路  \u_中断按键参考电路_3  (.\与中断屏蔽位与 (INT3), .\同步清零信号 (RST3), .in_1(CLK), .in_2(IR3_t), .out_5(W3));
  Priority_Encoder #(.select(2), .disabled("Z")) priority_encoder_1 (
    .in0(1'b0), .in1(INT1), .in2(INT2), .in3(INT3), .out(INTNUM), .gs(priority_encoder_1_gs), .en_in(1'b1));  // open: en_out
  Multiplexer #(.select(2), .width(32), .disabled("Z"), .enable("false")) multiplexer_20 (
    .in1(32'h30ac), .in2(32'h3150), .in3(32'h31f4), .out(\中断程序入口地址 ), .sel(INTNUM));  // open: in0
  Comparator #(.width(32), .mode("twosComplement")) comparator_8 (
    .a(EX_IR), .b(32'h42000018), .eq(ERET));  // open: gt, lt
  or or_11 (or_11_out, \中断 , ERET);
  not not_3 (not_3_out, register_3_q);
  Register #(.width(1), .trigger("rising"), .Select("low")) register_3 (
    .D(\中断 ), .en(or_11_out), .Q(register_3_q), .clk(CLK));  // open: clr
  Register #(.width(32), .trigger("rising"), .Select("low")) register_4 (
    .D(PC_4), .en(\中断 ), .Q(EPC), .clk(CLK));  // open: clr
  Register #(.width(2), .trigger("rising"), .Select("low")) register_5 (
    .D(INTNUM), .en(\中断 ), .Q(register_5_q), .clk(CLK));  // open: clr
  and and_9 (\中断 , not_3_out, priority_encoder_1_gs);
  Decoder #(.select(2), .tristate("false"), .disabled("Z"), .enable("false")) decoder_1 (
    .out1(decoder_1_out1), .out2(decoder_1_out2), .out3(decoder_1_out3), .sel(register_5_q));  // open: out0
  and and_10 (RST1, decoder_1_out1, ERET);
  and and_11 (RST2, decoder_1_out2, ERET);
  and and_12 (RST3, decoder_1_out3, ERET);

  // Other names for the same wires on the sheet: OP[5:0] = ID_IR[31:26]; ID_IR[5:0] = Func;
  //   JMPaddr[27:2] = {ID_IR[25:6], Func}; MEM_PC[31:0] = M_PC; MemWrite3 = MemWrite; R1[31:0] = GPR_rs;
  //   RegWrite4 = RegWrite

  // Notes on the sheet:
  //   中断源
  //   时空图监测，可删除
  //   中断等待指示
  //   数码管输出
  //   指令存储器
  //   控制位
  //   contents of rom_1 (hex, n*v repeats v):
  //   201d07d0 20100001 109fc0 139fc3 8021 2012000c 24160008 26100001 3210000f 20080008 20090001 139900
  //   2709825 132020 20020022 c 1094022 1500fff9 22100001 2018000f 2188024 108700 20080008 20090001 139902
  //   2709825 132021 20020022 c 1094022 1500fff9 108702 2c9b022 12c00001 8000c07 4020 1084027 84400
  //   3508ffff 82021 20020022 c 8000c01 afa20000 23bd0004 afa40000 23bd0004 afb00000 23bd0004 afb30000
  //   23bd0004 afb40000 23bd0004 afb50000 23bd0004 afb60000 23bd0004 20160001 20140003 20150001 168020
  //   108100 2149825 132020 20020022 c 1600fffa 295a022 1680fff7 23bdfffc 8fb60000 23bdfffc 8fb50000
  //   23bdfffc 8fb40000 23bdfffc 8fb30000 23bdfffc 8fb00000 23bdfffc 8fa40000 23bdfffc 8fa20000 42000018
  //   afa20000 23bd0004 afa40000 23bd0004 afb00000 23bd0004 afb30000 23bd0004 afb40000 23bd0004 afb50000
  //   23bd0004 afb60000 23bd0004 20160002 20140003 20150001 168020 108100 2149825 132020 20020022 c
  //   1600fffa 295a022 1680fff7 23bdfffc 8fb60000 23bdfffc 8fb50000 23bdfffc 8fb40000 23bdfffc 8fb30000
  //   23bdfffc 8fb00000 23bdfffc 8fa40000 23bdfffc 8fa20000 42000018 afa20000 23bd0004 afa40000 23bd0004
  //   afb00000 23bd0004 afb30000 23bd0004 afb40000 23bd0004 afb50000 23bd0004 afb60000 23bd0004 20160003
  //   20140003 20150001 168020 108100 2149825 132020 20020022 c 1600fffa 295a022 1680fff7 23bdfffc
  //   8fb60000 23bdfffc 8fb50000 23bdfffc 8fb40000 23bdfffc 8fb30000 23bdfffc 8fb00000 23bdfffc 8fa40000
  //   23bdfffc 8fa20000 42000018
  //   流水调试日志用
  //   暂停节拍，不能为0
  //   OP
  //   Func
  //   rs
  //   rt
  //   指令字
  //   rd
  //   戳工具置1进入计数暂停模式，ctrl+k时钟自动运行到对应节拍暂停
  //   ctrl+k关闭时钟连续运行，将控制位置零，进入单步调试模式调试
  //   可计数暂停的时钟源
  //   为方便自动评测，需要输出流水线各段保存的PC值，注意是PC不是PC+4，另外ID段寄存器写入信息，Mem段内存写入信息也要输出
  //   JMP
  //   JR
  //   OP
  //   Func
  //   Beq
  //   Bne
  //   MemToReg
  //   MemWrite
  //   AluOP
  //   AluSrcB
  //   RegWrite
  //   JAL
  //   RegDst
  //   Syscall
  //   单级中断测试信号模拟器
endmodule

module \封装正确性测试  (
);

  wire IR1, IR2, IR3, MemW, RegW;
  wire [31:0] EX_PC, ID_PC, IF_PC, IR, LED, MDin, MDinr, MEM_PC, PC, RDin, RDinr, WB_PC;

  \单周期MIPS  \u_单周期mips_1  (
    .RegWrite(RegW), .MemWrite(MemW), .PC(PC), .IR(IR), .RDin(RDin), .MDin(MDin), .LedData(LED));  // open: IR1, IR2, IR3
  \气泡流水线  \u_气泡流水线_1  (
    .RegWrite(RegW), .MemWrite(MemW), .IF_PC(IF_PC), .ID_PC(ID_PC), .EX_PC(EX_PC), .M_PC(MEM_PC),
    .WB_PC(WB_PC), .RDin(RDinr), .MDin(MDinr), .LedData(LED));
  \单周期MIPS_单级中断  \u_单周期mips_单级中断_1  (
    .IR1(IR1), .IR2(IR2), .IR3(IR3), .RegWrite(RegW), .MemWrite(MemW), .PC(PC), .IR(IR), .RDin(RDin),
    .MDin(MDin), .LedData(LED));
  \理想流水线  \u_理想流水线_1  (
    .RegWrite(RegW), .MemWrite(MemW), .IF_PC(IF_PC), .ID_PC(ID_PC), .EX_PC(EX_PC), .M_PC(MEM_PC),
    .WB_PC(WB_PC), .RDin(RDinr), .MDin(MDinr), .LedData(LED));
  \重定向流水线  \u_重定向流水线_1  (
    .RegWrite(RegW), .MemWrite(MemW), .IF_PC(IF_PC), .ID_PC(ID_PC), .EX_PC(EX_PC), .M_PC(MEM_PC),
    .WB_PC(WB_PC), .RDin(RDinr), .MDin(MDinr), .LedData(LED));
  \单周期MIPS_多级中断  \u_单周期mips_多级中断_1  (
    .IR1(IR1), .IR2(IR2), .IR3(IR3), .RegWrite(RegW), .MemWrite(MemW), .PC(PC), .IR(IR), .RDin(RDin),
    .MDin(MDin), .LedData(LED));

  // Notes on the sheet:
  //   单周期封装测试
  //   气泡流水封装测试
  //   单周期+单级中断封装测试
  //   请检查上面封装有无位宽不匹配，引脚标签是否和连接的标签相对应，否则无法在educoder平台上正确测试
  //   理想流水封装测试
  //   重定向流水封装测试
  //   单周期+多级中断封装测试
endmodule

module \重定向检测  (
  input  MEM_MemToReg,
  input  [5:0] OP,
  input  [4:0] ID_ReadReg1,
  input  [5:0] FUNC,
  input  [4:0] EX_WriteReg,
  input  EX_RegWrite,
  input  EX_MemToReg,
  input  [4:0] MEM_WriteReg,
  input  MEM_RegWrite,
  input  [4:0] ID_ReadReg2,
  output [1:0] FORWARD1,
  output [1:0] FORWARD2,
  output \冲突 ,
  output Load_Use
);

  wire comparator_1_eq, comparator_2_eq, comparator_3_eq, comparator_4_eq, comparator_5_eq, comparator_6_eq,
       EX_R1, EX_R2, MEM_R1, MEM_R2, not_1_out, not_2_out, or_4_out, R1, R1_USED, R2, R2_USED;
  wire [1:0] multiplexer_1_out, multiplexer_2_out, multiplexer_3_out, multiplexer_4_out;

  Multiplexer #(.select(1), .width(2), .disabled("Z"), .enable("false")) multiplexer_1 (
    .in0(2'b01), .in1(2'b10), .out(multiplexer_1_out), .sel(MEM_MemToReg));
  Multiplexer #(.select(1), .width(2), .disabled("Z"), .enable("false")) multiplexer_2 (
    .in0(2'b01), .in1(2'b10), .out(multiplexer_2_out), .sel(MEM_MemToReg));
  Multiplexer #(.select(1), .width(2), .disabled("Z"), .enable("false")) multiplexer_3 (
    .in0(multiplexer_1_out), .in1(2'b11), .out(multiplexer_3_out), .sel(EX_R1));
  Multiplexer #(.select(1), .width(2), .disabled("Z"), .enable("false")) multiplexer_4 (
    .in0(multiplexer_2_out), .in1(2'b11), .out(multiplexer_4_out), .sel(EX_R2));
  Multiplexer #(.select(1), .width(2), .disabled("Z"), .enable("false")) multiplexer_5 (
    .in0(2'b00), .in1(multiplexer_3_out), .out(FORWARD1), .sel(R1));
  Multiplexer #(.select(1), .width(2), .disabled("Z"), .enable("false")) multiplexer_6 (
    .in0(2'b00), .in1(multiplexer_4_out), .out(FORWARD2), .sel(R2));
  Comparator #(.width(5), .mode("twosComplement")) comparator_1 (
    .a({5{1'b0}}), .b(ID_ReadReg1), .eq(comparator_1_eq));  // open: gt, lt
  Comparator #(.width(5), .mode("twosComplement")) comparator_2 (
    .a(ID_ReadReg1), .b(EX_WriteReg), .eq(comparator_2_eq));  // open: gt, lt
  Comparator #(.width(5), .mode("twosComplement")) comparator_3 (
    .a(ID_ReadReg1), .b(MEM_WriteReg), .eq(comparator_3_eq));  // open: gt, lt
  Comparator #(.width(5), .mode("twosComplement")) comparator_4 (
    .a({5{1'b0}}), .b(ID_ReadReg2), .eq(comparator_4_eq));  // open: gt, lt
  Comparator #(.width(5), .mode("twosComplement")) comparator_5 (
    .a(ID_ReadReg2), .b(EX_WriteReg), .eq(comparator_5_eq));  // open: gt, lt
  Comparator #(.width(5), .mode("twosComplement")) comparator_6 (
    .a(ID_ReadReg2), .b(MEM_WriteReg), .eq(comparator_6_eq));  // open: gt, lt
  not not_1 (not_1_out, comparator_1_eq);
  not not_2 (not_2_out, comparator_4_eq);
  and and_1 (MEM_R1, R1_USED, not_1_out, comparator_3_eq, MEM_RegWrite);
  and and_2 (EX_R2, R2_USED, not_2_out, comparator_5_eq, EX_RegWrite);
  and and_3 (MEM_R2, R2_USED, not_2_out, comparator_6_eq, MEM_RegWrite);
  and and_4 (EX_R1, R1_USED, not_1_out, comparator_2_eq, EX_RegWrite);
  or or_1 (R1, EX_R1, MEM_R1);
  or or_2 (R2, EX_R2, MEM_R2);
  or or_3 (\冲突 , R1, R2);
  and and_5 (Load_Use, EX_MemToReg, or_4_out);
  or or_4 (or_4_out, EX_R1, EX_R2);
  \源寄存器使用情况  \u_源寄存器使用情况_1  (
    .OP0(OP[0]), .OP1(OP[1]), .OP2(OP[2]), .OP3(OP[3]), .OP4(OP[4]), .OP5(OP[5]), .F0(FUNC[0]), .F1(FUNC[1]),
    .F2(FUNC[2]), .F3(FUNC[3]), .F4(FUNC[4]), .F5(FUNC[5]), .R1_Used(R1_USED), .R2_Used(R2_USED));
endmodule

module IF_ID (
  input  [31:0] IR_in,
  input  [31:0] PC_in,
  input  clk,
  input  \使能 ,
  input  \同步清零 ,
  output [31:0] IR_out,
  output [31:0] PC_out
);

  wire [31:0] multiplexer_1_out, multiplexer_2_out;

  Multiplexer #(.select(1), .width(32), .disabled("Z"), .enable("false")) multiplexer_1 (
    .in0(IR_in), .in1({32{1'b0}}), .out(multiplexer_1_out), .sel(\同步清零 ));
  Multiplexer #(.select(1), .width(32), .disabled("Z"), .enable("false")) multiplexer_2 (
    .in0(PC_in), .in1({32{1'b0}}), .out(multiplexer_2_out), .sel(\同步清零 ));
  Register #(.width(32), .trigger("rising"), .Select("low")) register_1 (
    .D(multiplexer_1_out), .en(\使能 ), .Q(IR_out), .clk(clk));  // open: clr
  Register #(.width(32), .trigger("rising"), .Select("low")) register_2 (
    .D(multiplexer_2_out), .en(\使能 ), .Q(PC_out), .clk(clk));  // open: clr
endmodule

module ID_EX (
  input  [1:0] forward1,
  input  [1:0] forward2,
  input  [31:0] JMPaddr,
  input  SLLV_in,
  input  XOR_in,
  input  SH_in,
  input  [31:0] IR_in,
  input  BLTZ_in,
  input  [3:0] ALUOP_in,
  input  [31:0] PC_in,
  input  MemToReg_in,
  input  MemWrite_in,
  input  [31:0] R1,
  input  ALU_SRC_in,
  input  RegWrite_in,
  input  [31:0] R2,
  input  Syscall_in,
  input  RegDst_in,
  input  [4:0] IMM,
  input  Beq_in,
  input  [4:0] WriteReg,
  input  Bne_in,
  input  [31:0] MUX_in,
  input  JR_in,
  input  JMP_in,
  input  JAL_in,
  input  [31:0] \有符号扩展 ,
  input  \使能 ,
  input  clk,
  input  \同步清零 ,
  output [1:0] forward1_out,
  output [1:0] forward2_out,
  output [31:0] JMPaddr_out,
  output SLLV,
  output XOR,
  output SH,
  output [31:0] IR_out,
  output BLTZ,
  output [3:0] ALUOP,
  output [31:0] PC_out,
  output MemToReg,
  output MemWrite,
  output [31:0] A,
  output ALU_SRC,
  output RegWrite,
  output [31:0] B,
  output SysCALL,
  output RegDst,
  output [4:0] imm_out,
  output Beq,
  output [4:0] WriteReg_out,
  output Bne,
  output [31:0] MUX_out,
  output JR,
  output JMP,
  output JAL,
  output [31:0] \有符号扩展_out 
);

  wire multiplexer_3_out, multiplexer_4_out, multiplexer_5_out, multiplexer_6_out, multiplexer_8_out,
       multiplexer_9_out, multiplexer_10_out, multiplexer_11_out, multiplexer_12_out, multiplexer_13_out,
       multiplexer_14_out, multiplexer_15_out, multiplexer_16_out, multiplexer_17_out, multiplexer_18_out;
  wire [1:0] multiplexer_1_out, multiplexer_2_out;
  wire [3:0] multiplexer_7_out;
  wire [4:0] multiplexer_24_out, multiplexer_25_out;
  wire [31:0] multiplexer_19_out, multiplexer_20_out, multiplexer_21_out, multiplexer_22_out,
       multiplexer_23_out, multiplexer_26_out, multiplexer_27_out;

  Multiplexer #(.select(1), .width(2), .disabled("Z"), .enable("false")) multiplexer_1 (
    .in0(forward1), .in1(2'b00), .out(multiplexer_1_out), .sel(\同步清零 ));
  Multiplexer #(.select(1), .width(2), .disabled("Z"), .enable("false")) multiplexer_2 (
    .in0(forward2), .in1(2'b00), .out(multiplexer_2_out), .sel(\同步清零 ));
  Multiplexer #(.select(1), .width(1), .disabled("Z"), .enable("false")) multiplexer_3 (
    .in0(SLLV_in), .in1(1'b0), .out(multiplexer_3_out), .sel(\同步清零 ));
  Multiplexer #(.select(1), .width(1), .disabled("Z"), .enable("false")) multiplexer_4 (
    .in0(XOR_in), .in1(1'b0), .out(multiplexer_4_out), .sel(\同步清零 ));
  Multiplexer #(.select(1), .width(1), .disabled("Z"), .enable("false")) multiplexer_5 (
    .in0(SH_in), .in1(1'b0), .out(multiplexer_5_out), .sel(\同步清零 ));
  Multiplexer #(.select(1), .width(1), .disabled("Z"), .enable("false")) multiplexer_6 (
    .in0(BLTZ_in), .in1(1'b0), .out(multiplexer_6_out), .sel(\同步清零 ));
  Multiplexer #(.select(1), .width(4), .disabled("Z"), .enable("false")) multiplexer_7 (
    .in0(ALUOP_in), .in1(4'b0000), .out(multiplexer_7_out), .sel(\同步清零 ));
  Multiplexer #(.select(1), .width(1), .disabled("Z"), .enable("false")) multiplexer_8 (
    .in0(MemToReg_in), .in1(1'b0), .out(multiplexer_8_out), .sel(\同步清零 ));
  Multiplexer #(.select(1), .width(1), .disabled("Z"), .enable("false")) multiplexer_9 (
    .in0(MemWrite_in), .in1(1'b0), .out(multiplexer_9_out), .sel(\同步清零 ));
  Multiplexer #(.select(1), .width(1), .disabled("Z"), .enable("false")) multiplexer_10 (
    .in0(ALU_SRC_in), .in1(1'b0), .out(multiplexer_10_out), .sel(\同步清零 ));
  Multiplexer #(.select(1), .width(1), .disabled("Z"), .enable("false")) multiplexer_11 (
    .in0(RegWrite_in), .in1(1'b0), .out(multiplexer_11_out), .sel(\同步清零 ));
  Multiplexer #(.select(1), .width(1), .disabled("Z"), .enable("false")) multiplexer_12 (
    .in0(Syscall_in), .in1(1'b0), .out(multiplexer_12_out), .sel(\同步清零 ));
  Multiplexer #(.select(1), .width(1), .disabled("Z"), .enable("false")) multiplexer_13 (
    .in0(RegDst_in), .in1(1'b0), .out(multiplexer_13_out), .sel(\同步清零 ));
  Multiplexer #(.select(1), .width(1), .disabled("Z"), .enable("false")) multiplexer_14 (
    .in0(Beq_in), .in1(1'b0), .out(multiplexer_14_out), .sel(\同步清零 ));
  Multiplexer #(.select(1), .width(1), .disabled("Z"), .enable("false")) multiplexer_15 (
    .in0(Bne_in), .in1(1'b0), .out(multiplexer_15_out), .sel(\同步清零 ));
  Multiplexer #(.select(1), .width(1), .disabled("Z"), .enable("false")) multiplexer_16 (
    .in0(JR_in), .in1(1'b0), .out(multiplexer_16_out), .sel(\同步清零 ));
  Multiplexer #(.select(1), .width(1), .disabled("Z"), .enable("false")) multiplexer_17 (
    .in0(JMP_in), .in1(1'b0), .out(multiplexer_17_out), .sel(\同步清零 ));
  Multiplexer #(.select(1), .width(1), .disabled("Z"), .enable("false")) multiplexer_18 (
    .in0(JAL_in), .in1(1'b0), .out(multiplexer_18_out), .sel(\同步清零 ));
  Register #(.width(2), .trigger("rising"), .Select("low")) register_1 (
    .D(multiplexer_1_out), .en(\使能 ), .Q(forward1_out), .clk(clk));  // open: clr
  Register #(.width(2), .trigger("rising"), .Select("low")) register_2 (
    .D(multiplexer_2_out), .en(\使能 ), .Q(forward2_out), .clk(clk));  // open: clr
  Register #(.width(1), .trigger("rising"), .Select("low")) register_3 (
    .D(multiplexer_3_out), .en(\使能 ), .Q(SLLV), .clk(clk));  // open: clr
  Register #(.width(1), .trigger("rising"), .Select("low")) register_4 (
    .D(multiplexer_4_out), .en(\使能 ), .Q(XOR), .clk(clk));  // open: clr
  Register #(.width(1), .trigger("rising"), .Select("low")) register_5 (
    .D(multiplexer_5_out), .en(\使能 ), .Q(SH), .clk(clk));  // open: clr
  Register #(.width(1), .trigger("rising"), .Select("low")) register_6 (
    .D(multiplexer_6_out), .en(\使能 ), .Q(BLTZ), .clk(clk));  // open: clr
  Register #(.width(4), .trigger("rising"), .Select("low")) register_7 (
    .D(multiplexer_7_out), .en(\使能 ), .Q(ALUOP), .clk(clk));  // open: clr
  Register #(.width(1), .trigger("rising"), .Select("low")) register_8 (
    .D(multiplexer_8_out), .en(\使能 ), .Q(MemToReg), .clk(clk));  // open: clr
  Register #(.width(1), .trigger("rising"), .Select("low")) register_9 (
    .D(multiplexer_9_out), .en(\使能 ), .Q(MemWrite), .clk(clk));  // open: clr
  Register #(.width(1), .trigger("rising"), .Select("low")) register_10 (
    .D(multiplexer_10_out), .en(\使能 ), .Q(ALU_SRC), .clk(clk));  // open: clr
  Register #(.width(1), .trigger("rising"), .Select("low")) register_11 (
    .D(multiplexer_11_out), .en(\使能 ), .Q(RegWrite), .clk(clk));  // open: clr
  Register #(.width(1), .trigger("rising"), .Select("low")) register_12 (
    .D(multiplexer_12_out), .en(\使能 ), .Q(SysCALL), .clk(clk));  // open: clr
  Register #(.width(1), .trigger("rising"), .Select("low")) register_13 (
    .D(multiplexer_13_out), .en(\使能 ), .Q(RegDst), .clk(clk));  // open: clr
  Register #(.width(1), .trigger("rising"), .Select("low")) register_14 (
    .D(multiplexer_14_out), .en(\使能 ), .Q(Beq), .clk(clk));  // open: clr
  Register #(.width(1), .trigger("rising"), .Select("low")) register_15 (
    .D(multiplexer_15_out), .en(\使能 ), .Q(Bne), .clk(clk));  // open: clr
  Register #(.width(1), .trigger("rising"), .Select("low")) register_16 (
    .D(multiplexer_16_out), .en(\使能 ), .Q(JR), .clk(clk));  // open: clr
  Register #(.width(1), .trigger("rising"), .Select("low")) register_17 (
    .D(multiplexer_17_out), .en(\使能 ), .Q(JMP), .clk(clk));  // open: clr
  Register #(.width(1), .trigger("rising"), .Select("low")) register_18 (
    .D(multiplexer_18_out), .en(\使能 ), .Q(JAL), .clk(clk));  // open: clr
  Multiplexer #(.select(1), .width(32), .disabled("Z"), .enable("false")) multiplexer_19 (
    .in0(JMPaddr), .in1({32{1'b0}}), .out(multiplexer_19_out), .sel(\同步清零 ));
  Multiplexer #(.select(1), .width(32), .disabled("Z"), .enable("false")) multiplexer_20 (
    .in0(IR_in), .in1({32{1'b0}}), .out(multiplexer_20_out), .sel(\同步清零 ));
  Multiplexer #(.select(1), .width(32), .disabled("Z"), .enable("false")) multiplexer_21 (
    .in0(PC_in), .in1({32{1'b0}}), .out(multiplexer_21_out), .sel(\同步清零 ));
  Multiplexer #(.select(1), .width(32), .disabled("Z"), .enable("false")) multiplexer_22 (
    .in0(R1), .in1({32{1'b0}}), .out(multiplexer_22_out), .sel(\同步清零 ));
  Multiplexer #(.select(1), .width(32), .disabled("Z"), .enable("false")) multiplexer_23 (
    .in0(R2), .in1({32{1'b0}}), .out(multiplexer_23_out), .sel(\同步清零 ));
  Multiplexer #(.select(1), .width(5), .disabled("Z"), .enable("false")) multiplexer_24 (
    .in0(IMM), .in1({5{1'b0}}), .out(multiplexer_24_out), .sel(\同步清零 ));
  Multiplexer #(.select(1), .width(5), .disabled("Z"), .enable("false")) multiplexer_25 (
    .in0(WriteReg), .in1({5{1'b0}}), .out(multiplexer_25_out), .sel(\同步清零 ));
  Multiplexer #(.select(1), .width(32), .disabled("Z"), .enable("false")) multiplexer_26 (
    .in0(MUX_in), .in1({32{1'b0}}), .out(multiplexer_26_out), .sel(\同步清零 ));
  Multiplexer #(.select(1), .width(32), .disabled("Z"), .enable("false")) multiplexer_27 (
    .in0(\有符号扩展 ), .in1({32{1'b0}}), .out(multiplexer_27_out), .sel(\同步清零 ));
  Register #(.width(32), .trigger("rising"), .Select("low")) register_19 (
    .D(multiplexer_19_out), .en(\使能 ), .Q(JMPaddr_out), .clk(clk));  // open: clr
  Register #(.width(32), .trigger("rising"), .Select("low")) register_20 (
    .D(multiplexer_20_out), .en(\使能 ), .Q(IR_out), .clk(clk));  // open: clr
  Register #(.width(32), .trigger("rising"), .Select("low")) register_21 (
    .D(multiplexer_21_out), .en(\使能 ), .Q(PC_out), .clk(clk));  // open: clr
  Register #(.width(32), .trigger("rising"), .Select("low")) register_22 (
    .D(multiplexer_22_out), .en(\使能 ), .Q(A), .clk(clk));  // open: clr
  Register #(.width(32), .trigger("rising"), .Select("low")) register_23 (
    .D(multiplexer_23_out), .en(\使能 ), .Q(B), .clk(clk));  // open: clr
  Register #(.width(5), .trigger("rising"), .Select("low")) register_24 (
    .D(multiplexer_24_out), .en(\使能 ), .Q(imm_out), .clk(clk));  // open: clr
  Register #(.width(5), .trigger("rising"), .Select("low")) register_25 (
    .D(multiplexer_25_out), .en(\使能 ), .Q(WriteReg_out), .clk(clk));  // open: clr
  Register #(.width(32), .trigger("rising"), .Select("low")) register_26 (
    .D(multiplexer_26_out), .en(\使能 ), .Q(MUX_out), .clk(clk));  // open: clr
  Register #(.width(32), .trigger("rising"), .Select("low")) register_27 (
    .D(multiplexer_27_out), .en(\使能 ), .Q(\有符号扩展_out ), .clk(clk));  // open: clr
endmodule

module EX_MEM (
  input  SLLV_in,
  input  XOR_in,
  input  SH_in,
  input  BLTZ_in,
  input  [3:0] ALUOP_in,
  input  MemToReg_in,
  input  [31:0] IR_in,
  input  MemWrite_in,
  input  ALU_SRC_in,
  input  [31:0] PC_in,
  input  RegWrite_in,
  input  halt,
  input  Syscall_in,
  input  RegDst_in,
  input  LEDIN_IN,
  input  Beq_in,
  input  [31:0] B,
  input  Bne_in,
  input  [31:0] ALU_in,
  input  JR_in,
  input  JMP_in,
  input  [4:0] WriteReg,
  input  JAL_in,
  input  \使能 ,
  input  clk,
  input  \同步清零 ,
  output SLLV,
  output XOR,
  output SH,
  output BLTZ,
  output [3:0] ALUOP,
  output MemToReg,
  output [31:0] IR_out,
  output MemWrite,
  output ALU_SRC,
  output [31:0] PC_out,
  output RegWrite,
  output halt_2,
  output SysCALL,
  output RegDst,
  output ledin,
  output Beq,
  output [31:0] B_2,
  output Bne,
  output [31:0] ALU_out,
  output JR,
  output JMP,
  output [4:0] WriteReg_out,
  output JAL
);

  wire multiplexer_1_out, multiplexer_2_out, multiplexer_3_out, multiplexer_4_out, multiplexer_6_out,
       multiplexer_7_out, multiplexer_8_out, multiplexer_9_out, multiplexer_10_out, multiplexer_11_out,
       multiplexer_12_out, multiplexer_13_out, multiplexer_14_out, multiplexer_15_out, multiplexer_16_out,
       multiplexer_19_out, multiplexer_20_out;
  wire [3:0] multiplexer_5_out;
  wire [4:0] multiplexer_23_out;
  wire [31:0] multiplexer_17_out, multiplexer_18_out, multiplexer_21_out, multiplexer_22_out;

  Multiplexer #(.select(1), .width(1), .disabled("Z"), .enable("false")) multiplexer_1 (
    .in0(SLLV_in), .in1(1'b0), .out(multiplexer_1_out), .sel(\同步清零 ));
  Multiplexer #(.select(1), .width(1), .disabled("Z"), .enable("false")) multiplexer_2 (
    .in0(XOR_in), .in1(1'b0), .out(multiplexer_2_out), .sel(\同步清零 ));
  Multiplexer #(.select(1), .width(1), .disabled("Z"), .enable("false")) multiplexer_3 (
    .in0(SH_in), .in1(1'b0), .out(multiplexer_3_out), .sel(\同步清零 ));
  Multiplexer #(.select(1), .width(1), .disabled("Z"), .enable("false")) multiplexer_4 (
    .in0(BLTZ_in), .in1(1'b0), .out(multiplexer_4_out), .sel(\同步清零 ));
  Multiplexer #(.select(1), .width(4), .disabled("Z"), .enable("false")) multiplexer_5 (
    .in0(ALUOP_in), .in1(4'b0000), .out(multiplexer_5_out), .sel(\同步清零 ));
  Multiplexer #(.select(1), .width(1), .disabled("Z"), .enable("false")) multiplexer_6 (
    .in0(MemToReg_in), .in1(1'b0), .out(multiplexer_6_out), .sel(\同步清零 ));
  Multiplexer #(.select(1), .width(1), .disabled("Z"), .enable("false")) multiplexer_7 (
    .in0(MemWrite_in), .in1(1'b0), .out(multiplexer_7_out), .sel(\同步清零 ));
  Multiplexer #(.select(1), .width(1), .disabled("Z"), .enable("false")) multiplexer_8 (
    .in0(ALU_SRC_in), .in1(1'b0), .out(multiplexer_8_out), .sel(\同步清零 ));
  Multiplexer #(.select(1), .width(1), .disabled("Z"), .enable("false")) multiplexer_9 (
    .in0(RegWrite_in), .in1(1'b0), .out(multiplexer_9_out), .sel(\同步清零 ));
  Multiplexer #(.select(1), .width(1), .disabled("Z"), .enable("false")) multiplexer_10 (
    .in0(Syscall_in), .in1(1'b0), .out(multiplexer_10_out), .sel(\同步清零 ));
  Multiplexer #(.select(1), .width(1), .disabled("Z"), .enable("false")) multiplexer_11 (
    .in0(RegDst_in), .in1(1'b0), .out(multiplexer_11_out), .sel(\同步清零 ));
  Multiplexer #(.select(1), .width(1), .disabled("Z"), .enable("false")) multiplexer_12 (
    .in0(Beq_in), .in1(1'b0), .out(multiplexer_12_out), .sel(\同步清零 ));
  Multiplexer #(.select(1), .width(1), .disabled("Z"), .enable("false")) multiplexer_13 (
    .in0(Bne_in), .in1(1'b0), .out(multiplexer_13_out), .sel(\同步清零 ));
  Multiplexer #(.select(1), .width(1), .disabled("Z"), .enable("false")) multiplexer_14 (
    .in0(JR_in), .in1(1'b0), .out(multiplexer_14_out), .sel(\同步清零 ));
  Multiplexer #(.select(1), .width(1), .disabled("Z"), .enable("false")) multiplexer_15 (
    .in0(JMP_in), .in1(1'b0), .out(multiplexer_15_out), .sel(\同步清零 ));
  Multiplexer #(.select(1), .width(1), .disabled("Z"), .enable("false")) multiplexer_16 (
    .in0(JAL_in), .in1(1'b0), .out(multiplexer_16_out), .sel(\同步清零 ));
  Register #(.width(1), .trigger("rising"), .Select("low")) register_1 (
    .D(multiplexer_1_out), .en(\使能 ), .Q(SLLV), .clk(clk));  // open: clr
  Register #(.width(1), .trigger("rising"), .Select("low")) register_2 (
    .D(multiplexer_2_out), .en(\使能 ), .Q(XOR), .clk(clk));  // open: clr
  Register #(.width(1), .trigger("rising"), .Select("low")) register_3 (
    .D(multiplexer_3_out), .en(\使能 ), .Q(SH), .clk(clk));  // open: clr
  Register #(.width(1), .trigger("rising"), .Select("low")) register_4 (
    .D(multiplexer_4_out), .en(\使能 ), .Q(BLTZ), .clk(clk));  // open: clr
  Register #(.width(4), .trigger("rising"), .Select("low")) register_5 (
    .D(multiplexer_5_out), .en(\使能 ), .Q(ALUOP), .clk(clk));  // open: clr
  Register #(.width(1), .trigger("rising"), .Select("low")) register_6 (
    .D(multiplexer_6_out), .en(\使能 ), .Q(MemToReg), .clk(clk));  // open: clr
  Register #(.width(1), .trigger("rising"), .Select("low")) register_7 (
    .D(multiplexer_7_out), .en(\使能 ), .Q(MemWrite), .clk(clk));  // open: clr
  Register #(.width(1), .trigger("rising"), .Select("low")) register_8 (
    .D(multiplexer_8_out), .en(\使能 ), .Q(ALU_SRC), .clk(clk));  // open: clr
  Register #(.width(1), .trigger("rising"), .Select("low")) register_9 (
    .D(multiplexer_9_out), .en(\使能 ), .Q(RegWrite), .clk(clk));  // open: clr
  Register #(.width(1), .trigger("rising"), .Select("low")) register_10 (
    .D(multiplexer_10_out), .en(\使能 ), .Q(SysCALL), .clk(clk));  // open: clr
  Register #(.width(1), .trigger("rising"), .Select("low")) register_11 (
    .D(multiplexer_11_out), .en(\使能 ), .Q(RegDst), .clk(clk));  // open: clr
  Register #(.width(1), .trigger("rising"), .Select("low")) register_12 (
    .D(multiplexer_12_out), .en(\使能 ), .Q(Beq), .clk(clk));  // open: clr
  Register #(.width(1), .trigger("rising"), .Select("low")) register_13 (
    .D(multiplexer_13_out), .en(\使能 ), .Q(Bne), .clk(clk));  // open: clr
  Register #(.width(1), .trigger("rising"), .Select("low")) register_14 (
    .D(multiplexer_14_out), .en(\使能 ), .Q(JR), .clk(clk));  // open: clr
  Register #(.width(1), .trigger("rising"), .Select("low")) register_15 (
    .D(multiplexer_15_out), .en(\使能 ), .Q(JMP), .clk(clk));  // open: clr
  Register #(.width(1), .trigger("rising"), .Select("low")) register_16 (
    .D(multiplexer_16_out), .en(\使能 ), .Q(JAL), .clk(clk));  // open: clr
  Multiplexer #(.select(1), .width(32), .disabled("Z"), .enable("false")) multiplexer_17 (
    .in0(IR_in), .in1({32{1'b0}}), .out(multiplexer_17_out), .sel(\同步清零 ));
  Multiplexer #(.select(1), .width(32), .disabled("Z"), .enable("false")) multiplexer_18 (
    .in0(PC_in), .in1({32{1'b0}}), .out(multiplexer_18_out), .sel(\同步清零 ));
  Multiplexer #(.select(1), .width(1), .disabled("Z"), .enable("false")) multiplexer_19 (
    .in0(halt), .in1(1'b0), .out(multiplexer_19_out), .sel(\同步清零 ));
  Multiplexer #(.select(1), .width(1), .disabled("Z"), .enable("false")) multiplexer_20 (
    .in0(LEDIN_IN), .in1(1'b0), .out(multiplexer_20_out), .sel(\同步清零 ));
  Multiplexer #(.select(1), .width(32), .disabled("Z"), .enable("false")) multiplexer_21 (
    .in0(B), .in1({32{1'b0}}), .out(multiplexer_21_out), .sel(\同步清零 ));
  Multiplexer #(.select(1), .width(32), .disabled("Z"), .enable("false")) multiplexer_22 (
    .in0(ALU_in), .in1({32{1'b0}}), .out(multiplexer_22_out), .sel(\同步清零 ));
  Multiplexer #(.select(1), .width(5), .disabled("Z"), .enable("false")) multiplexer_23 (
    .in0(WriteReg), .in1({5{1'b0}}), .out(multiplexer_23_out), .sel(\同步清零 ));
  Register #(.width(32), .trigger("rising"), .Select("low")) register_17 (
    .D(multiplexer_17_out), .en(\使能 ), .Q(IR_out), .clk(clk));  // open: clr
  Register #(.width(32), .trigger("rising"), .Select("low")) register_18 (
    .D(multiplexer_18_out), .en(\使能 ), .Q(PC_out), .clk(clk));  // open: clr
  Register #(.width(1), .trigger("rising"), .Select("low")) register_19 (
    .D(multiplexer_19_out), .en(\使能 ), .Q(halt_2), .clk(clk));  // open: clr
  Register #(.width(1), .trigger("rising"), .Select("low")) register_20 (
    .D(multiplexer_20_out), .en(\使能 ), .Q(ledin), .clk(clk));  // open: clr
  Register #(.width(32), .trigger("rising"), .Select("low")) register_21 (
    .D(multiplexer_21_out), .en(\使能 ), .Q(B_2), .clk(clk));  // open: clr
  Register #(.width(32), .trigger("rising"), .Select("low")) register_22 (
    .D(multiplexer_22_out), .en(\使能 ), .Q(ALU_out), .clk(clk));  // open: clr
  Register #(.width(5), .trigger("rising"), .Select("low")) register_23 (
    .D(multiplexer_23_out), .en(\使能 ), .Q(WriteReg_out), .clk(clk));  // open: clr
endmodule

module EX_MEM_ideal (
  input  SLLV_in,
  input  XOR_in,
  input  SH_in,
  input  BLTZ_in,
  input  [3:0] ALUOP_in,
  input  MemToReg_in,
  input  [31:0] IR_in,
  input  MemWrite_in,
  input  ALU_SRC_in,
  input  [31:0] PC_in,
  input  RegWrite_in,
  input  Syscall_in,
  input  [31:0] A_in,
  input  RegDst_in,
  input  LEDIN_IN,
  input  Beq_in,
  input  [31:0] B,
  input  Bne_in,
  input  [31:0] ALU_in,
  input  JR_in,
  input  JMP_in,
  input  [4:0] WriteReg,
  input  JAL_in,
  input  \使能 ,
  input  clk,
  input  \同步清零 ,
  output SLLV,
  output XOR,
  output SH,
  output BLTZ,
  output [3:0] ALUOP,
  output MemToReg,
  output [31:0] IR_out,
  output MemWrite,
  output ALU_SRC,
  output [31:0] PC_out,
  output RegWrite,
  output [31:0] A,
  output SysCALL,
  output RegDst,
  output ledin,
  output Beq,
  output [31:0] B_2,
  output Bne,
  output [31:0] ALU_out,
  output JR,
  output JMP,
  output [4:0] WriteReg_out,
  output JAL
);

  wire multiplexer_1_out, multiplexer_2_out, multiplexer_3_out, multiplexer_4_out, multiplexer_6_out,
       multiplexer_7_out, multiplexer_8_out, multiplexer_9_out, multiplexer_10_out, multiplexer_11_out,
       multiplexer_12_out, multiplexer_13_out, multiplexer_14_out, multiplexer_15_out, multiplexer_16_out,
       multiplexer_20_out;
  wire [3:0] multiplexer_5_out;
  wire [4:0] multiplexer_23_out;
  wire [31:0] multiplexer_17_out, multiplexer_18_out, multiplexer_19_out, multiplexer_21_out,
       multiplexer_22_out;

  Multiplexer #(.select(1), .width(1), .disabled("Z"), .enable("false")) multiplexer_1 (
    .in0(SLLV_in), .in1(1'b0), .out(multiplexer_1_out), .sel(\同步清零 ));
  Multiplexer #(.select(1), .width(1), .disabled("Z"), .enable("false")) multiplexer_2 (
    .in0(XOR_in), .in1(1'b0), .out(multiplexer_2_out), .sel(\同步清零 ));
  Multiplexer #(.select(1), .width(1), .disabled("Z"), .enable("false")) multiplexer_3 (
    .in0(SH_in), .in1(1'b0), .out(multiplexer_3_out), .sel(\同步清零 ));
  Multiplexer #(.select(1), .width(1), .disabled("Z"), .enable("false")) multiplexer_4 (
    .in0(BLTZ_in), .in1(1'b0), .out(multiplexer_4_out), .sel(\同步清零 ));
  Multiplexer #(.select(1), .width(4), .disabled("Z"), .enable("false")) multiplexer_5 (
    .in0(ALUOP_in), .in1(4'b0000), .out(multiplexer_5_out), .sel(\同步清零 ));
  Multiplexer #(.select(1), .width(1), .disabled("Z"), .enable("false")) multiplexer_6 (
    .in0(MemToReg_in), .in1(1'b0), .out(multiplexer_6_out), .sel(\同步清零 ));
  Multiplexer #(.select(1), .width(1), .disabled("Z"), .enable("false")) multiplexer_7 (
    .in0(MemWrite_in), .in1(1'b0), .out(multiplexer_7_out), .sel(\同步清零 ));
  Multiplexer #(.select(1), .width(1), .disabled("Z"), .enable("false")) multiplexer_8 (
    .in0(ALU_SRC_in), .in1(1'b0), .out(multiplexer_8_out), .sel(\同步清零 ));
  Multiplexer #(.select(1), .width(1), .disabled("Z"), .enable("false")) multiplexer_9 (
    .in0(RegWrite_in), .in1(1'b0), .out(multiplexer_9_out), .sel(\同步清零 ));
  Multiplexer #(.select(1), .width(1), .disabled("Z"), .enable("false")) multiplexer_10 (
    .in0(Syscall_in), .in1(1'b0), .out(multiplexer_10_out), .sel(\同步清零 ));
  Multiplexer #(.select(1), .width(1), .disabled("Z"), .enable("false")) multiplexer_11 (
    .in0(RegDst_in), .in1(1'b0), .out(multiplexer_11_out), .sel(\同步清零 ));
  Multiplexer #(.select(1), .width(1), .disabled("Z"), .enable("false")) multiplexer_12 (
    .in0(Beq_in), .in1(1'b0), .out(multiplexer_12_out), .sel(\同步清零 ));
  Multiplexer #(.select(1), .width(1), .disabled("Z"), .enable("false")) multiplexer_13 (
    .in0(Bne_in), .in1(1'b0), .out(multiplexer_13_out), .sel(\同步清零 ));
  Multiplexer #(.select(1), .width(1), .disabled("Z"), .enable("false")) multiplexer_14 (
    .in0(JR_in), .in1(1'b0), .out(multiplexer_14_out), .sel(\同步清零 ));
  Multiplexer #(.select(1), .width(1), .disabled("Z"), .enable("false")) multiplexer_15 (
    .in0(JMP_in), .in1(1'b0), .out(multiplexer_15_out), .sel(\同步清零 ));
  Multiplexer #(.select(1), .width(1), .disabled("Z"), .enable("false")) multiplexer_16 (
    .in0(JAL_in), .in1(1'b0), .out(multiplexer_16_out), .sel(\同步清零 ));
  Register #(.width(1), .trigger("rising"), .Select("low")) register_1 (
    .D(multiplexer_1_out), .en(\使能 ), .Q(SLLV), .clk(clk));  // open: clr
  Register #(.width(1), .trigger("rising"), .Select("low")) register_2 (
    .D(multiplexer_2_out), .en(\使能 ), .Q(XOR), .clk(clk));  // open: clr
  Register #(.width(1), .trigger("rising"), .Select("low")) register_3 (
    .D(multiplexer_3_out), .en(\使能 ), .Q(SH), .clk(clk));  // open: clr
  Register #(.width(1), .trigger("rising"), .Select("low")) register_4 (
    .D(multiplexer_4_out), .en(\使能 ), .Q(BLTZ), .clk(clk));  // open: clr
  Register #(.width(4), .trigger("rising"), .Select("low")) register_5 (
    .D(multiplexer_5_out), .en(\使能 ), .Q(ALUOP), .clk(clk));  // open: clr
  Register #(.width(1), .trigger("rising"), .Select("low")) register_6 (
    .D(multiplexer_6_out), .en(\使能 ), .Q(MemToReg), .clk(clk));  // open: clr
  Register #(.width(1), .trigger("rising"), .Select("low")) register_7 (
    .D(multiplexer_7_out), .en(\使能 ), .Q(MemWrite), .clk(clk));  // open: clr
  Register #(.width(1), .trigger("rising"), .Select("low")) register_8 (
    .D(multiplexer_8_out), .en(\使能 ), .Q(ALU_SRC), .clk(clk));  // open: clr
  Register #(.width(1), .trigger("rising"), .Select("low")) register_9 (
    .D(multiplexer_9_out), .en(\使能 ), .Q(RegWrite), .clk(clk));  // open: clr
  Register #(.width(1), .trigger("rising"), .Select("low")) register_10 (
    .D(multiplexer_10_out), .en(\使能 ), .Q(SysCALL), .clk(clk));  // open: clr
  Register #(.width(1), .trigger("rising"), .Select("low")) register_11 (
    .D(multiplexer_11_out), .en(\使能 ), .Q(RegDst), .clk(clk));  // open: clr
  Register #(.width(1), .trigger("rising"), .Select("low")) register_12 (
    .D(multiplexer_12_out), .en(\使能 ), .Q(Beq), .clk(clk));  // open: clr
  Register #(.width(1), .trigger("rising"), .Select("low")) register_13 (
    .D(multiplexer_13_out), .en(\使能 ), .Q(Bne), .clk(clk));  // open: clr
  Register #(.width(1), .trigger("rising"), .Select("low")) register_14 (
    .D(multiplexer_14_out), .en(\使能 ), .Q(JR), .clk(clk));  // open: clr
  Register #(.width(1), .trigger("rising"), .Select("low")) register_15 (
    .D(multiplexer_15_out), .en(\使能 ), .Q(JMP), .clk(clk));  // open: clr
  Register #(.width(1), .trigger("rising"), .Select("low")) register_16 (
    .D(multiplexer_16_out), .en(\使能 ), .Q(JAL), .clk(clk));  // open: clr
  Multiplexer #(.select(1), .width(32), .disabled("Z"), .enable("false")) multiplexer_17 (
    .in0(IR_in), .in1({32{1'b0}}), .out(multiplexer_17_out), .sel(\同步清零 ));
  Multiplexer #(.select(1), .width(32), .disabled("Z"), .enable("false")) multiplexer_18 (
    .in0(PC_in), .in1({32{1'b0}}), .out(multiplexer_18_out), .sel(\同步清零 ));
  Multiplexer #(.select(1), .width(32), .disabled("Z"), .enable("false")) multiplexer_19 (
    .in0(A_in), .in1({32{1'b0}}), .out(multiplexer_19_out), .sel(\同步清零 ));
  Multiplexer #(.select(1), .width(1), .disabled("Z"), .enable("false")) multiplexer_20 (
    .in0(LEDIN_IN), .in1(1'b0), .out(multiplexer_20_out), .sel(\同步清零 ));
  Multiplexer #(.select(1), .width(32), .disabled("Z"), .enable("false")) multiplexer_21 (
    .in0(B), .in1({32{1'b0}}), .out(multiplexer_21_out), .sel(\同步清零 ));
  Multiplexer #(.select(1), .width(32), .disabled("Z"), .enable("false")) multiplexer_22 (
    .in0(ALU_in), .in1({32{1'b0}}), .out(multiplexer_22_out), .sel(\同步清零 ));
  Multiplexer #(.select(1), .width(5), .disabled("Z"), .enable("false")) multiplexer_23 (
    .in0(WriteReg), .in1({5{1'b0}}), .out(multiplexer_23_out), .sel(\同步清零 ));
  Register #(.width(32), .trigger("rising"), .Select("low")) register_17 (
    .D(multiplexer_17_out), .en(\使能 ), .Q(IR_out), .clk(clk));  // open: clr
  Register #(.width(32), .trigger("rising"), .Select("low")) register_18 (
    .D(multiplexer_18_out), .en(\使能 ), .Q(PC_out), .clk(clk));  // open: clr
  Register #(.width(32), .trigger("rising"), .Select("low")) register_19 (
    .D(multiplexer_19_out), .en(\使能 ), .Q(A), .clk(clk));  // open: clr
  Register #(.width(1), .trigger("rising"), .Select("low")) register_20 (
    .D(multiplexer_20_out), .en(\使能 ), .Q(ledin), .clk(clk));  // open: clr
  Register #(.width(32), .trigger("rising"), .Select("low")) register_21 (
    .D(multiplexer_21_out), .en(\使能 ), .Q(B_2), .clk(clk));  // open: clr
  Register #(.width(32), .trigger("rising"), .Select("low")) register_22 (
    .D(multiplexer_22_out), .en(\使能 ), .Q(ALU_out), .clk(clk));  // open: clr
  Register #(.width(5), .trigger("rising"), .Select("low")) register_23 (
    .D(multiplexer_23_out), .en(\使能 ), .Q(WriteReg_out), .clk(clk));  // open: clr
endmodule

module MEM_WB (
  input  HALT_in,
  input  SLLV_in,
  input  XOR_in,
  input  SH_in,
  input  BLTZ_in,
  input  [3:0] ALUOP_in,
  input  MemToReg_in,
  input  [31:0] IR_in,
  input  MemWrite_in,
  input  ALU_SRC_in,
  input  [31:0] PC_in,
  input  RegWrite_in,
  input  Syscall_in,
  input  [31:0] RD,
  input  RegDst_in,
  input  Beq_in,
  input  [31:0] leddata,
  input  Bne_in,
  input  [31:0] ALU_in,
  input  JR_in,
  input  JMP_in,
  input  [4:0] WriteReg,
  input  JAL_in,
  input  \使能 ,
  input  clk,
  input  \同步清零 ,
  output halt,
  output SLLV,
  output XOR,
  output SH,
  output BLTZ,
  output [3:0] ALUOP,
  output MemToReg,
  output [31:0] IR_out,
  output MemWrite,
  output ALU_SRC,
  output [31:0] PC_out,
  output RegWrite,
  output SysCALL,
  output [31:0] RD_out,
  output RegDst,
  output Beq,
  output [31:0] leddata_out,
  output Bne,
  output [31:0] ALU_out,
  output JR,
  output JMP,
  output [4:0] WriteReg_out,
  output JAL
);

  wire multiplexer_1_out, multiplexer_2_out, multiplexer_3_out, multiplexer_4_out, multiplexer_5_out,
       multiplexer_7_out, multiplexer_8_out, multiplexer_9_out, multiplexer_10_out, multiplexer_11_out,
       multiplexer_12_out, multiplexer_13_out, multiplexer_14_out, multiplexer_15_out, multiplexer_16_out,
       multiplexer_17_out;
  wire [3:0] multiplexer_6_out;
  wire [4:0] multiplexer_23_out;
  wire [31:0] multiplexer_18_out, multiplexer_19_out, multiplexer_20_out, multiplexer_21_out,
       multiplexer_22_out;

  Multiplexer #(.select(1), .width(1), .disabled("Z"), .enable("false")) multiplexer_1 (
    .in0(HALT_in), .in1(1'b0), .out(multiplexer_1_out), .sel(\同步清零 ));
  Multiplexer #(.select(1), .width(1), .disabled("Z"), .enable("false")) multiplexer_2 (
    .in0(SLLV_in), .in1(1'b0), .out(multiplexer_2_out), .sel(\同步清零 ));
  Multiplexer #(.select(1), .width(1), .disabled("Z"), .enable("false")) multiplexer_3 (
    .in0(XOR_in), .in1(1'b0), .out(multiplexer_3_out), .sel(\同步清零 ));
  Multiplexer #(.select(1), .width(1), .disabled("Z"), .enable("false")) multiplexer_4 (
    .in0(SH_in), .in1(1'b0), .out(multiplexer_4_out), .sel(\同步清零 ));
  Multiplexer #(.select(1), .width(1), .disabled("Z"), .enable("false")) multiplexer_5 (
    .in0(BLTZ_in), .in1(1'b0), .out(multiplexer_5_out), .sel(\同步清零 ));
  Multiplexer #(.select(1), .width(4), .disabled("Z"), .enable("false")) multiplexer_6 (
    .in0(ALUOP_in), .in1(4'b0000), .out(multiplexer_6_out), .sel(\同步清零 ));
  Multiplexer #(.select(1), .width(1), .disabled("Z"), .enable("false")) multiplexer_7 (
    .in0(MemToReg_in), .in1(1'b0), .out(multiplexer_7_out), .sel(\同步清零 ));
  Multiplexer #(.select(1), .width(1), .disabled("Z"), .enable("false")) multiplexer_8 (
    .in0(MemWrite_in), .in1(1'b0), .out(multiplexer_8_out), .sel(\同步清零 ));
  Multiplexer #(.select(1), .width(1), .disabled("Z"), .enable("false")) multiplexer_9 (
    .in0(ALU_SRC_in), .in1(1'b0), .out(multiplexer_9_out), .sel(\同步清零 ));
  Multiplexer #(.select(1), .width(1), .disabled("Z"), .enable("false")) multiplexer_10 (
    .in0(RegWrite_in), .in1(1'b0), .out(multiplexer_10_out), .sel(\同步清零 ));
  Multiplexer #(.select(1), .width(1), .disabled("Z"), .enable("false")) multiplexer_11 (
    .in0(Syscall_in), .in1(1'b0), .out(multiplexer_11_out), .sel(\同步清零 ));
  Multiplexer #(.select(1), .width(1), .disabled("Z"), .enable("false")) multiplexer_12 (
    .in0(RegDst_in), .in1(1'b0), .out(multiplexer_12_out), .sel(\同步清零 ));
  Multiplexer #(.select(1), .width(1), .disabled("Z"), .enable("false")) multiplexer_13 (
    .in0(Beq_in), .in1(1'b0), .out(multiplexer_13_out), .sel(\同步清零 ));
  Multiplexer #(.select(1), .width(1), .disabled("Z"), .enable("false")) multiplexer_14 (
    .in0(Bne_in), .in1(1'b0), .out(multiplexer_14_out), .sel(\同步清零 ));
  Multiplexer #(.select(1), .width(1), .disabled("Z"), .enable("false")) multiplexer_15 (
    .in0(JR_in), .in1(1'b0), .out(multiplexer_15_out), .sel(\同步清零 ));
  Multiplexer #(.select(1), .width(1), .disabled("Z"), .enable("false")) multiplexer_16 (
    .in0(JMP_in), .in1(1'b0), .out(multiplexer_16_out), .sel(\同步清零 ));
  Multiplexer #(.select(1), .width(1), .disabled("Z"), .enable("false")) multiplexer_17 (
    .in0(JAL_in), .in1(1'b0), .out(multiplexer_17_out), .sel(\同步清零 ));
  Register #(.width(1), .trigger("rising"), .Select("low")) register_1 (
    .D(multiplexer_1_out), .en(\使能 ), .Q(halt), .clk(clk));  // open: clr
  Register #(.width(1), .trigger("rising"), .Select("low")) register_2 (
    .D(multiplexer_2_out), .en(\使能 ), .Q(SLLV), .clk(clk));  // open: clr
  Register #(.width(1), .trigger("rising"), .Select("low")) register_3 (
    .D(multiplexer_3_out), .en(\使能 ), .Q(XOR), .clk(clk));  // open: clr
  Register #(.width(1), .trigger("rising"), .Select("low")) register_4 (
    .D(multiplexer_4_out), .en(\使能 ), .Q(SH), .clk(clk));  // open: clr
  Register #(.width(1), .trigger("rising"), .Select("low")) register_5 (
    .D(multiplexer_5_out), .en(\使能 ), .Q(BLTZ), .clk(clk));  // open: clr
  Register #(.width(4), .trigger("rising"), .Select("low")) register_6 (
    .D(multiplexer_6_out), .en(\使能 ), .Q(ALUOP), .clk(clk));  // open: clr
  Register #(.width(1), .trigger("rising"), .Select("low")) register_7 (
    .D(multiplexer_7_out), .en(\使能 ), .Q(MemToReg), .clk(clk));  // open: clr
  Register #(.width(1), .trigger("rising"), .Select("low")) register_8 (
    .D(multiplexer_8_out), .en(\使能 ), .Q(MemWrite), .clk(clk));  // open: clr
  Register #(.width(1), .trigger("rising"), .Select("low")) register_9 (
    .D(multiplexer_9_out), .en(\使能 ), .Q(ALU_SRC), .clk(clk));  // open: clr
  Register #(.width(1), .trigger("rising"), .Select("low")) register_10 (
    .D(multiplexer_10_out), .en(\使能 ), .Q(RegWrite), .clk(clk));  // open: clr
  Register #(.width(1), .trigger("rising"), .Select("low")) register_11 (
    .D(multiplexer_11_out), .en(\使能 ), .Q(SysCALL), .clk(clk));  // open: clr
  Register #(.width(1), .trigger("rising"), .Select("low")) register_12 (
    .D(multiplexer_12_out), .en(\使能 ), .Q(RegDst), .clk(clk));  // open: clr
  Register #(.width(1), .trigger("rising"), .Select("low")) register_13 (
    .D(multiplexer_13_out), .en(\使能 ), .Q(Beq), .clk(clk));  // open: clr
  Register #(.width(1), .trigger("rising"), .Select("low")) register_14 (
    .D(multiplexer_14_out), .en(\使能 ), .Q(Bne), .clk(clk));  // open: clr
  Register #(.width(1), .trigger("rising"), .Select("low")) register_15 (
    .D(multiplexer_15_out), .en(\使能 ), .Q(JR), .clk(clk));  // open: clr
  Register #(.width(1), .trigger("rising"), .Select("low")) register_16 (
    .D(multiplexer_16_out), .en(\使能 ), .Q(JMP), .clk(clk));  // open: clr
  Register #(.width(1), .trigger("rising"), .Select("low")) register_17 (
    .D(multiplexer_17_out), .en(\使能 ), .Q(JAL), .clk(clk));  // open: clr
  Multiplexer #(.select(1), .width(32), .disabled("Z"), .enable("false")) multiplexer_18 (
    .in0(IR_in), .in1({32{1'b0}}), .out(multiplexer_18_out), .sel(\同步清零 ));
  Multiplexer #(.select(1), .width(32), .disabled("Z"), .enable("false")) multiplexer_19 (
    .in0(PC_in), .in1({32{1'b0}}), .out(multiplexer_19_out), .sel(\同步清零 ));
  Multiplexer #(.select(1), .width(32), .disabled("Z"), .enable("false")) multiplexer_20 (
    .in0(RD), .in1({32{1'b0}}), .out(multiplexer_20_out), .sel(\同步清零 ));
  Multiplexer #(.select(1), .width(32), .disabled("Z"), .enable("false")) multiplexer_21 (
    .in0(leddata), .in1({32{1'b0}}), .out(multiplexer_21_out), .sel(\同步清零 ));
  Multiplexer #(.select(1), .width(32), .disabled("Z"), .enable("false")) multiplexer_22 (
    .in0(ALU_in), .in1({32{1'b0}}), .out(multiplexer_22_out), .sel(\同步清零 ));
  Multiplexer #(.select(1), .width(5), .disabled("Z"), .enable("false")) multiplexer_23 (
    .in0(WriteReg), .in1({5{1'b0}}), .out(multiplexer_23_out), .sel(\同步清零 ));
  Register #(.width(32), .trigger("rising"), .Select("low")) register_18 (
    .D(multiplexer_18_out), .en(\使能 ), .Q(IR_out), .clk(clk));  // open: clr
  Register #(.width(32), .trigger("rising"), .Select("low")) register_19 (
    .D(multiplexer_19_out), .en(\使能 ), .Q(PC_out), .clk(clk));  // open: clr
  Register #(.width(32), .trigger("rising"), .Select("low")) register_20 (
    .D(multiplexer_20_out), .en(\使能 ), .Q(RD_out), .clk(clk));  // open: clr
  Register #(.width(32), .trigger("rising"), .Select("low")) register_21 (
    .D(multiplexer_21_out), .en(\使能 ), .Q(leddata_out), .clk(clk));  // open: clr
  Register #(.width(32), .trigger("rising"), .Select("low")) register_22 (
    .D(multiplexer_22_out), .en(\使能 ), .Q(ALU_out), .clk(clk));  // open: clr
  Register #(.width(5), .trigger("rising"), .Select("low")) register_23 (
    .D(multiplexer_23_out), .en(\使能 ), .Q(WriteReg_out), .clk(clk));  // open: clr
endmodule
module \源寄存器使用情况  (
  input  OP0,
  input  OP1,
  input  OP2,
  input  OP3,
  input  OP4,
  input  OP5,
  input  F0,
  input  F1,
  input  F2,
  input  F3,
  input  F4,
  input  F5,
  output R1_Used,
  output R2_Used
);

  wire and_1_out, and_2_out, and_3_out, and_4_out, and_5_out, and_6_out, and_7_out, and_8_out, and_9_out,
       and_10_out, and_11_out, and_12_out, and_13_out, and_14_out, and_15_out, and_16_out, and_17_out,
       and_18_out, and_19_out, and_20_out, and_21_out, and_22_out, and_23_out, and_24_out, not_1_out,
       not_2_out, not_3_out, not_4_out, not_5_out, not_6_out, not_7_out, not_8_out, not_9_out, not_10_out,
       not_11_out, not_12_out, not_13_out, not_14_out, not_15_out, not_16_out, not_17_out, not_18_out,
       not_19_out, not_20_out, not_21_out, not_22_out, not_23_out, not_24_out, not_25_out, not_26_out,
       not_27_out, not_28_out, not_29_out, not_30_out, not_31_out, not_32_out, not_33_out, not_34_out,
       not_35_out, not_36_out, not_37_out, not_38_out, not_39_out, not_40_out, not_41_out, not_42_out,
       not_43_out, not_44_out, not_45_out, not_46_out, not_47_out, not_48_out, not_49_out, not_50_out,
       not_51_out, not_52_out, not_53_out, not_54_out, not_55_out, not_56_out, not_57_out, not_58_out,
       not_59_out, not_60_out, not_61_out, not_62_out, not_63_out, not_64_out, not_65_out, not_66_out,
       not_67_out, not_68_out, not_69_out, not_70_out, not_71_out, not_72_out, not_73_out, not_74_out,
       not_75_out, not_76_out, not_77_out, not_78_out, not_79_out, not_80_out, not_81_out, not_82_out,
       not_83_out, not_84_out, not_85_out, not_86_out, not_87_out, not_88_out, not_89_out, not_90_out,
       not_91_out, not_92_out, not_93_out, not_94_out, not_95_out, not_96_out, not_97_out, not_98_out,
       not_99_out, not_100_out, not_101_out, not_102_out, not_103_out, not_104_out, not_105_out, not_106_out,
       not_107_out, not_108_out, not_109_out, not_110_out, not_111_out, not_112_out, not_113_out,
       not_114_out, not_115_out, not_116_out, not_117_out, not_118_out, not_119_out, not_120_out,
       not_121_out, not_122_out, not_123_out, not_124_out, not_125_out, not_126_out, not_127_out,
       not_128_out, not_129_out, not_130_out, not_131_out, not_132_out, not_133_out, not_134_out,
       not_135_out, not_136_out, not_137_out, not_138_out, not_139_out, not_140_out, not_141_out,
       not_142_out, not_143_out, not_144_out, not_145_out;

  not not_1 (not_1_out, OP1);
  not not_2 (not_2_out, OP4);
  not not_3 (not_3_out, OP5);
  not not_4 (not_4_out, F0);
  not not_5 (not_5_out, F2);
  not not_6 (not_6_out, F3);
  not not_7 (not_7_out, F4);
  not not_8 (not_8_out, OP1);
  not not_9 (not_9_out, OP4);
  not not_10 (not_10_out, OP5);
  not not_11 (not_11_out, F1);
  not not_12 (not_12_out, F3);
  not not_13 (not_13_out, F4);
  not not_14 (not_14_out, OP1);
  not not_15 (not_15_out, OP4);
  not not_16 (not_16_out, OP5);
  not not_17 (not_17_out, F0);
  not not_18 (not_18_out, F1);
  not not_19 (not_19_out, F4);
  not not_20 (not_20_out, F5);
  not not_21 (not_21_out, OP1);
  not not_22 (not_22_out, OP4);
  not not_23 (not_23_out, OP5);
  not not_24 (not_24_out, F3);
  not not_25 (not_25_out, F4);
  not not_26 (not_26_out, OP1);
  not not_27 (not_27_out, OP4);
  not not_28 (not_28_out, OP5);
  not not_29 (not_29_out, F2);
  not not_30 (not_30_out, F3);
  not not_31 (not_31_out, F4);
  not not_32 (not_32_out, F5);
  not not_33 (not_33_out, OP1);
  not not_34 (not_34_out, OP4);
  not not_35 (not_35_out, OP5);
  not not_36 (not_36_out, F2);
  not not_37 (not_37_out, F4);
  not not_38 (not_38_out, OP1);
  not not_39 (not_39_out, OP4);
  not not_40 (not_40_out, OP5);
  not not_41 (not_41_out, F1);
  not not_42 (not_42_out, F2);
  not not_43 (not_43_out, F5);
  not not_44 (not_44_out, OP0);
  not not_45 (not_45_out, OP1);
  not not_46 (not_46_out, OP2);
  not not_47 (not_47_out, OP3);
  not not_48 (not_48_out, OP4);
  not not_49 (not_49_out, OP0);
  not not_50 (not_50_out, OP2);
  not not_51 (not_51_out, OP4);
  not not_52 (not_52_out, OP5);
  not not_53 (not_53_out, OP1);
  not not_54 (not_54_out, OP4);
  not not_55 (not_55_out, OP5);
  not not_56 (not_56_out, OP1);
  not not_57 (not_57_out, OP4);
  not not_58 (not_58_out, OP5);
  not not_59 (not_59_out, OP2);
  not not_60 (not_60_out, OP4);
  not not_61 (not_61_out, OP0);
  not not_62 (not_62_out, OP1);
  not not_63 (not_63_out, OP2);
  not not_64 (not_64_out, OP3);
  not not_65 (not_65_out, OP4);
  not not_66 (not_66_out, F0);
  not not_67 (not_67_out, F1);
  not not_68 (not_68_out, F3);
  not not_69 (not_69_out, F4);
  not not_70 (not_70_out, OP0);
  not not_71 (not_71_out, OP1);
  not not_72 (not_72_out, OP2);
  not not_73 (not_73_out, OP3);
  not not_74 (not_74_out, OP4);
  not not_75 (not_75_out, F0);
  not not_76 (not_76_out, F2);
  not not_77 (not_77_out, F3);
  not not_78 (not_78_out, F4);
  not not_79 (not_79_out, OP0);
  not not_80 (not_80_out, OP1);
  not not_81 (not_81_out, OP2);
  not not_82 (not_82_out, OP3);
  not not_83 (not_83_out, OP4);
  not not_84 (not_84_out, F1);
  not not_85 (not_85_out, F3);
  not not_86 (not_86_out, F4);
  not not_87 (not_87_out, OP0);
  not not_88 (not_88_out, OP1);
  not not_89 (not_89_out, OP2);
  not not_90 (not_90_out, OP3);
  not not_91 (not_91_out, OP4);
  not not_92 (not_92_out, F0);
  not not_93 (not_93_out, F1);
  not not_94 (not_94_out, F4);
  not not_95 (not_95_out, F5);
  not not_96 (not_96_out, OP0);
  not not_97 (not_97_out, OP1);
  not not_98 (not_98_out, OP2);
  not not_99 (not_99_out, OP3);
  not not_100 (not_100_out, OP4);
  not not_101 (not_101_out, F3);
  not not_102 (not_102_out, F4);
  not not_103 (not_103_out, OP0);
  not not_104 (not_104_out, OP1);
  not not_105 (not_105_out, OP2);
  not not_106 (not_106_out, OP3);
  not not_107 (not_107_out, OP4);
  not not_108 (not_108_out, F2);
  not not_109 (not_109_out, F3);
  not not_110 (not_110_out, F4);
  not not_111 (not_111_out, F5);
  not not_112 (not_112_out, OP0);
  not not_113 (not_113_out, OP1);
  not not_114 (not_114_out, OP2);
  not not_115 (not_115_out, OP3);
  not not_116 (not_116_out, OP4);
  not not_117 (not_117_out, F2);
  not not_118 (not_118_out, F4);
  not not_119 (not_119_out, OP0);
  not not_120 (not_120_out, OP1);
  not not_121 (not_121_out, OP2);
  not not_122 (not_122_out, OP3);
  not not_123 (not_123_out, OP4);
  not not_124 (not_124_out, F1);
  not not_125 (not_125_out, F2);
  not not_126 (not_126_out, F5);
  not not_127 (not_127_out, OP0);
  not not_128 (not_128_out, OP1);
  not not_129 (not_129_out, OP2);
  not not_130 (not_130_out, OP3);
  not not_131 (not_131_out, OP4);
  not not_132 (not_132_out, OP1);
  not not_133 (not_133_out, OP3);
  not not_134 (not_134_out, OP4);
  not not_135 (not_135_out, OP5);
  not not_136 (not_136_out, OP2);
  not not_137 (not_137_out, OP4);
  not not_138 (not_138_out, F0);
  not not_139 (not_139_out, F1);
  not not_140 (not_140_out, F2);
  not not_141 (not_141_out, F3);
  not not_142 (not_142_out, F4);
  not not_143 (not_143_out, F5);
  not not_144 (not_144_out, OP2);
  not not_145 (not_145_out, OP4);
  and and_1 (and_1_out, not_1_out, not_2_out, not_3_out, not_4_out, not_5_out, not_6_out, not_7_out);
  and and_2 (and_2_out, not_8_out, not_9_out, not_10_out, not_11_out, not_12_out, not_13_out, F5);
  and and_3 (and_3_out, not_14_out, not_15_out, not_16_out, not_17_out, not_18_out, F3, not_19_out, not_20_out);
  and and_4 (and_4_out, not_21_out, not_22_out, not_23_out, F2, not_24_out, not_25_out, F5);
  and and_5 (and_5_out, not_26_out, not_27_out, not_28_out, F1, not_29_out, not_30_out, not_31_out, not_32_out);
  and and_6 (and_6_out, not_33_out, not_34_out, not_35_out, F1, not_36_out, F3, not_37_out, F5);
  and and_7 (and_7_out, not_38_out, not_39_out, not_40_out, F0, not_41_out, not_42_out, F3, F4, not_43_out);
  and and_8 (and_8_out, not_44_out, not_45_out, not_46_out, not_47_out, not_48_out, OP5);
  and and_9 (and_9_out, not_49_out, not_50_out, OP3, not_51_out, not_52_out);
  and and_10 (and_10_out, not_53_out, OP2, not_54_out, not_55_out);
  and and_11 (and_11_out, OP0, not_56_out, not_57_out, not_58_out);
  and and_12 (and_12_out, OP0, OP1, not_59_out, not_60_out, OP5);
  and and_13 (and_13_out, not_61_out, not_62_out, not_63_out, not_64_out, not_65_out, not_66_out, not_67_out, not_68_out, not_69_out);
  and and_14 (and_14_out, not_70_out, not_71_out, not_72_out, not_73_out, not_74_out, not_75_out, not_76_out, not_77_out, not_78_out);
  and and_15 (and_15_out, not_79_out, not_80_out, not_81_out, not_82_out, not_83_out, not_84_out, not_85_out, not_86_out, F5);
  and and_16 (and_16_out, not_87_out, not_88_out, not_89_out, not_90_out, not_91_out, not_92_out, not_93_out, F2, not_94_out, not_95_out);
  and and_17 (and_17_out, not_96_out, not_97_out, not_98_out, not_99_out, not_100_out, F2, not_101_out, not_102_out, F5);
  and and_18 (and_18_out, not_103_out, not_104_out, not_105_out, not_106_out, not_107_out, F1, not_108_out, not_109_out, not_110_out, not_111_out);
  and and_19 (and_19_out, not_112_out, not_113_out, not_114_out, not_115_out, not_116_out, F1, not_117_out, F3, not_118_out, F5);
  and and_20 (and_20_out, not_119_out, not_120_out, not_121_out, not_122_out, not_123_out, F0, not_124_out, not_125_out, F3, F4, not_126_out);
  and and_21 (and_21_out, not_127_out, not_128_out, not_129_out, not_130_out, not_131_out, OP5);
  and and_22 (and_22_out, not_132_out, OP2, not_133_out, not_134_out, not_135_out);
  and and_23 (and_23_out, OP0, not_136_out, OP3, not_137_out, OP5, not_138_out, not_139_out, not_140_out, not_141_out, not_142_out, not_143_out);
  and and_24 (and_24_out, OP0, OP1, not_144_out, not_145_out, OP5);
  or or_1 (R1_Used, and_1_out, and_2_out, and_3_out, and_4_out, and_5_out, and_6_out, and_7_out, and_8_out, and_9_out, and_10_out, and_11_out, and_12_out);
  or or_2 (R2_Used, and_13_out, and_14_out, and_15_out, and_16_out, and_17_out, and_18_out, and_19_out, and_20_out, and_21_out, and_22_out, and_23_out, and_24_out);
endmodule

module \数据相关检测  (
  input  [5:0] OP,
  input  [5:0] FUNC,
  input  [4:0] ID_ReadReg1,
  input  [4:0] EX_WriteReg,
  input  EX_RegWrite,
  input  [4:0] MEM_WriteReg,
  input  MEM_RegWrite,
  input  [4:0] ID_ReadReg2,
  output \EX冲突1 ,
  output \MEM冲突1 ,
  output \EX冲突2 ,
  output \MEM冲突2 
);

  wire comparator_1_eq, comparator_2_eq, comparator_3_eq, comparator_4_eq, comparator_5_eq, comparator_6_eq,
       not_1_out, not_2_out, \源寄存器使用情况_1_r1_used , \源寄存器使用情况_1_r2_used ;

  \源寄存器使用情况  \u_源寄存器使用情况_1  (
    .OP0(OP[0]), .OP1(OP[1]), .OP2(OP[2]), .OP3(OP[3]), .OP4(OP[4]), .OP5(OP[5]), .F0(FUNC[0]), .F1(FUNC[1]),
    .F2(FUNC[2]), .F3(FUNC[3]), .F4(FUNC[4]), .F5(FUNC[5]), .R1_Used(\源寄存器使用情况_1_r1_used ),
    .R2_Used(\源寄存器使用情况_1_r2_used ));
  Comparator #(.width(5), .mode("twosComplement")) comparator_1 (
    .a({5{1'b0}}), .b(ID_ReadReg1), .eq(comparator_1_eq));  // open: gt, lt
  Comparator #(.width(5), .mode("twosComplement")) comparator_2 (
    .a(ID_ReadReg1), .b(EX_WriteReg), .eq(comparator_2_eq));  // open: gt, lt
  Comparator #(.width(5), .mode("twosComplement")) comparator_3 (
    .a(ID_ReadReg1), .b(MEM_WriteReg), .eq(comparator_3_eq));  // open: gt, lt
  Comparator #(.width(5), .mode("twosComplement")) comparator_4 (
    .a({5{1'b0}}), .b(ID_ReadReg2), .eq(comparator_4_eq));  // open: gt, lt
  Comparator #(.width(5), .mode("twosComplement")) comparator_5 (
    .a(ID_ReadReg2), .b(EX_WriteReg), .eq(comparator_5_eq));  // open: gt, lt
  Comparator #(.width(5), .mode("twosComplement")) comparator_6 (
    .a(ID_ReadReg2), .b(MEM_WriteReg), .eq(comparator_6_eq));  // open: gt, lt
  not not_1 (not_1_out, comparator_1_eq);
  not not_2 (not_2_out, comparator_4_eq);
  and and_1 (\EX冲突1 , \源寄存器使用情况_1_r1_used , not_1_out, comparator_2_eq, EX_RegWrite);
  and and_2 (\MEM冲突1 , \源寄存器使用情况_1_r1_used , not_1_out, comparator_3_eq, MEM_RegWrite);
  and and_3 (\EX冲突2 , \源寄存器使用情况_1_r2_used , not_2_out, comparator_5_eq, EX_RegWrite);
  and and_4 (\MEM冲突2 , \源寄存器使用情况_1_r2_used , not_2_out, comparator_6_eq, MEM_RegWrite);
endmodule

module \堆栈  (
  input  choose,
  input  [31:0] push,
  input  en,
  input  clk,
  output [31:0] pop
);

  wire [31:0] _2, _3, _4, _5, _6, multiplexer_1_out, multiplexer_2_out, multiplexer_3_out, multiplexer_4_out,
       multiplexer_5_out, multiplexer_6_out;

  Multiplexer #(.select(1), .width(32), .disabled("Z"), .enable("false")) multiplexer_1 (
    .in0(push), .in1(_2), .out(multiplexer_1_out), .sel(choose));
  Multiplexer #(.select(1), .width(32), .disabled("Z"), .enable("false")) multiplexer_2 (
    .in0(pop), .in1(_3), .out(multiplexer_2_out), .sel(choose));
  Multiplexer #(.select(1), .width(32), .disabled("Z"), .enable("false")) multiplexer_3 (
    .in0(_2), .in1(_4), .out(multiplexer_3_out), .sel(choose));
  Multiplexer #(.select(1), .width(32), .disabled("Z"), .enable("false")) multiplexer_4 (
    .in0(_3), .in1(_5), .out(multiplexer_4_out), .sel(choose));
  Multiplexer #(.select(1), .width(32), .disabled("Z"), .enable("false")) multiplexer_5 (
    .in0(_4), .in1(_6), .out(multiplexer_5_out), .sel(choose));
  Multiplexer #(.select(1), .width(32), .disabled("Z"), .enable("false")) multiplexer_6 (
    .in0(_5), .in1({32{1'b0}}), .out(multiplexer_6_out), .sel(choose));
  Register #(.width(32), .trigger("rising"), .Select("low")) register_1 (
    .D(multiplexer_1_out), .en(en), .Q(pop), .clk(clk));  // open: clr
  Register #(.width(32), .trigger("rising"), .Select("low")) register_2 (
    .D(multiplexer_2_out), .en(en), .Q(_2), .clk(clk));  // open: clr
  Register #(.width(32), .trigger("rising"), .Select("low")) register_3 (
    .D(multiplexer_3_out), .en(en), .Q(_3), .clk(clk));  // open: clr
  Register #(.width(32), .trigger("rising"), .Select("low")) register_4 (
    .D(multiplexer_4_out), .en(en), .Q(_4), .clk(clk));  // open: clr
  Register #(.width(32), .trigger("rising"), .Select("low")) register_5 (
    .D(multiplexer_5_out), .en(en), .Q(_5), .clk(clk));  // open: clr
  Register #(.width(32), .trigger("rising"), .Select("low")) register_6 (
    .D(multiplexer_6_out), .en(en), .Q(_6), .clk(clk));  // open: clr
endmodule

module team (
  input  IR1,
  input  IR2,
  input  IR3,
  output RegWrite,
  output MemWrite,
  output [31:0] PC,
  output [31:0] IR,
  output [31:0] RDin,
  output [31:0] MDin,
  output [31:0] LedData
);

  wire AluScrB, and_1_out, and_2_out, and_4_out, Beq, Bne, CLK, clock_2_out, comparator_1_eq,
       comparator_2_eq, comparator_3_eq, comparator_4_eq, comparator_5_eq, comparator_5_lt, comparator_7_eq,
       controlled_inverter_1_out, controlled_inverter_2_out, controlled_inverter_3_out, d_ff_1_q,
       decoder_1_out1, decoder_1_out2, decoder_1_out3, ERET, Go, halt, INT1, INT2, INT3, IR1_t, IR2_t, IR3_t,
       IRA, IRB, IRC, JAL, JMP, JR, ledin, MemToReg, mips_alu_1_equal, nand_1_out, not_1_out, not_2_out,
       not_3_out, or_1_out, or_5_out, or_6_out, priority_encoder_1_gs, RegDst, register_2_q, RST1, RST2,
       RST3, SignedExt, Syscall, W1, W2, W3, \中断 ;
  wire [1:0] INTNUM, register_4_q;
  wire [3:0] AluOP;
  wire [4:0] multiplexer_6_out, multiplexer_7_out, multiplexer_8_out, multiplexer_9_out;
  wire [12:0] CNT_num;
  wire [15:0] \总周期数 ;
  wire [31:0] adder_1_out, adder_2_out, bit_extender_1_out, bit_extender_2_out, EPC, mips_alu_1_result,
       mips_regifile_1_r1, multiplexer_1_out, multiplexer_2_out, multiplexer_4_out, multiplexer_5_out,
       multiplexer_10_out, multiplexer_12_out, multiplexer_14_out, PC_4, ram_1_data, shifter_1_out,
       \中断程序入口地址 ;

  Clock #(.highDuration(1), .lowDuration(1)) clock_1 ();  // open: out
  Button _1 (.out(IRA));
  Button _2 (.out(IRB));
  Button _3 (.out(IRC));
  Button \u_继续运行  (.out(Go));
  LED #(.active("true")) led_1 (.in(W1));
  LED #(.active("true")) led_2 (.in(W2));
  LED #(.active("true")) led_3 (.in(W3));
  Hex_Digit_Display hex_digit_display_1 (.value(LedData[31:28]));  // open: dp
  Comparator #(.width(16), .mode("twosComplement")) comparator_1 (
    .a(16'h23b), .b(\总周期数 ), .eq(comparator_1_eq));  // open: gt, lt
  Comparator #(.width(16), .mode("twosComplement")) comparator_2 (
    .a(\总周期数 ), .b(16'h1), .eq(comparator_2_eq));  // open: gt, lt
  Comparator #(.width(16), .mode("twosComplement")) comparator_3 (
    .a(\总周期数 ), .b(16'h4), .eq(comparator_3_eq));  // open: gt, lt
  Comparator #(.width(16), .mode("twosComplement")) comparator_4 (
    .a(\总周期数 ), .b(16'h7), .eq(comparator_4_eq));  // open: gt, lt
  Multiplexer #(.select(1), .width(32), .disabled("Z"), .enable("false")) multiplexer_1 (
    .in0(adder_1_out), .in1(adder_2_out), .out(multiplexer_1_out), .sel(or_5_out));
  Multiplexer #(.select(1), .width(32), .disabled("Z"), .enable("false")) multiplexer_2 (
    .in0(multiplexer_1_out), .in1({4'b0000, IR[25:0], 2'b00}), .out(multiplexer_2_out), .sel(JMP));
  D_Flip_Flop #(.trigger("high"), .Pre_Clr_Positions("LEGACY"), .NegatePresetClear("false"), .enable("true"), .NewFFLayout("false")) d_ff_1 (.Q(d_ff_1_q));  // open: clk, D, Qn, preset, en, reset
  // Probe on 13'h2f6
  Hex_Digit_Display hex_digit_display_2 (.value(LedData[27:24]));  // open: dp
  Hex_Digit_Display hex_digit_display_3 (.value(LedData[23:20]));  // open: dp
  or or_1 (or_1_out, comparator_1_eq, comparator_2_eq);
  assign controlled_inverter_1_out = or_1_out ? ~CLK : 1'bz;  // Controlled_Inverter controlled_inverter_1
  assign controlled_inverter_2_out = comparator_3_eq ? ~CLK : 1'bz;  // Controlled_Inverter controlled_inverter_2
  assign controlled_inverter_3_out = comparator_4_eq ? ~CLK : 1'bz;  // Controlled_Inverter controlled_inverter_3
  Multiplexer #(.select(1), .width(32), .disabled("Z"), .enable("false")) multiplexer_3 (
    .in0(multiplexer_2_out), .in1(mips_regifile_1_r1), .out(PC_4), .sel(JR));
  Comparator #(.width(13), .mode("twosComplement")) comparator_5 (
    .a(CNT_num), .b(13'h2f6), .eq(comparator_5_eq), .lt(comparator_5_lt));  // open: gt
  Clock #(.highDuration(1), .lowDuration(1)) clock_2 (.out(clock_2_out));
  Hex_Digit_Display hex_digit_display_4 (.value(LedData[19:16]));  // open: dp
  Hex_Digit_Display hex_digit_display_5 (.value(LedData[15:12]));  // open: dp
  Pull_Resistor #(.pull(0)) pull_resistor_1 (.node(controlled_inverter_1_out));
  Pull_Resistor #(.pull(0)) pull_resistor_2 (.node(controlled_inverter_2_out));
  Pull_Resistor #(.pull(0)) pull_resistor_3 (.node(controlled_inverter_3_out));
  Multiplexer #(.select(1), .width(32), .disabled("Z"), .enable("false")) multiplexer_4 (
    .in0(PC_4), .in1(\中断程序入口地址 ), .out(multiplexer_4_out), .sel(\中断 ));
  Multiplexer #(.select(1), .width(32), .disabled("Z"), .enable("false")) multiplexer_5 (
    .in0(multiplexer_4_out), .in1(EPC), .out(multiplexer_5_out), .sel(ERET));
  nand nand_1 (nand_1_out, d_ff_1_q, comparator_5_eq);
  Counter #(.width(13), .max('h1fff), .ongoal("stay"), .trigger("rising"), .behavior("old")) counter_1 (
    .count(comparator_5_lt), .Q(CNT_num), .clk(clock_2_out));  // open: load, D, carry, clr, preset
  Hex_Digit_Display hex_digit_display_6 (.value(LedData[7:4]));  // open: dp
  Hex_Digit_Display hex_digit_display_7 (.value(LedData[11:8]));  // open: dp
  // Probe on \总周期数 
  // Probe on PC
  Register #(.width(32), .trigger("rising"), .Select("low")) u_PC (
    .D(multiplexer_5_out), .en(not_1_out), .Q(PC), .clk(CLK));  // open: clr
  not not_1 (not_1_out, halt);
  assign CLK = nand_1_out ? clock_2_out : 1'bz;  // Controlled_Buffer controlled_buffer_1
  Hex_Digit_Display hex_digit_display_8 (.value(LedData[3:0]));  // open: dp
  Adder #(.width(32)) adder_1 (.a(PC), .b(32'h4), .out(adder_1_out));  // open: cin, cout
  Pull_Resistor #(.pull(1)) pull_resistor_4 (.node(CLK));
  or or_2 (IR1_t, IR1, IRA);
  \中断按键参考电路  \u_中断按键参考电路_1  (.\与中断屏蔽位与 (INT1), .\同步清零信号 (RST1), .in_1(CLK), .in_2(IR1_t), .out_5(W1));
  \中断按键参考电路  \u_中断按键参考电路_2  (.\与中断屏蔽位与 (INT2), .\同步清零信号 (RST2), .in_1(CLK), .in_2(IR2_t), .out_5(W2));
  \中断按键参考电路  \u_中断按键参考电路_3  (.\与中断屏蔽位与 (INT3), .\同步清零信号 (RST3), .in_1(CLK), .in_2(IR3_t), .out_5(W3));
  // Mips_Probe mips_probe_1: pin names not known; wires that end beside it: IR
  ROM #(.addrWidth(10), .dataWidth(32), .Select("high")) rom_1 (.addr(PC[11:2]), .data(IR));
  or or_3 (IR2_t, IR2, IRB);
  Multiplexer #(.select(1), .width(5), .disabled("Z"), .enable("false")) multiplexer_6 (
    .in0(IR[25:21]), .in1(5'b00010), .out(multiplexer_6_out), .sel(Syscall));
  Multiplexer #(.select(1), .width(5), .disabled("Z"), .enable("false")) multiplexer_7 (
    .in0(IR[20:16]), .in1(5'b00100), .out(multiplexer_7_out), .sel(Syscall));
  Multiplexer #(.select(1), .width(5), .disabled("Z"), .enable("false")) multiplexer_8 (
    .in0(IR[20:16]), .in1(IR[15:11]), .out(multiplexer_8_out), .sel(RegDst));
  Multiplexer #(.select(1), .width(5), .disabled("Z"), .enable("false")) multiplexer_9 (
    .in0(multiplexer_8_out), .in1({5{1'b1}}), .out(multiplexer_9_out), .sel(JAL));
  assign bit_extender_1_out = {{16{1'b0}}, IR[15:0]};  // Bit_Extender bit_extender_1
  assign bit_extender_2_out = {{16{IR[15]}}, IR[15:0]};  // Bit_Extender bit_extender_2
  or or_4 (IR3_t, IR3, IRC);
  Multiplexer #(.select(1), .width(32), .disabled("Z"), .enable("false")) multiplexer_10 (
    .in0(bit_extender_1_out), .in1(bit_extender_2_out), .out(multiplexer_10_out), .sel(SignedExt));
  and and_1 (and_1_out, Beq, mips_alu_1_equal);
  or or_5 (or_5_out, and_1_out, and_2_out);
  and and_2 (and_2_out, Bne, ~mips_alu_1_equal);  // AND_Gate
  MIPS_Regifile mips_regifile_1 (
    .Din(RDin), .Clk(CLK), .R1(mips_regifile_1_r1), .R2(MDin), .WE(RegWrite), .W_num(multiplexer_9_out),
    .R1_num(multiplexer_6_out), .R2_num(multiplexer_7_out));
  Priority_Encoder #(.select(2), .disabled("Z")) priority_encoder_1 (
    .in0(1'b0), .in1(INT1), .in2(INT2), .in3(INT3), .out(INTNUM), .gs(priority_encoder_1_gs), .en_in(1'b1));  // open: en_out
  Multiplexer #(.select(2), .width(32), .disabled("Z"), .enable("false")) multiplexer_11 (
    .in1(32'h30ac), .in2(32'h3150), .in3(32'h31f4), .out(\中断程序入口地址 ), .sel(INTNUM));  // open: in0
  Comparator #(.width(32), .mode("twosComplement")) comparator_6 (.a(IR), .b(32'h42000018), .eq(ERET));  // open: gt, lt
  Multiplexer #(.select(1), .width(32), .disabled("Z"), .enable("false")) multiplexer_12 (
    .in0(MDin), .in1(multiplexer_10_out), .out(multiplexer_12_out), .sel(AluScrB));
  Shifter #(.width(32), .shift("ll")) shifter_1 (.in(bit_extender_2_out), .\dist (5'b00010), .out(shifter_1_out));
  MIPS_ALU mips_alu_1 (
    .X(mips_regifile_1_r1), .Y(multiplexer_12_out), .AluOP(AluOP), .Equal(mips_alu_1_equal),
    .Result(mips_alu_1_result), .shamt(IR[10:6]));  // open: Result_2
  Adder #(.width(32)) adder_2 (.a(shifter_1_out), .b(adder_1_out), .out(adder_2_out));  // open: cin, cout
  not not_2 (not_2_out, halt);
  or or_6 (or_6_out, \中断 , ERET);
  Comparator #(.width(32), .mode("twosComplement")) comparator_7 (
    .a(32'h22), .b(mips_regifile_1_r1), .eq(comparator_7_eq));  // open: gt, lt
  Counter #(.width(16), .max('hffff), .ongoal("stay"), .trigger("rising"), .behavior("old")) counter_2 (
    .count(not_2_out), .Q(\总周期数 ), .clk(CLK));  // open: load, D, carry, clr, preset
  and and_3 (ledin, Syscall, comparator_7_eq);
  and and_4 (and_4_out, Syscall, ~comparator_7_eq);  // AND_Gate
  Register #(.width(32), .trigger("rising"), .Select("low")) register_1 (
    .D(MDin), .en(ledin), .Q(LedData), .clk(CLK));  // open: clr
  Register #(.width(1), .trigger("rising"), .Select("low")) register_2 (
    .D(\中断 ), .en(or_6_out), .Q(register_2_q), .clk(CLK));  // open: clr
  not not_3 (not_3_out, register_2_q);
  Register #(.width(32), .trigger("rising"), .Select("low")) register_3 (
    .D(PC_4), .en(\中断 ), .Q(EPC), .clk(CLK));  // open: clr
  Register #(.width(2), .trigger("rising"), .Select("low")) register_4 (
    .D(INTNUM), .en(\中断 ), .Q(register_4_q), .clk(CLK));  // open: clr
  Register #(.width(1), .trigger("rising"), .Select("low")) register_5 (
    .D(Syscall), .en(and_4_out), .Q(halt), .clk(CLK), .clr(Go));
  RAM #(.addrWidth(10), .dataWidth(32), .bus("separate"), .Select("high")) ram_1 (
    .addr(mips_alu_1_result[11:2]), .din(MDin), .data(ram_1_data), .str(MemWrite), .clk(CLK), .ld(1'b1));  // open: sel, clr
  Multiplexer #(.select(1), .width(32), .disabled("Z"), .enable("false")) multiplexer_13 (
    .in0(multiplexer_14_out), .in1(adder_1_out), .out(RDin), .sel(JAL));
  and and_5 (\中断 , not_3_out, priority_encoder_1_gs);
  Decoder #(.select(2), .tristate("false"), .disabled("Z"), .enable("false")) decoder_1 (
    .out1(decoder_1_out1), .out2(decoder_1_out2), .out3(decoder_1_out3), .sel(register_4_q));  // open: out0
  Multiplexer #(.select(1), .width(32), .disabled("Z"), .enable("false")) multiplexer_14 (
    .in0(mips_alu_1_result), .in1(ram_1_data), .out(multiplexer_14_out), .sel(MemToReg));
  and and_6 (RST1, decoder_1_out1, ERET);
  and and_7 (RST2, decoder_1_out2, ERET);
  and and_8 (RST3, decoder_1_out3, ERET);
  \单周期硬布线控制器  \u_单周期硬布线控制器_1  (
    .Func(IR[5:0]), .OP(IR[31:26]), .ALU_OP(AluOP), .MemToReg(MemToReg), .MemWrite(MemWrite),
    .ALU_SRC(AluScrB), .RegWrite(RegWrite), .SysCALL(Syscall), .SignedExt(SignedExt), .RegDst(RegDst),
    .JR(JR), .JMP(JMP), .Beq(Beq), .JAL(JAL), .Bne(Bne));  // open: SLLV, XOR, SH, BLTZ

  // Other names for the same wires on the sheet: Func[5:0] = IR[5:0]; OP[5:0] = IR[31:26]

  // Notes on the sheet:
  //   中断源
  //   中断等待指示
  //   总复位信号应将除ROM以外所有存储组件全部清零
  //   控制位
  //   单级中断测试信号模拟器
  //   暂停节拍，不能为0
  //   戳工具置1进入计数暂停模式，ctrl+k时钟自动运行到对应节拍暂停
  //   ctrl+k关闭时钟连续运行，将控制位置零，进入单步调试模式调试
  //   用这个时钟源需要去掉电路中的其他时钟源
  //   数码管输出
  //   数码管输出应该用寄存器锁存，否则显示数据只能一闪而过
  //   可计数暂停的时钟源
  //   指令存储器
  //   指令字
  //   contents of rom_1 (hex, n*v repeats v):
  //   201d07d0 20100001 109fc0 139fc3 8021 2012000c 24160008 26100001 3210000f 20080008 20090001 139900
  //   2709825 132020 20020022 c 1094022 1500fff9 22100001 2018000f 2188024 108700 20080008 20090001 139902
  //   2709825 132021 20020022 c 1094022 1500fff9 108702 2c9b022 12c00001 8000c07 4020 1084027 84400
  //   3508ffff 82021 20020022 c 8000c01 afa20000 23bd0004 afa40000 23bd0004 afb00000 23bd0004 afb30000
  //   23bd0004 afb40000 23bd0004 afb50000 23bd0004 afb60000 23bd0004 20160001 20140003 20150001 168020
  //   108100 2149825 132020 20020022 c 1600fffa 295a022 1680fff7 23bdfffc 8fb60000 23bdfffc 8fb50000
  //   23bdfffc 8fb40000 23bdfffc 8fb30000 23bdfffc 8fb00000 23bdfffc 8fa40000 23bdfffc 8fa20000 42000018
  //   afa20000 23bd0004 afa40000 23bd0004 afb00000 23bd0004 afb30000 23bd0004 afb40000 23bd0004 afb50000
  //   23bd0004 afb60000 23bd0004 20160002 20140003 20150001 168020 108100 2149825 132020 20020022 c
  //   1600fffa 295a022 1680fff7 23bdfffc 8fb60000 23bdfffc 8fb50000 23bdfffc 8fb40000 23bdfffc 8fb30000
  //   23bdfffc 8fb00000 23bdfffc 8fa40000 23bdfffc 8fa20000 42000018 afa20000 23bd0004 afa40000 23bd0004
  //   afb00000 23bd0004 afb30000 23bd0004 afb40000 23bd0004 afb50000 23bd0004 afb60000 23bd0004 20160003
  //   20140003 20150001 168020 108100 2149825 132020 20020022 c 1600fffa 295a022 1680fff7 23bdfffc
  //   8fb60000 23bdfffc 8fb50000 23bdfffc 8fb40000 23bdfffc 8fb30000 23bdfffc 8fb00000 23bdfffc 8fa40000
  //   23bdfffc 8fa20000 42000018
  //   OP
  //   Func
  //   rs
  //   rt
  //   rd
  //   为方便自动评测，需要输出PC，IR，寄存器堆写如数据RDin
  //   RAM写使能MemWrite、RAM写入数据MDin等信号
  //   JMP
  //   JR
  //   OP
  //   Func
  //   Beq
  //   Bne
  //   MemToReg
  //   MemWrite
  //   AluOP
  //   AluSrcB
  //   RegWrite
  //   JAL
  //   RegDst
  //   Syscall
endmodule

module yao (
  output [6:0] out_1
);

  wire button_1_out, clock_1_out;

  Keyboard #(.Char_bit_width(7), .buflen(32), .trigger("rising")) keyboard_1 (
    .clk(clock_1_out), .clr(button_1_out), .data(out_1));  // open: re, avail
  Clock #(.highDuration(1), .lowDuration(1)) clock_1 (.out(clock_1_out));
  Button button_1 (.out(button_1_out));
  TTY #(.Char_bit_width(7), .rows(8), .cols(32), .trigger("rising")) tty_1 (
    .data(out_1), .clk(clock_1_out));  // open: we, clr
endmodule
